// Digital circuit BenEaster8bit.dig as structural Verilog
module BenEaster8bit (
  input  clk,
  input  Pulse,
  input  ADDR3,
  input  in_4,
  input  in_5,
  input  in_6,
  input  in_7,
  input  in_8,
  input  in_9,
  input  in_10,
  input  in_11,
  input  in_12,
  input  ADDR2,
  input  ADDR1,
  input  ADDR0,
  input  Program,
  input  RESET,
  input  RAMD0,
  input  RAMD1,
  input  RAMD2,
  input  RAMD3,
  input  RAMD4,
  input  RAMD5,
  input  RAMD6,
  input  RAMD7,
  input  ProgData,
  input  BOut,
  input  Source,
  input  Pulse2
);

  wire _74138_1_pin7, _74138_1_pin9, _74138_1_pin10, _74138_1_pin11, _74138_1_pin12, _74138_1_pin13,
       _74138_1_pin14, _74138_1_pin15, _74157_1_pin4, _74157_1_pin7, _74157_1_pin9, _74157_2_pin2,
       _74157_2_pin5, _74157_2_pin11, _74157_2_pin14, _74157_3_pin4, _74157_3_pin7, _74157_3_pin9,
       _74157_3_pin12, _74157_4_pin4, _74157_4_pin7, _74157_4_pin9, _74157_4_pin12, _74161_1_pin2,
       _74161_1_pin12, _74161_1_pin13, _74161_1_pin14, _74161_2_pin7, _74161_2_pin11, _74161_2_pin12,
       _74161_2_pin13, _74161_2_pin14, _74161_2_pin15, _74173_1_pin3, _74173_1_pin4, _74173_1_pin5,
       _74173_1_pin6, _74173_1_pin7, _74173_1_pin9, _74173_1_pin11, _74173_1_pin12, _74173_1_pin13,
       _74173_1_pin14, _74173_2_pin3, _74173_2_pin4, _74173_2_pin5, _74173_2_pin6, _74173_2_pin11,
       _74173_2_pin12, _74173_2_pin13, _74173_2_pin14, _74173_3_pin9, _74173_4_pin3, _74173_4_pin4,
       _74173_4_pin11, _74173_4_pin12, _74189_a_1_pin1, _74189_a_1_pin3, _74189_a_1_pin4, _74189_a_1_pin5,
       _74189_a_1_pin6, _74189_a_1_pin7, _74189_a_1_pin9, _74189_a_1_pin10, _74189_a_1_pin11,
       _74189_a_1_pin12, _74189_a_1_pin13, _74189_a_1_pin14, _74189_a_1_pin15, _74245_1_pin19,
       _74245_4_pin11, _74245_4_pin12, _74245_4_pin13, _74245_4_pin14, _74245_4_pin15, _74245_4_pin16,
       _74245_4_pin17, _74245_4_pin18, _74245_5_pin11, _74245_5_pin12, _74245_5_pin13, _74245_5_pin14,
       _74245_5_pin15, _74245_5_pin16, _74245_5_pin17, _74245_5_pin18, _74245_6_pin2, _74245_6_pin3,
       _74245_6_pin4, _74245_6_pin5, _74245_6_pin6, _74245_6_pin7, _74245_6_pin8, _74245_6_pin9,
       _74245_7_pin6, _74245_7_pin7, _74245_7_pin8, _74245_7_pin9, _74245_7_pin11, _74245_7_pin12,
       _74245_7_pin13, _74245_7_pin14, _74273_1_pin11, _74283_1_pin2, _74283_1_pin6, _74283_1_pin7,
       _74283_1_pin11, _74283_1_pin15, _74283_2_pin2, _74283_2_pin6, _74283_2_pin11, _74283_2_pin15,
       and_1_out, and_2_out, and_4_out, and_6_out, B_pin4, B_pin5, B_pin6, B_pin7, B_pin9, B_pin10, B_pin11,
       B_pin12, Control1_p2, Control1_p3, Control1_p4, Control1_p5, Control1_p6, Control1_p8, Control2_p2,
       Control2_p3, Control2_p4, Control2_p5, Control2_p6, Control2_p8, Control2_p18, Control2_p20,
       nand_1_out, nand_2_out, nor_1_out, nor_2_out, nor_3_out, nor_4_out, not_1_out, not_2_out, not_3_out,
       not_4_out, not_5_out, not_6_out, not_7_out, not_8_out, not_9_out, not_13_out, not_14_out, not_17_out,
       not_23_out, not_24_out, not_27_out, not_28_out, or_1_out, or_2_out, undriven, undriven_2, undriven_3;
  wire [3:0] _74273_1_pin5, _74273_1_pin12;

  LED led_1 (.in(_74138_1_pin11));
  LED led_2 (.in(_74138_1_pin12));
  LED led_3 (.in(_74138_1_pin13));
  LED led_4 (.in(_74138_1_pin14));
  LED led_5 (.in(_74138_1_pin15));
  not not_1 (not_1_out, nand_2_out);
  _74161 _74161_1 (
    .pin1(not_1_out), .pin2(_74161_1_pin2), .pin3(1'b0), .pin4(1'b0), .pin5(1'b0), .pin6(1'b0), .pin7(1'b1),
    .pin8(1'b0), .pin9(1'b1), .pin10(1'b1), .pin12(_74161_1_pin12), .pin13(_74161_1_pin13),
    .pin14(_74161_1_pin14), .pin16(1'b1));  // open: pin11, pin15
  not not_2 (not_2_out, Control2_p5);
  LED Flag (.in(Control2_p5));
  _74189_A _74189_a_1 (
    .pin1(_74189_a_1_pin1), .pin2(1'b0), .pin3(_74189_a_1_pin3), .pin4(_74189_a_1_pin4),
    .pin5(_74189_a_1_pin5), .pin6(_74189_a_1_pin6), .pin7(_74189_a_1_pin7), .pin8(1'b0),
    .pin9(_74189_a_1_pin9), .pin10(_74189_a_1_pin10), .pin11(_74189_a_1_pin11), .pin12(_74189_a_1_pin12),
    .pin13(_74189_a_1_pin13), .pin14(_74189_a_1_pin14), .pin15(_74189_a_1_pin15), .pin16(1'b1));
  nand nand_1 (nand_1_out, _74173_1_pin7, Control1_p4);
  not not_3 (not_3_out, RESET);
  nand nand_2 (nand_2_out, _74138_1_pin10, not_3_out);
  not not_4 (not_4_out, Control2_p3);
  LED Jump (.in(Control2_p3));
  LED MARA3 (.in(_74189_a_1_pin13));
  LED MARA2 (.in(_74189_a_1_pin14));
  not not_5 (not_5_out, not_3_out);
  not not_6 (not_6_out, Control2_p2);
  LED PCOut (.in(Control2_p2));
  or or_1 (or_1_out, Pulse, Pulse2);
  LED MARA1 (.in(_74189_a_1_pin15));
  LED MARA0 (.in(_74189_a_1_pin1));
  _74189 B (
    .pin1(_74189_a_1_pin1), .pin2(1'b0), .pin3(_74189_a_1_pin3), .pin4(B_pin4), .pin5(B_pin5), .pin6(B_pin6),
    .pin7(B_pin7), .pin8(1'b0), .pin9(B_pin9), .pin10(B_pin10), .pin11(B_pin11), .pin12(B_pin12),
    .pin13(_74189_a_1_pin13), .pin14(_74189_a_1_pin14), .pin15(_74189_a_1_pin15), .pin16(1'b1));
  _74157 _74157_1 (
    .pin1(Program), .pin2(1'b0), .pin3(1'b0), .pin4(_74157_1_pin4), .pin5(1'b0), .pin6(1'b0),
    .pin7(_74157_1_pin7), .pin8(1'b0), .pin9(_74157_1_pin9), .pin10(1'b0), .pin11(1'b0),
    .pin12(_74189_a_1_pin3), .pin13(ProgData), .pin14(nand_1_out), .pin15(1'b0), .pin16(1'b1));
  LED led_6 (.in(_74173_1_pin5));
  LED led_7 (.in(_74173_1_pin6));
  _74173 _74173_1 (
    .pin1(1'b0), .pin2(1'b0), .pin3(_74173_1_pin3), .pin4(_74173_1_pin4), .pin5(_74173_1_pin5),
    .pin6(_74173_1_pin6), .pin7(_74173_1_pin7), .pin8(1'b0), .pin9(_74173_1_pin9), .pin10(_74173_1_pin9),
    .pin11(_74173_1_pin11), .pin12(_74173_1_pin12), .pin13(_74173_1_pin13), .pin14(_74173_1_pin14),
    .pin15(not_5_out), .pin16(1'b1));
  LED led_8 (.in(_74161_1_pin14));
  LED PCInc (.in(_74161_2_pin7));
  not not_7 (not_7_out, Source);
  LED led_9 (.in(_74173_1_pin3));
  LED led_10 (.in(_74173_1_pin4));
  _74138 _74138_1 (
    .pin1(_74161_1_pin14), .pin2(_74161_1_pin13), .pin3(_74161_1_pin12), .pin4(1'b0), .pin5(1'b0),
    .pin6(1'b1), .pin7(_74138_1_pin7), .pin8(1'b0), .pin9(_74138_1_pin9), .pin10(_74138_1_pin10),
    .pin11(_74138_1_pin11), .pin12(_74138_1_pin12), .pin13(_74138_1_pin13), .pin14(_74138_1_pin14),
    .pin15(_74138_1_pin15), .pin16(1'b1));
  LED led_11 (.in(_74161_1_pin13));
  LED led_12 (.in(_74161_1_pin12));
  LED OutIn (.in(undriven));
  not not_8 (not_8_out, Control2_p4);
  and and_1 (and_1_out, or_1_out, not_7_out);
  and and_2 (and_2_out, Source, clk);
  not not_9 (not_9_out, Control1_p8);
  _74157 _74157_2 (
    .pin1(Program), .pin2(_74157_2_pin2), .pin3(ADDR0), .pin4(_74189_a_1_pin1), .pin5(_74157_2_pin5),
    .pin6(ADDR1), .pin7(_74189_a_1_pin15), .pin8(1'b0), .pin9(_74189_a_1_pin14), .pin10(ADDR2),
    .pin11(_74157_2_pin11), .pin12(_74189_a_1_pin13), .pin13(ADDR3), .pin14(_74157_2_pin14), .pin15(1'b0),
    .pin16(1'b1));
  LED led_13 (.in(_74173_2_pin5));
  LED led_14 (.in(_74173_2_pin6));
  LED BIn (.in(Control2_p4));
  LED SU (.in(Control2_p6));
  not not_10 (B_pin10, _74157_3_pin9);
  not not_11 (B_pin4, _74157_3_pin4);
  not not_12 (B_pin12, _74157_3_pin12);
  LED led_15 (.in(B_pin11));
  LED led_16 (.in(_74173_2_pin3));
  LED led_17 (.in(_74173_2_pin4));
  not not_13 (not_13_out, Control2_p8);
  LED ALUOut (.in(Control2_p8));
  or or_2 (or_2_out, and_1_out, and_2_out);
  LED led_18 (.in(B_pin7));
  LED led_19 (.in(B_pin9));
  not not_14 (not_14_out, Control1_p5);
  LED AOut (.in(Control1_p5));
  not not_15 (B_pin6, _74157_3_pin7);
  LED led_20 (.in(_74189_a_1_pin11));
  LED led_21 (.in(B_pin5));
  not not_16 (_74161_1_pin2, _74173_1_pin7);
  not not_17 (not_17_out, Control1_p3);
  LED AIn (.in(Control1_p3));
  and and_3 (_74173_1_pin7, or_2_out, not_9_out);
  not not_18 (_74189_a_1_pin4, _74157_4_pin4);
  not not_19 (_74189_a_1_pin6, _74157_4_pin7);
  not not_20 (_74189_a_1_pin10, _74157_4_pin9);
  not not_21 (_74189_a_1_pin12, _74157_4_pin12);
  _74157 _74157_3 (
    .pin1(Program), .pin2(_74173_1_pin14), .pin3(RAMD4), .pin4(_74157_3_pin4), .pin5(_74173_1_pin13),
    .pin6(RAMD5), .pin7(_74157_3_pin7), .pin8(1'b0), .pin9(_74157_3_pin9), .pin10(RAMD6),
    .pin11(_74173_1_pin12), .pin12(_74157_3_pin12), .pin13(RAMD7), .pin14(_74173_1_pin11), .pin15(1'b0),
    .pin16(1'b1));
  LED led_22 (.in(_74189_a_1_pin7));
  LED led_23 (.in(_74189_a_1_pin9));
  _74173 _74173_2 (
    .pin1(1'b0), .pin2(1'b0), .pin3(_74173_2_pin3), .pin4(_74173_2_pin4), .pin5(_74173_2_pin5),
    .pin6(_74173_2_pin6), .pin7(_74173_1_pin7), .pin8(1'b0), .pin9(_74173_1_pin9), .pin10(_74173_1_pin9),
    .pin11(_74173_2_pin11), .pin12(_74173_2_pin12), .pin13(_74173_2_pin13), .pin14(_74173_2_pin14),
    .pin15(not_5_out), .pin16(1'b1));
  not not_22 (_74173_1_pin9, Control1_p2);
  LED IRIn (.in(Control1_p2));
  LED led_24 (.in(_74189_a_1_pin5));
  not not_23 (not_23_out, undriven_2);
  LED IROut (.in(undriven_2));
  LED led_25 (.in(_74173_1_pin7));
  not not_24 (not_24_out, _74173_1_pin7);
  _74245 _74245_1 (
    .pin1(1'b1), .pin2(_74189_a_1_pin5), .pin3(_74189_a_1_pin7), .pin4(_74189_a_1_pin9),
    .pin5(_74189_a_1_pin11), .pin6(B_pin5), .pin7(B_pin7), .pin8(B_pin9), .pin9(B_pin11), .pin10(1'b0),
    .pin11(_74173_1_pin11), .pin12(_74173_1_pin12), .pin13(_74173_1_pin13), .pin14(_74173_1_pin14),
    .pin15(_74173_2_pin11), .pin16(_74173_2_pin12), .pin17(_74173_2_pin13), .pin18(_74173_2_pin14),
    .pin19(_74245_1_pin19), .pin20(1'b1));
  not not_25 (_74245_1_pin19, undriven_3);
  LED RAMOut (.in(undriven_3));
  _74245 _74245_2 (
    .pin1(1'b0), .pin2(_74173_1_pin11), .pin3(_74173_1_pin12), .pin4(_74173_1_pin13), .pin5(_74173_1_pin14),
    .pin6(_74173_2_pin11), .pin7(_74173_2_pin12), .pin8(_74173_2_pin13), .pin9(_74173_2_pin14), .pin10(1'b0),
    .pin11(_74173_2_pin3), .pin12(_74173_2_pin4), .pin13(_74173_2_pin5), .pin14(_74173_2_pin6),
    .pin15(_74173_1_pin3), .pin16(_74173_1_pin4), .pin17(_74173_1_pin5), .pin18(_74173_1_pin6),
    .pin19(not_23_out), .pin20(1'b1));
  LED RAMIn (.in(Control1_p4));
  _74173 _74173_3 (
    .pin1(1'b0), .pin2(1'b0), .pin3(_74157_2_pin2), .pin4(_74157_2_pin5), .pin5(_74157_2_pin11),
    .pin6(_74157_2_pin14), .pin7(_74173_1_pin7), .pin8(1'b0), .pin9(_74173_3_pin9), .pin10(_74173_3_pin9),
    .pin11(_74173_2_pin11), .pin12(_74173_2_pin12), .pin13(_74173_2_pin13), .pin14(_74173_2_pin14),
    .pin15(not_5_out), .pin16(1'b1));
  _74157 _74157_4 (
    .pin1(Program), .pin2(_74173_2_pin14), .pin3(RAMD0), .pin4(_74157_4_pin4), .pin5(_74173_2_pin13),
    .pin6(RAMD1), .pin7(_74157_4_pin7), .pin8(1'b0), .pin9(_74157_4_pin9), .pin10(RAMD2),
    .pin11(_74173_2_pin12), .pin12(_74157_4_pin12), .pin13(RAMD3), .pin14(_74173_2_pin11), .pin15(1'b0),
    .pin16(1'b1));
  // _28c16 Control2: pin names not known; wires that end beside it: 1'b0, Control2_p2, Control2_p3, Control2_p4, Control2_p5, Control2_p6, _74161_1_pin14, Control2_p8, _74161_1_pin13, 1'b0, _74161_1_pin12, 1'b0, _74173_1_pin3, 1'b0, _74173_1_pin4, 1'b1, _74173_1_pin5, Control2_p18, _74173_1_pin6, Control2_p20, 1'b1, 1'b1
  not not_26 (_74173_3_pin9, Control1_p6);
  LED MARIn (.in(Control1_p6));
  // _28c16 Control1: pin names not known; wires that end beside it: 1'b0, Control1_p2, Control1_p3, Control1_p4, Control1_p5, Control1_p6, _74161_1_pin14, Control1_p8, _74161_1_pin13, 1'b0, _74161_1_pin12, 1'b0, _74173_1_pin3, 1'b0, _74173_1_pin4, 1'b1, _74173_1_pin5, Control2_p18, _74173_1_pin3, _74173_1_pin4, _74173_1_pin5, _74173_1_pin6, _74173_1_pin6, Control2_p20, 1'b0, 1'b1, _74173_1_pin11, _74173_1_pin12, _74173_1_pin13, _74173_1_pin14, _74173_2_pin11, _74173_2_pin12, _74173_2_pin13, _74173_2_pin14
  LED Halt (.in(Control1_p8));
  LED B7 (.in(_74173_1_pin11));
  LED B6 (.in(_74173_1_pin12));
  LED B5 (.in(_74173_1_pin13));
  LED B4 (.in(_74173_1_pin14));
  LED B3 (.in(_74173_2_pin11));
  LED B2 (.in(_74173_2_pin12));
  LED B1 (.in(_74173_2_pin13));
  LED B0 (.in(_74173_2_pin14));
  _74245 _74245_3 (
    .pin1(1'b1), .pin2(in_11), .pin3(in_10), .pin4(in_9), .pin5(in_8), .pin6(in_7), .pin7(in_6), .pin8(in_5),
    .pin9(in_4), .pin10(1'b0), .pin11(_74173_1_pin11), .pin12(_74173_1_pin12), .pin13(_74173_1_pin13),
    .pin14(_74173_1_pin14), .pin15(_74173_2_pin11), .pin16(_74173_2_pin12), .pin17(_74173_2_pin13),
    .pin18(_74173_2_pin14), .pin19(in_12), .pin20(1'b1));
  LED Carry (.in(Control2_p20));
  LED Zerro (.in(Control2_p18));
  not not_27 (not_27_out, not_5_out);
  not not_28 (not_28_out, not_5_out);
  _74245 _74245_4 (
    .pin1(1'b0), .pin2(_74173_2_pin14), .pin3(_74173_2_pin13), .pin4(_74173_2_pin12), .pin5(_74173_2_pin11),
    .pin6(_74173_1_pin14), .pin7(_74173_1_pin13), .pin8(_74173_1_pin12), .pin9(_74173_1_pin11), .pin10(1'b0),
    .pin11(_74245_4_pin11), .pin12(_74245_4_pin12), .pin13(_74245_4_pin13), .pin14(_74245_4_pin14),
    .pin15(_74245_4_pin15), .pin16(_74245_4_pin16), .pin17(_74245_4_pin17), .pin18(_74245_4_pin18),
    .pin19(not_14_out), .pin20(1'b1));
  _74173 _74173_4 (
    .pin1(1'b0), .pin2(1'b0), .pin3(_74173_4_pin3), .pin4(_74173_4_pin4), .pin5(Control2_p20),
    .pin6(Control2_p18), .pin7(_74173_1_pin7), .pin8(1'b0), .pin9(not_2_out), .pin10(not_2_out),
    .pin11(_74173_4_pin11), .pin12(_74173_4_pin12), .pin13(_74173_4_pin12), .pin14(_74173_4_pin12),
    .pin15(not_5_out), .pin16(1'b1));
  _74245 _74245_5 (
    .pin1(1'b0), .pin2(_74173_2_pin14), .pin3(_74173_2_pin13), .pin4(_74173_2_pin12), .pin5(_74173_2_pin11),
    .pin6(_74173_1_pin14), .pin7(_74173_1_pin13), .pin8(_74173_1_pin12), .pin9(_74173_1_pin11), .pin10(1'b0),
    .pin11(_74245_5_pin11), .pin12(_74245_5_pin12), .pin13(_74245_5_pin13), .pin14(_74245_5_pin14),
    .pin15(_74245_5_pin15), .pin16(_74245_5_pin16), .pin17(_74245_5_pin17), .pin18(_74245_5_pin18),
    .pin19(BOut), .pin20(1'b1));
  _74273 _74273_1 (
    .pin1(not_27_out), .pin2(_74273_1_pin5[0]), .pin3(_74173_2_pin14), .pin4(_74173_2_pin13),
    .pin5(_74273_1_pin5[1]), .pin6(_74273_1_pin5[2]), .pin7(_74173_2_pin12), .pin8(_74173_2_pin11),
    .pin9(_74273_1_pin5[3]), .pin10(1'b0), .pin11(_74273_1_pin11), .pin12(_74273_1_pin12[0]),
    .pin13(_74173_1_pin14), .pin14(_74173_1_pin13), .pin15(_74273_1_pin12[1]), .pin16(_74273_1_pin12[2]),
    .pin17(_74173_1_pin12), .pin18(_74173_1_pin11), .pin19(_74273_1_pin12[3]), .pin20(1'b1));
  LED led_26 (.in(_74245_6_pin2));
  LED led_27 (.in(_74245_6_pin3));
  _74245 _74245_6 (
    .pin1(1'b1), .pin2(_74245_6_pin2), .pin3(_74245_6_pin3), .pin4(_74245_6_pin4), .pin5(_74245_6_pin5),
    .pin6(_74245_6_pin6), .pin7(_74245_6_pin7), .pin8(_74245_6_pin8), .pin9(_74245_6_pin9), .pin10(1'b0),
    .pin11(_74173_2_pin14), .pin12(_74173_2_pin13), .pin13(_74173_2_pin12), .pin14(_74173_2_pin11),
    .pin15(_74173_1_pin14), .pin16(_74173_1_pin13), .pin17(_74173_1_pin12), .pin18(_74173_1_pin11),
    .pin19(not_13_out), .pin20(1'b1));
  _74161 _74161_2 (
    .pin1(not_28_out), .pin2(_74173_1_pin7), .pin3(_74173_2_pin14), .pin4(_74173_2_pin13),
    .pin5(_74173_2_pin12), .pin6(_74173_2_pin11), .pin7(_74161_2_pin7), .pin8(1'b0), .pin9(not_4_out),
    .pin10(_74161_2_pin7), .pin11(_74161_2_pin11), .pin12(_74161_2_pin12), .pin13(_74161_2_pin13),
    .pin14(_74161_2_pin14), .pin15(_74161_2_pin15), .pin16(1'b1));
  LED led_28 (.in(_74245_6_pin4));
  LED led_29 (.in(_74245_6_pin5));
  nor nor_1 (nor_1_out, _74245_6_pin5, _74245_6_pin4);
  LED led_30 (.in(_74245_6_pin6));
  LED led_31 (.in(_74245_6_pin7));
  nor nor_2 (nor_2_out, _74245_6_pin9, _74245_6_pin8);
  and and_4 (and_4_out, nor_2_out, nor_1_out);
  _74173 _74173_5 (
    .pin1(1'b0), .pin2(1'b0), .pin3(_74245_4_pin11), .pin4(_74245_4_pin12), .pin5(_74245_4_pin13),
    .pin6(_74245_4_pin14), .pin7(_74173_1_pin7), .pin8(1'b0), .pin9(not_17_out), .pin10(not_17_out),
    .pin11(_74173_1_pin14), .pin12(_74173_1_pin13), .pin13(_74173_1_pin12), .pin14(_74173_1_pin11),
    .pin15(not_5_out), .pin16(1'b1));
  LED led_32 (.in(_74245_6_pin8));
  LED led_33 (.in(_74245_6_pin9));
  nor nor_3 (nor_3_out, _74245_6_pin2, _74245_6_pin3);
  and and_5 (_74173_4_pin11, and_6_out, and_4_out);
  _74173 _74173_6 (
    .pin1(1'b0), .pin2(1'b0), .pin3(_74245_5_pin11), .pin4(_74245_5_pin12), .pin5(_74245_5_pin13),
    .pin6(_74245_5_pin14), .pin7(_74173_1_pin7), .pin8(1'b0), .pin9(not_8_out), .pin10(not_8_out),
    .pin11(_74173_1_pin14), .pin12(_74173_1_pin13), .pin13(_74173_1_pin12), .pin14(_74173_1_pin11),
    .pin15(not_5_out), .pin16(1'b1));
  _74283 _74283_1 (
    .pin1(_74245_6_pin4), .pin2(_74283_1_pin2), .pin3(_74245_4_pin13), .pin4(_74245_6_pin5),
    .pin5(_74245_4_pin14), .pin6(_74283_1_pin6), .pin7(_74283_1_pin7), .pin8(1'b0), .pin9(_74173_4_pin12),
    .pin10(_74245_6_pin2), .pin11(_74283_1_pin11), .pin12(_74245_4_pin11), .pin13(_74245_6_pin3),
    .pin14(_74245_4_pin12), .pin15(_74283_1_pin15), .pin16(1'b1));
  nor nor_4 (nor_4_out, _74245_6_pin7, _74245_6_pin6);
  and and_6 (and_6_out, nor_4_out, nor_3_out);
  xor xor_1 (_74283_1_pin11, _74245_5_pin11, Control2_p6);
  xor xor_2 (_74283_1_pin15, _74245_5_pin12, Control2_p6);
  and and_7 (_74273_1_pin11, undriven, _74173_1_pin7);
  _74245 _74245_7 (
    .pin1(1'b1), .pin2(_74161_2_pin14), .pin3(_74161_2_pin13), .pin4(_74161_2_pin12), .pin5(_74161_2_pin11),
    .pin6(_74245_7_pin6), .pin7(_74245_7_pin7), .pin8(_74245_7_pin8), .pin9(_74245_7_pin9), .pin10(1'b0),
    .pin11(_74245_7_pin11), .pin12(_74245_7_pin12), .pin13(_74245_7_pin13), .pin14(_74245_7_pin14),
    .pin15(_74173_2_pin11), .pin16(_74173_2_pin12), .pin17(_74173_2_pin13), .pin18(_74173_2_pin14),
    .pin19(not_6_out), .pin20(1'b1));
  LED led_34 (.in(_74245_4_pin11));
  LED led_35 (.in(_74245_4_pin12));
  xor xor_3 (_74283_1_pin2, _74245_5_pin13, Control2_p6);
  LED led_36 (.in(_74245_5_pin11));
  LED led_37 (.in(_74245_5_pin12));
  LED led_38 (.in(_74245_4_pin13));
  LED led_39 (.in(_74245_4_pin14));
  xor xor_4 (_74283_1_pin6, _74245_5_pin14, Control2_p6);
  LED led_40 (.in(_74245_5_pin13));
  LED led_41 (.in(_74245_5_pin14));
  LED led_42 (.in(_74161_2_pin11));
  LED led_43 (.in(_74245_4_pin15));
  LED led_44 (.in(_74245_4_pin16));
  _74283 _74283_2 (
    .pin1(_74245_6_pin8), .pin2(_74283_2_pin2), .pin3(_74245_4_pin17), .pin4(_74245_6_pin9),
    .pin5(_74245_4_pin18), .pin6(_74283_2_pin6), .pin7(Control2_p6), .pin8(1'b0), .pin9(_74283_1_pin7),
    .pin10(_74245_6_pin6), .pin11(_74283_2_pin11), .pin12(_74245_4_pin15), .pin13(_74245_6_pin7),
    .pin14(_74245_4_pin16), .pin15(_74283_2_pin15), .pin16(1'b1));
  LED led_45 (.in(_74283_1_pin15));
  LED led_46 (.in(_74283_1_pin11));
  xor xor_5 (_74283_2_pin11, _74245_5_pin15, Control2_p6);
  LED led_47 (.in(_74245_5_pin15));
  LED led_48 (.in(_74245_5_pin16));
  LED led_49 (.in(_74161_2_pin12));
  LED led_50 (.in(_74161_2_pin13));
  _74173 _74173_7 (
    .pin1(1'b0), .pin2(1'b0), .pin3(_74245_4_pin15), .pin4(_74245_4_pin16), .pin5(_74245_4_pin17),
    .pin6(_74245_4_pin18), .pin7(_74173_1_pin7), .pin8(1'b0), .pin9(not_17_out), .pin10(not_17_out),
    .pin11(_74173_2_pin14), .pin12(_74173_2_pin13), .pin13(_74173_2_pin12), .pin14(_74173_2_pin11),
    .pin15(not_5_out), .pin16(1'b1));
  LED led_51 (.in(_74245_4_pin17));
  LED led_52 (.in(_74245_4_pin18));
  LED led_53 (.in(_74283_1_pin6));
  LED led_54 (.in(_74283_1_pin2));
  xor xor_6 (_74283_2_pin15, _74245_5_pin16, Control2_p6);
  _74173 _74173_8 (
    .pin1(1'b0), .pin2(1'b0), .pin3(_74245_5_pin15), .pin4(_74245_5_pin16), .pin5(_74245_5_pin17),
    .pin6(_74245_5_pin18), .pin7(_74173_1_pin7), .pin8(1'b0), .pin9(not_8_out), .pin10(not_8_out),
    .pin11(_74173_2_pin14), .pin12(_74173_2_pin13), .pin13(_74173_2_pin12), .pin14(_74173_2_pin11),
    .pin15(not_5_out), .pin16(1'b1));
  LED led_55 (.in(_74245_5_pin17));
  LED led_56 (.in(_74245_5_pin18));
  Seven_Seg_Hex seven_seg_hex_1 (.d(_74273_1_pin12), .dp(1'b0));
  LED led_57 (.in(_74161_2_pin14));
  LED led_58 (.in(_74283_2_pin15));
  LED led_59 (.in(_74283_2_pin11));
  xor xor_7 (_74283_2_pin2, _74245_5_pin17, Control2_p6);
  Seven_Seg_Hex seven_seg_hex_2 (.d(_74273_1_pin5), .dp(1'b0));
  LED led_60 (.in(_74283_2_pin6));
  LED led_61 (.in(_74283_2_pin2));
  xor xor_8 (_74283_2_pin6, _74245_5_pin18, Control2_p6);

  // Notes on the sheet:
  //   in_12: default 1
  //   ProgData: default 1
  //   BOut: default 1
  //   Clock
  //   MAR
  //   RAM
  //   Instruction Reg
  //   Controller
  //   Reg A
  //   ALU
  //   Reg B
  //   Output
  //   Program Counter
  //   contents of Control2 (hex, n*v repeats v):
  //   40,14,0,0,0,0,0,0,40,14,48,12,0,0,0,0,40,14,48,10,2,0,0,0,40,14,48,10,2,0,0,0,40, 14,48,21,
  //   0,0,0,0,40,14,a,0,0,0,0,0,40,14,8,0,0,0,0,0,40,14,0,0,0,0,0,0,40,14,0,0, 0,0,0,0,40,14,0,0,
  //   0,0,0,0,40,14,0,0,0,0,0,0,40,14,0,0,0,0,0,0,40,14,0,0,0,0,0,0,40, 14,0,0,0,0,0,0,40,14,1,0,
  //   0,0,0,0,40,14,80,0,0,0,0,0,4,8,0,0,0,0,0,0,4,8,0,0,0,0,0, 0,4,8,0,20,81,0,0,0,4,8,0,20,c1,0,
  //   0,0,4,8,0,0,0,0,0,0,4,8,0,0,0,0,0,0,4,8,2,0,0,0, 0,0,4,8,0,0,0,0,0,0,4,8,0,0,0,0,0,0,4,8,0,
  //   0,0,0,0,0,4,8,0,0,0,0,0,0,4,8,0,0,0,0,0, 0,4,8,0,0,0,0,0,0,4,8,0,0,0,0,0,0,4,8,10,0,0,0,0,0,
  //   4,8,0,0,0,0,0,0,40,14,0,0,0,0, 0,0,40,14,48,12,0,0,0,0,40,14,48,10,2,0,0,0,40,14,48,10,2,0,
  //   0,0,40,14,48,21,0,0,0, 0,40,14,a,0,0,0,0,0,40,14,8,0,0,0,0,0,40,14,8,0,0,0,0,0,40,14,0,0,0,
  //   0,0,0,40,14,0, 0,0,0,0,0,40,14,0,0,0,0,0,0,40,14,0,0,0,0,0,0,40,14,0,0,0,0,0,0,40,14,0,0,0,
  //   0,0,0, 40,14,1,0,0,0,0,0,40,14,80,0,0,0,0,0,4,8,0,0,0,0,0,0,4,8,0,0,0,0,0,0,4,8,0,20,81, 0,
  //   0,0,4,8,0,20,c1,0,0,0,4,8,0,0,0,0,0,0,4,8,0,0,0,0,0,0,4,8,2,0,0,0,0,0,4,8,2,0,0, 0,0,0,4,8,
  //   0,0,0,0,0,0,4,8,0,0,0,0,0,0,4,8,0,0,0,0,0,0,4,8,0,0,0,0,0,0,4,8,0,0,0,0, 0,0,4,8,0,0,0,0,0,
  //   0,4,8,10,0,0,0,0,0,4,8,0,0,0,0,0,0,40,14,0,0,0,0,0,0,40,14,48,12, 0,0,0,0,40,14,48,10,2,0,0,
  //   0,40,14,48,10,2,0,0,0,40,14,48,21,0,0,0,0,40,14,a,0,0,0, 0,0,40,14,8,0,0,0,0,0,40,14,0,0,0,
  //   0,0,0,40,14,8,0,0,0,0,0,40,14,0,0,0,0,0,0,40,14, 0,0,0,0,0,0,40,14,0,0,0,0,0,0,40,14,0,0,0,
  //   0,0,0,40,14,0,0,0,0,0,0,40,14,1,0,0,0,0, 0,40,14,80,0,0,0,0,0,4,8,0,0,0,0,0,0,4,8,0,0,0,0,0,
  //   0,4,8,0,20,81,0,0,0,4,8,0,20,c1, 0,0,0,4,8,0,0,0,0,0,0,4,8,0,0,0,0,0,0,4,8,2,0,0,0,0,0,4,8,
  //   0,0,0,0,0,0,4,8,2,0,0,0, 0,0,4,8,0,0,0,0,0,0,4,8,0,0,0,0,0,0,4,8,0,0,0,0,0,0,4,8,0,0,0,0,0,
  //   0,4,8,0,0,0,0,0, 0,4,8,10,0,0,0,0,0,4,8,0,0,0,0,0,0,40,14,0,0,0,0,0,0,40,14,48,12,0,0,0,0,40,
  //   14,48, 10,2,0,0,0,40,14,48,10,2,0,0,0,40,14,48,21,0,0,0,0,40,14,a,0,0,0,0,0,40,14,8,0,0, 0,
  //   0,0,40,14,8,0,0,0,0,0,40,14,8,0,0,0,0,0,40,14,0,0,0,0,0,0,40,14,0,0,0,0,0,0,40, 14,0,0,0,0,
  //   0,0,40,14,0,0,0,0,0,0,40,14,0,0,0,0,0,0,40,14,1,0,0,0,0,0,40,14,80,0,0, 0,0,0,4,8,0,0,0,0,0,
  //   0,4,8,0,0,0,0,0,0,4,8,0,20,81,0,0,0,4,8,0,20,c1,0,0,0,4,8,0,0, 0,0,0,0,4,8,0,0,0,0,0,0,4,8,
  //   2,0,0,0,0,0,4,8,2,0,0,0,0,0,4,8,2,0,0,0,0,0,4,8,0,0,0, 0,0,0,4,8,0,0,0,0,0,0,4,8,0,0,0,0,0,
  //   0,4,8,0,0,0,0,0,0,4,8,0,0,0,0,0,0,4,8,10,0,0, 0,0,0,4,8
  //   contents of Control1 (hex, n*v repeats v):
  //   40,14,0,0,0,0,0,0,40,14,48,12,0,0,0,0,40,14,48,10,2,0,0,0,40,14,48,10,2,0,0,0,40, 14,48,21,
  //   0,0,0,0,40,14,a,0,0,0,0,0,40,14,8,0,0,0,0,0,40,14,0,0,0,0,0,0,40,14,0,0, 0,0,0,0,40,14,0,0,
  //   0,0,0,0,40,14,0,0,0,0,0,0,40,14,0,0,0,0,0,0,40,14,0,0,0,0,0,0,40, 14,0,0,0,0,0,0,40,14,1,0,
  //   0,0,0,0,40,14,80,0,0,0,0,0,4,8,0,0,0,0,0,0,4,8,0,0,0,0,0, 0,4,8,0,20,81,0,0,0,4,8,0,20,c1,0,
  //   0,0,4,8,0,0,0,0,0,0,4,8,0,0,0,0,0,0,4,8,2,0,0,0, 0,0,4,8,0,0,0,0,0,0,4,8,0,0,0,0,0,0,4,8,0,
  //   0,0,0,0,0,4,8,0,0,0,0,0,0,4,8,0,0,0,0,0, 0,4,8,0,0,0,0,0,0,4,8,0,0,0,0,0,0,4,8,10,0,0,0,0,0,
  //   4,8,0,0,0,0,0,0,40,14,0,0,0,0, 0,0,40,14,48,12,0,0,0,0,40,14,48,10,2,0,0,0,40,14,48,10,2,0,
  //   0,0,40,14,48,21,0,0,0, 0,40,14,a,0,0,0,0,0,40,14,8,0,0,0,0,0,40,14,8,0,0,0,0,0,40,14,0,0,0,
  //   0,0,0,40,14,0, 0,0,0,0,0,40,14,0,0,0,0,0,0,40,14,0,0,0,0,0,0,40,14,0,0,0,0,0,0,40,14,0,0,0,
  //   0,0,0, 40,14,1,0,0,0,0,0,40,14,80,0,0,0,0,0,4,8,0,0,0,0,0,0,4,8,0,0,0,0,0,0,4,8,0,20,81, 0,
  //   0,0,4,8,0,20,c1,0,0,0,4,8,0,0,0,0,0,0,4,8,0,0,0,0,0,0,4,8,2,0,0,0,0,0,4,8,2,0,0, 0,0,0,4,8,
  //   0,0,0,0,0,0,4,8,0,0,0,0,0,0,4,8,0,0,0,0,0,0,4,8,0,0,0,0,0,0,4,8,0,0,0,0, 0,0,4,8,0,0,0,0,0,
  //   0,4,8,10,0,0,0,0,0,4,8,0,0,0,0,0,0,40,14,0,0,0,0,0,0,40,14,48,12, 0,0,0,0,40,14,48,10,2,0,0,
  //   0,40,14,48,10,2,0,0,0,40,14,48,21,0,0,0,0,40,14,a,0,0,0, 0,0,40,14,8,0,0,0,0,0,40,14,0,0,0,
  //   0,0,0,40,14,8,0,0,0,0,0,40,14,0,0,0,0,0,0,40,14, 0,0,0,0,0,0,40,14,0,0,0,0,0,0,40,14,0,0,0,
  //   0,0,0,40,14,0,0,0,0,0,0,40,14,1,0,0,0,0, 0,40,14,80,0,0,0,0,0,4,8,0,0,0,0,0,0,4,8,0,0,0,0,0,
  //   0,4,8,0,20,81,0,0,0,4,8,0,20,c1, 0,0,0,4,8,0,0,0,0,0,0,4,8,0,0,0,0,0,0,4,8,2,0,0,0,0,0,4,8,
  //   0,0,0,0,0,0,4,8,2,0,0,0, 0,0,4,8,0,0,0,0,0,0,4,8,0,0,0,0,0,0,4,8,0,0,0,0,0,0,4,8,0,0,0,0,0,
  //   0,4,8,0,0,0,0,0, 0,4,8,10,0,0,0,0,0,4,8,0,0,0,0,0,0,40,14,0,0,0,0,0,0,40,14,48,12,0,0,0,0,40,
  //   14,48, 10,2,0,0,0,40,14,48,10,2,0,0,0,40,14,48,21,0,0,0,0,40,14,a,0,0,0,0,0,40,14,8,0,0, 0,
  //   0,0,40,14,8,0,0,0,0,0,40,14,8,0,0,0,0,0,40,14,0,0,0,0,0,0,40,14,0,0,0,0,0,0,40, 14,0,0,0,0,
  //   0,0,40,14,0,0,0,0,0,0,40,14,0,0,0,0,0,0,40,14,1,0,0,0,0,0,40,14,80,0,0, 0,0,0,4,8,0,0,0,0,0,
  //   0,4,8,0,0,0,0,0,0,4,8,0,20,81,0,0,0,4,8,0,20,c1,0,0,0,4,8,0,0, 0,0,0,0,4,8,0,0,0,0,0,0,4,8,
  //   2,0,0,0,0,0,4,8,2,0,0,0,0,0,4,8,2,0,0,0,0,0,4,8,0,0,0, 0,0,0,4,8,0,0,0,0,0,0,4,8,0,0,0,0,0,
  //   0,4,8,0,0,0,0,0,0,4,8,0,0,0,0,0,0,4,8,10,0,0, 0,0,0,4,8
endmodule
