// Digital circuit 16Bit.dig as structural Verilog
module _16Bit (
  input  clk,
  input  Pulse,
  input  Source,
  input  Reset,
  input  Pulse_2
);

  wire _16bitaluint_1_carry, _16bitaluint_1_carryout, _16bitaluint_1_neg, _16bitaluint_1_negout,
       _16bitaluint_1_zero, _16bitaluint_1_zeroout, _16bitcontrolint_1_alu0, _16bitcontrolint_1_alu1,
       _16bitcontrolint_1_alu2, _16bitcontrolint_1_alu3, _16bitcontrolint_1_areset,
       _16bitcontrolint_1_breset, _16bitcontrolint_1_creset, _16bitcontrolint_1_dreset,
       _16bitcontrolint_1_halt, _16bitcontrolint_1_nahh, _16bitcontrolint_1_nain, _16bitcontrolint_1_nainhl,
       _16bitcontrolint_1_nainlh, _16bitcontrolint_1_nall, _16bitcontrolint_1_naluout,
       _16bitcontrolint_1_naout, _16bitcontrolint_1_naouthh, _16bitcontrolint_1_naoutll,
       _16bitcontrolint_1_naoutswap, _16bitcontrolint_1_nbhh, _16bitcontrolint_1_nbin,
       _16bitcontrolint_1_nbinhl, _16bitcontrolint_1_nbinlh, _16bitcontrolint_1_nbll,
       _16bitcontrolint_1_nbout, _16bitcontrolint_1_nbouthh, _16bitcontrolint_1_nboutll,
       _16bitcontrolint_1_nboutswap, _16bitcontrolint_1_ncdec, _16bitcontrolint_1_ncin,
       _16bitcontrolint_1_ncinc, _16bitcontrolint_1_ncout, _16bitcontrolint_1_ndinhh,
       _16bitcontrolint_1_ndinll, _16bitcontrolint_1_ndout, _16bitcontrolint_1_ndouthh,
       _16bitcontrolint_1_ndoutll, _16bitcontrolint_1_ndoutswap, _16bitcontrolint_1_nflagin,
       _16bitcontrolint_1_nirin, _16bitcontrolint_1_nmarin, _16bitcontrolint_1_npcdec,
       _16bitcontrolint_1_npcin, _16bitcontrolint_1_npcinc, _16bitcontrolint_1_npcout,
       _16bitcontrolint_1_nraminh, _16bitcontrolint_1_nraminl, _16bitcontrolint_1_nramout,
       _16bitcontrolint_1_nstackdec, _16bitcontrolint_1_nstackin, _16bitcontrolint_1_nstackinc,
       _16bitcontrolint_1_nstackout, _16bitcontrolint_1_nxin, _16bitcontrolint_1_nxout,
       _16bitcontrolint_1_reset, _16bitdisplayint_1_dec1, _16bitdisplayint_1_dec2, _16bitdisplayint_1_dec3,
       _16bitdisplayint_1_dec4, _16bitdisplayint_2_dec1, _16bitdisplayint_2_dec2, _16bitdisplayint_2_dec3,
       _16bitdisplayint_2_dec4, _16bitdisplayint_3_dec1, _16bitdisplayint_3_dec2, _16bitdisplayint_3_dec3,
       _16bitdisplayint_3_dec4, _16bitdisplayint_4_dec1, _16bitdisplayint_4_dec2, _16bitdisplayint_4_dec3,
       _16bitdisplayint_4_dec4, _16bitdisplayint_5_dec1, _16bitdisplayint_5_dec2, _16bitdisplayint_5_dec3,
       _16bitdisplayint_5_dec4, _16bitdisplayint_6_dec1, _16bitdisplayint_6_dec2, _16bitdisplayint_6_dec3,
       _16bitdisplayint_6_dec4, _16bitdisplayint_7_dec1, _16bitdisplayint_7_dec2, _16bitdisplayint_7_dec3,
       _16bitdisplayint_7_dec4, _16bitdisplayint_8_dec1, _16bitdisplayint_8_dec2, _16bitdisplayint_8_dec3,
       _16bitdisplayint_8_dec4, _16bitdisplayint_9_dec1, _16bitdisplayint_9_dec2, _16bitdisplayint_9_dec3,
       _16bitdisplayint_9_dec4, _16bitdisplayint_10_dec1, _16bitdisplayint_10_dec2, _16bitdisplayint_10_dec3,
       _16bitdisplayint_10_dec4, _16bitdisplayint_11_dec1, _16bitdisplayint_11_dec2,
       _16bitdisplayint_11_dec3, _16bitdisplayint_11_dec4, _16bitdisplayint_12_dec1,
       _16bitdisplayint_12_dec2, _16bitdisplayint_12_dec3, _16bitdisplayint_12_dec4, _16bitramint_1_flash,
       _16bitramint_1_pref, _16bitramint_1_sram, _74161_1_pin1, _74161_1_pin9, _74161_1_pin11,
       _74161_1_pin12, _74161_1_pin13, _74161_1_pin14, and_1_out, and_2_out, and_3_out, not_1_out, not_2_out,
       not_3_out, not_4_out, not_5_out, not_6_out, not_7_out, not_8_out, not_9_out, not_10_out, not_11_out,
       not_12_out, not_14_out, not_15_out, not_16_out, not_17_out, not_18_out, not_19_out, not_20_out,
       not_21_out, not_22_out, not_23_out, not_24_out, not_25_out, not_26_out, not_27_out, not_28_out,
       not_29_out, not_30_out, not_31_out, not_32_out, not_33_out, not_34_out, not_35_out, not_36_out,
       not_37_out, not_38_out, not_39_out, not_40_out, not_41_out, not_42_out, not_43_out, not_44_out,
       not_45_out, not_46_out, not_47_out, not_48_out, not_49_out, or_1_out, or_2_out;
  wire [3:0] _16bitdisplayint_1_digit1, _16bitdisplayint_1_digit2, _16bitdisplayint_1_digit3,
       _16bitdisplayint_1_digit4, _16bitdisplayint_2_digit1, _16bitdisplayint_2_digit2,
       _16bitdisplayint_2_digit3, _16bitdisplayint_2_digit4, _16bitdisplayint_3_digit1,
       _16bitdisplayint_3_digit2, _16bitdisplayint_3_digit3, _16bitdisplayint_3_digit4,
       _16bitdisplayint_4_digit1, _16bitdisplayint_4_digit2, _16bitdisplayint_4_digit3,
       _16bitdisplayint_4_digit4, _16bitdisplayint_5_digit1, _16bitdisplayint_5_digit2,
       _16bitdisplayint_5_digit3, _16bitdisplayint_5_digit4, _16bitdisplayint_6_digit1,
       _16bitdisplayint_6_digit2, _16bitdisplayint_6_digit3, _16bitdisplayint_6_digit4,
       _16bitdisplayint_7_digit1, _16bitdisplayint_7_digit2, _16bitdisplayint_7_digit3,
       _16bitdisplayint_7_digit4, _16bitdisplayint_8_digit1, _16bitdisplayint_8_digit2,
       _16bitdisplayint_8_digit3, _16bitdisplayint_8_digit4, _16bitdisplayint_9_digit1,
       _16bitdisplayint_9_digit2, _16bitdisplayint_9_digit3, _16bitdisplayint_9_digit4,
       _16bitdisplayint_10_digit1, _16bitdisplayint_10_digit2, _16bitdisplayint_10_digit3,
       _16bitdisplayint_10_digit4, _16bitdisplayint_11_digit1, _16bitdisplayint_11_digit2,
       _16bitdisplayint_11_digit3, _16bitdisplayint_11_digit4, _16bitdisplayint_12_digit1,
       _16bitdisplayint_12_digit2, _16bitdisplayint_12_digit3, _16bitdisplayint_12_digit4;
  wire [15:0] _16bitaluint_1_displayout, _16bitramint_1_display, _16bitregistercounterint_1_bus9,
       _16bitregistercounterint_1_signalout, _16bitregistercounterint_2_signalout,
       _16bitregistercounterint_3_signalout, _16bitregisterint2_1_signalout, _16bitregisterint2_2_signalout,
       _16bitregisterint2_3_signalout, _16bitregisterswitchingint_1_signalout,
       _16bitregisterswitchingint_2_signalout, _16bitregisterswitchingint_3_signalout;

  or or_1 (or_1_out, Pulse, Pulse_2);
  not not_1 (not_1_out, Source);
  Seven_Seg_Hex seven_seg_hex_1 (.d(_16bitdisplayint_1_digit4), .dp(_16bitdisplayint_1_dec4));
  _16BitDisplayInt _16bitdisplayint_1 (
    .Digit4(_16bitdisplayint_1_digit4), .Dec4(_16bitdisplayint_1_dec4), .Digit3(_16bitdisplayint_1_digit3),
    .Dec3(_16bitdisplayint_1_dec3), .Digit2(_16bitdisplayint_1_digit2), .Dec2(_16bitdisplayint_1_dec2),
    .Digit1(_16bitdisplayint_1_digit1), .Dec1(_16bitdisplayint_1_dec1),
    .Input(_16bitregistercounterint_1_bus9));
  and and_1 (and_1_out, or_1_out, not_1_out);
  and and_2 (and_2_out, Source, clk);
  not not_2 (not_2_out, _16bitcontrolint_1_halt);
  Seven_Seg_Hex seven_seg_hex_2 (.d(_16bitdisplayint_1_digit3), .dp(_16bitdisplayint_1_dec3));
  or or_2 (or_2_out, and_1_out, and_2_out);
  Seven_Seg_Hex seven_seg_hex_3 (.d(_16bitdisplayint_1_digit2), .dp(_16bitdisplayint_1_dec2));
  Seven_Seg_Hex seven_seg_hex_4 (.d(_16bitdisplayint_1_digit1), .dp(_16bitdisplayint_1_dec1));
  and and_3 (and_3_out, or_2_out, not_2_out);
  LED led_1 (.in(and_3_out));
  _16BitDisplayInt _16bitdisplayint_2 (
    .Digit4(_16bitdisplayint_2_digit4), .Dec4(_16bitdisplayint_2_dec4), .Digit3(_16bitdisplayint_2_digit3),
    .Dec3(_16bitdisplayint_2_dec3), .Digit2(_16bitdisplayint_2_digit2), .Dec2(_16bitdisplayint_2_dec2),
    .Digit1(_16bitdisplayint_2_digit1), .Dec1(_16bitdisplayint_2_dec1),
    .Input(_16bitregistercounterint_1_signalout));
  _16BitRegisterCounterInt _16bitregistercounterint_1 (
    .RegOut(_16bitcontrolint_1_npcout), .RegIn(_16bitcontrolint_1_npcin), .Reset(Reset),
    .Dec(_16bitcontrolint_1_npcdec), .Inc(_16bitcontrolint_1_npcinc),
    .SignalOut(_16bitregistercounterint_1_signalout), .Bus15(_16bitregistercounterint_1_bus9[15]),
    .Bus14(_16bitregistercounterint_1_bus9[14]), .Bus13(_16bitregistercounterint_1_bus9[13]),
    .Bus12(_16bitregistercounterint_1_bus9[12]), .Bus11(_16bitregistercounterint_1_bus9[11]),
    .Bus10(_16bitregistercounterint_1_bus9[10]), .Bus9(_16bitregistercounterint_1_bus9[9]),
    .Bus8(_16bitregistercounterint_1_bus9[8]), .Bus7(_16bitregistercounterint_1_bus9[7]),
    .Bus6(_16bitregistercounterint_1_bus9[6]), .Bus5(_16bitregistercounterint_1_bus9[5]),
    .Bus4(_16bitregistercounterint_1_bus9[4]), .Bus3(_16bitregistercounterint_1_bus9[3]),
    .Bus2(_16bitregistercounterint_1_bus9[2]), .Bus1(_16bitregistercounterint_1_bus9[1]),
    .Bus0(_16bitregistercounterint_1_bus9[0]));
  _16BitDisplayInt _16bitdisplayint_3 (
    .Digit4(_16bitdisplayint_3_digit4), .Dec4(_16bitdisplayint_3_dec4), .Digit3(_16bitdisplayint_3_digit3),
    .Dec3(_16bitdisplayint_3_dec3), .Digit2(_16bitdisplayint_3_digit2), .Dec2(_16bitdisplayint_3_dec2),
    .Digit1(_16bitdisplayint_3_digit1), .Dec1(_16bitdisplayint_3_dec1),
    .Input(_16bitregisterswitchingint_1_signalout));
  _16BitRegisterSwitchingInt _16bitregisterswitchingint_1 (
    .ninHL(1'b1), .ninLH(1'b1), .ninHH(_16bitcontrolint_1_ndinll), .ninLL(_16bitcontrolint_1_ndinhh),
    .nIn(1'b1), .noutSwap(_16bitcontrolint_1_ndoutswap), .noutHH(_16bitcontrolint_1_ndouthh),
    .noutLL(_16bitcontrolint_1_ndoutll), .nOut(_16bitcontrolint_1_ndout), .Clock(and_3_out),
    .Reset(_16bitcontrolint_1_dreset), .Bus15(_16bitregistercounterint_1_bus9[15]),
    .Bus14(_16bitregistercounterint_1_bus9[14]), .Bus13(_16bitregistercounterint_1_bus9[13]),
    .Bus12(_16bitregistercounterint_1_bus9[12]), .Bus11(_16bitregistercounterint_1_bus9[11]),
    .Bus10(_16bitregistercounterint_1_bus9[10]), .Bus9(_16bitregistercounterint_1_bus9[9]),
    .Bus8(_16bitregistercounterint_1_bus9[8]), .Bus7(_16bitregistercounterint_1_bus9[7]),
    .Bus6(_16bitregistercounterint_1_bus9[6]), .Bus5(_16bitregistercounterint_1_bus9[5]),
    .Bus4(_16bitregistercounterint_1_bus9[4]), .Bus3(_16bitregistercounterint_1_bus9[3]),
    .Bus2(_16bitregistercounterint_1_bus9[2]), .Bus1(_16bitregistercounterint_1_bus9[1]),
    .Bus0(_16bitregistercounterint_1_bus9[0]), .SignalOut(_16bitregisterswitchingint_1_signalout));
  Seven_Seg_Hex seven_seg_hex_5 (.d(_16bitdisplayint_2_digit4), .dp(_16bitdisplayint_2_dec4));
  Seven_Seg_Hex seven_seg_hex_6 (.d(_16bitdisplayint_3_digit4), .dp(_16bitdisplayint_3_dec4));
  Seven_Seg_Hex seven_seg_hex_7 (.d(_16bitdisplayint_2_digit3), .dp(_16bitdisplayint_2_dec3));
  Seven_Seg_Hex seven_seg_hex_8 (.d(_16bitdisplayint_3_digit3), .dp(_16bitdisplayint_3_dec3));
  Seven_Seg_Hex seven_seg_hex_9 (.d(_16bitdisplayint_2_digit2), .dp(_16bitdisplayint_2_dec2));
  Seven_Seg_Hex seven_seg_hex_10 (.d(_16bitdisplayint_3_digit2), .dp(_16bitdisplayint_3_dec2));
  Seven_Seg_Hex seven_seg_hex_11 (.d(_16bitdisplayint_2_digit1), .dp(_16bitdisplayint_2_dec1));
  Seven_Seg_Hex seven_seg_hex_12 (.d(_16bitdisplayint_3_digit1), .dp(_16bitdisplayint_3_dec1));
  _16BitDisplayInt _16bitdisplayint_4 (
    .Digit4(_16bitdisplayint_4_digit4), .Dec4(_16bitdisplayint_4_dec4), .Digit3(_16bitdisplayint_4_digit3),
    .Dec3(_16bitdisplayint_4_dec3), .Digit2(_16bitdisplayint_4_digit2), .Dec2(_16bitdisplayint_4_dec2),
    .Digit1(_16bitdisplayint_4_digit1), .Dec1(_16bitdisplayint_4_dec1),
    .Input(_16bitregistercounterint_2_signalout));
  _16BitRegisterCounterInt _16bitregistercounterint_2 (
    .RegOut(_16bitcontrolint_1_nstackout), .RegIn(_16bitcontrolint_1_nstackin), .Reset(Reset),
    .Dec(_16bitcontrolint_1_nstackdec), .Inc(_16bitcontrolint_1_nstackinc),
    .SignalOut(_16bitregistercounterint_2_signalout), .Bus15(_16bitregistercounterint_1_bus9[15]),
    .Bus14(_16bitregistercounterint_1_bus9[14]), .Bus13(_16bitregistercounterint_1_bus9[13]),
    .Bus12(_16bitregistercounterint_1_bus9[12]), .Bus11(_16bitregistercounterint_1_bus9[11]),
    .Bus10(_16bitregistercounterint_1_bus9[10]), .Bus9(_16bitregistercounterint_1_bus9[9]),
    .Bus8(_16bitregistercounterint_1_bus9[8]), .Bus7(_16bitregistercounterint_1_bus9[7]),
    .Bus6(_16bitregistercounterint_1_bus9[6]), .Bus5(_16bitregistercounterint_1_bus9[5]),
    .Bus4(_16bitregistercounterint_1_bus9[4]), .Bus3(_16bitregistercounterint_1_bus9[3]),
    .Bus2(_16bitregistercounterint_1_bus9[2]), .Bus1(_16bitregistercounterint_1_bus9[1]),
    .Bus0(_16bitregistercounterint_1_bus9[0]));
  Seven_Seg_Hex seven_seg_hex_13 (.d(_16bitdisplayint_4_digit4), .dp(_16bitdisplayint_4_dec4));
  Seven_Seg_Hex seven_seg_hex_14 (.d(_16bitdisplayint_5_digit4), .dp(_16bitdisplayint_5_dec4));
  _16BitDisplayInt _16bitdisplayint_5 (
    .Digit4(_16bitdisplayint_5_digit4), .Dec4(_16bitdisplayint_5_dec4), .Digit3(_16bitdisplayint_5_digit3),
    .Dec3(_16bitdisplayint_5_dec3), .Digit2(_16bitdisplayint_5_digit2), .Dec2(_16bitdisplayint_5_dec2),
    .Digit1(_16bitdisplayint_5_digit1), .Dec1(_16bitdisplayint_5_dec1), .Input(_16bitregisterint2_1_signalout));
  _16BitRegisterInt2 _16bitregisterint2_1 (
    .RegOut(_16bitcontrolint_1_nxout), .RegIn(_16bitcontrolint_1_nxin), .Clock(and_3_out), .Reset(Reset),
    .BusOut15(_16bitregistercounterint_1_bus9[15]), .BusOut14(_16bitregistercounterint_1_bus9[14]),
    .BusOut13(_16bitregistercounterint_1_bus9[13]), .BusOut12(_16bitregistercounterint_1_bus9[12]),
    .BusOut11(_16bitregistercounterint_1_bus9[11]), .BusOut10(_16bitregistercounterint_1_bus9[10]),
    .BusOut9(_16bitregistercounterint_1_bus9[9]), .BusOut8(_16bitregistercounterint_1_bus9[8]),
    .BusOut7(_16bitregistercounterint_1_bus9[7]), .BusOut6(_16bitregistercounterint_1_bus9[6]),
    .BusOut5(_16bitregistercounterint_1_bus9[5]), .BusOut4(_16bitregistercounterint_1_bus9[4]),
    .BusOut3(_16bitregistercounterint_1_bus9[3]), .BusOut2(_16bitregistercounterint_1_bus9[2]),
    .BusOut1(_16bitregistercounterint_1_bus9[1]), .BusOut0(_16bitregistercounterint_1_bus9[0]),
    .SignalOut(_16bitregisterint2_1_signalout));
  Seven_Seg_Hex seven_seg_hex_15 (.d(_16bitdisplayint_4_digit3), .dp(_16bitdisplayint_4_dec3));
  Seven_Seg_Hex seven_seg_hex_16 (.d(_16bitdisplayint_5_digit3), .dp(_16bitdisplayint_5_dec3));
  Seven_Seg_Hex seven_seg_hex_17 (.d(_16bitdisplayint_4_digit2), .dp(_16bitdisplayint_4_dec2));
  Seven_Seg_Hex seven_seg_hex_18 (.d(_16bitdisplayint_5_digit2), .dp(_16bitdisplayint_5_dec2));
  Seven_Seg_Hex seven_seg_hex_19 (.d(_16bitdisplayint_4_digit1), .dp(_16bitdisplayint_4_dec1));
  Seven_Seg_Hex seven_seg_hex_20 (.d(_16bitdisplayint_5_digit1), .dp(_16bitdisplayint_5_dec1));
  _16BitDisplayInt _16bitdisplayint_6 (
    .Digit4(_16bitdisplayint_6_digit4), .Dec4(_16bitdisplayint_6_dec4), .Digit3(_16bitdisplayint_6_digit3),
    .Dec3(_16bitdisplayint_6_dec3), .Digit2(_16bitdisplayint_6_digit2), .Dec2(_16bitdisplayint_6_dec2),
    .Digit1(_16bitdisplayint_6_digit1), .Dec1(_16bitdisplayint_6_dec1), .Input(_16bitregisterint2_2_signalout));
  _16BitRegisterInt2 _16bitregisterint2_2 (
    .RegOut(1'b1), .RegIn(_16bitcontrolint_1_nmarin), .Clock(and_3_out), .Reset(Reset),
    .BusOut15(_16bitregistercounterint_1_bus9[15]), .BusOut14(_16bitregistercounterint_1_bus9[14]),
    .BusOut13(_16bitregistercounterint_1_bus9[13]), .BusOut12(_16bitregistercounterint_1_bus9[12]),
    .BusOut11(_16bitregistercounterint_1_bus9[11]), .BusOut10(_16bitregistercounterint_1_bus9[10]),
    .BusOut9(_16bitregistercounterint_1_bus9[9]), .BusOut8(_16bitregistercounterint_1_bus9[8]),
    .BusOut7(_16bitregistercounterint_1_bus9[7]), .BusOut6(_16bitregistercounterint_1_bus9[6]),
    .BusOut5(_16bitregistercounterint_1_bus9[5]), .BusOut4(_16bitregistercounterint_1_bus9[4]),
    .BusOut3(_16bitregistercounterint_1_bus9[3]), .BusOut2(_16bitregistercounterint_1_bus9[2]),
    .BusOut1(_16bitregistercounterint_1_bus9[1]), .BusOut0(_16bitregistercounterint_1_bus9[0]),
    .SignalOut(_16bitregisterint2_2_signalout));
  _16BitDisplayInt _16bitdisplayint_7 (
    .Digit4(_16bitdisplayint_7_digit4), .Dec4(_16bitdisplayint_7_dec4), .Digit3(_16bitdisplayint_7_digit3),
    .Dec3(_16bitdisplayint_7_dec3), .Digit2(_16bitdisplayint_7_digit2), .Dec2(_16bitdisplayint_7_dec2),
    .Digit1(_16bitdisplayint_7_digit1), .Dec1(_16bitdisplayint_7_dec1),
    .Input(_16bitregisterswitchingint_2_signalout));
  _16BitRegisterSwitchingInt _16bitregisterswitchingint_2 (
    .ninHL(_16bitcontrolint_1_nainhl), .ninLH(_16bitcontrolint_1_nainlh), .ninHH(_16bitcontrolint_1_nahh),
    .ninLL(_16bitcontrolint_1_nall), .nIn(_16bitcontrolint_1_nain), .noutSwap(_16bitcontrolint_1_naoutswap),
    .noutHH(_16bitcontrolint_1_naouthh), .noutLL(_16bitcontrolint_1_naoutll),
    .nOut(_16bitcontrolint_1_naout), .Clock(and_3_out), .Reset(_16bitcontrolint_1_areset),
    .Bus15(_16bitregistercounterint_1_bus9[15]), .Bus14(_16bitregistercounterint_1_bus9[14]),
    .Bus13(_16bitregistercounterint_1_bus9[13]), .Bus12(_16bitregistercounterint_1_bus9[12]),
    .Bus11(_16bitregistercounterint_1_bus9[11]), .Bus10(_16bitregistercounterint_1_bus9[10]),
    .Bus9(_16bitregistercounterint_1_bus9[9]), .Bus8(_16bitregistercounterint_1_bus9[8]),
    .Bus7(_16bitregistercounterint_1_bus9[7]), .Bus6(_16bitregistercounterint_1_bus9[6]),
    .Bus5(_16bitregistercounterint_1_bus9[5]), .Bus4(_16bitregistercounterint_1_bus9[4]),
    .Bus3(_16bitregistercounterint_1_bus9[3]), .Bus2(_16bitregistercounterint_1_bus9[2]),
    .Bus1(_16bitregistercounterint_1_bus9[1]), .Bus0(_16bitregistercounterint_1_bus9[0]),
    .SignalOut(_16bitregisterswitchingint_2_signalout));
  Seven_Seg_Hex seven_seg_hex_21 (.d(_16bitdisplayint_6_digit4), .dp(_16bitdisplayint_6_dec4));
  Seven_Seg_Hex seven_seg_hex_22 (.d(_16bitdisplayint_7_digit4), .dp(_16bitdisplayint_7_dec4));
  Seven_Seg_Hex seven_seg_hex_23 (.d(_16bitdisplayint_6_digit3), .dp(_16bitdisplayint_6_dec3));
  Seven_Seg_Hex seven_seg_hex_24 (.d(_16bitdisplayint_7_digit3), .dp(_16bitdisplayint_7_dec3));
  Seven_Seg_Hex seven_seg_hex_25 (.d(_16bitdisplayint_6_digit2), .dp(_16bitdisplayint_6_dec2));
  Seven_Seg_Hex seven_seg_hex_26 (.d(_16bitdisplayint_7_digit2), .dp(_16bitdisplayint_7_dec2));
  Seven_Seg_Hex seven_seg_hex_27 (.d(_16bitdisplayint_6_digit1), .dp(_16bitdisplayint_6_dec1));
  Seven_Seg_Hex seven_seg_hex_28 (.d(_16bitdisplayint_7_digit1), .dp(_16bitdisplayint_7_dec1));
  _16BitDisplayInt _16bitdisplayint_8 (
    .Digit4(_16bitdisplayint_8_digit4), .Dec4(_16bitdisplayint_8_dec4), .Digit3(_16bitdisplayint_8_digit3),
    .Dec3(_16bitdisplayint_8_dec3), .Digit2(_16bitdisplayint_8_digit2), .Dec2(_16bitdisplayint_8_dec2),
    .Digit1(_16bitdisplayint_8_digit1), .Dec1(_16bitdisplayint_8_dec1), .Input(_16bitramint_1_display));
  LED led_2 (.in(_16bitramint_1_pref));
  LED led_3 (.in(_16bitramint_1_flash));
  _16BitRAMint _16bitramint_1 (
    .Sig15(_16bitregistercounterint_1_bus9[15]), .Sig14(_16bitregistercounterint_1_bus9[14]),
    .Sig13(_16bitregistercounterint_1_bus9[13]), .Sig12(_16bitregistercounterint_1_bus9[12]),
    .Sig11(_16bitregistercounterint_1_bus9[11]), .Sig10(_16bitregistercounterint_1_bus9[10]),
    .Sig9(_16bitregistercounterint_1_bus9[9]), .Sig8(_16bitregistercounterint_1_bus9[8]),
    .Sig7(_16bitregistercounterint_1_bus9[7]), .Sig6(_16bitregistercounterint_1_bus9[6]),
    .Sig5(_16bitregistercounterint_1_bus9[5]), .Sig4(_16bitregistercounterint_1_bus9[4]),
    .Sig3(_16bitregistercounterint_1_bus9[3]), .Sig2(_16bitregistercounterint_1_bus9[2]),
    .Sig1(_16bitregistercounterint_1_bus9[1]), .Sig0(_16bitregistercounterint_1_bus9[0]),
    .SRAM(_16bitramint_1_sram), .FLASH(_16bitramint_1_flash), .PREF(_16bitramint_1_pref),
    .RAMInH(_16bitcontrolint_1_nraminh), .RAMInL(_16bitcontrolint_1_nraminl),
    .RAMOut(_16bitcontrolint_1_nramout), .Display(_16bitramint_1_display),
    .ADDRin(_16bitregisterint2_2_signalout));
  LED led_4 (.in(_16bitramint_1_sram));
  Seven_Seg_Hex seven_seg_hex_29 (.d(_16bitdisplayint_8_digit4), .dp(_16bitdisplayint_8_dec4));
  Seven_Seg_Hex seven_seg_hex_30 (.d(_16bitdisplayint_8_digit3), .dp(_16bitdisplayint_8_dec3));
  Seven_Seg_Hex seven_seg_hex_31 (.d(_16bitdisplayint_9_digit4), .dp(_16bitdisplayint_9_dec4));
  _16BitDisplayInt _16bitdisplayint_9 (
    .Digit4(_16bitdisplayint_9_digit4), .Dec4(_16bitdisplayint_9_dec4), .Digit3(_16bitdisplayint_9_digit3),
    .Dec3(_16bitdisplayint_9_dec3), .Digit2(_16bitdisplayint_9_digit2), .Dec2(_16bitdisplayint_9_dec2),
    .Digit1(_16bitdisplayint_9_digit1), .Dec1(_16bitdisplayint_9_dec1),
    .Input(_16bitregisterswitchingint_3_signalout));
  _16BitRegisterSwitchingInt _16bitregisterswitchingint_3 (
    .ninHL(_16bitcontrolint_1_nbinhl), .ninLH(_16bitcontrolint_1_nbinlh), .ninHH(_16bitcontrolint_1_nbhh),
    .ninLL(_16bitcontrolint_1_nbll), .nIn(_16bitcontrolint_1_nbin), .noutSwap(_16bitcontrolint_1_nboutswap),
    .noutHH(_16bitcontrolint_1_nbouthh), .noutLL(_16bitcontrolint_1_nboutll),
    .nOut(_16bitcontrolint_1_nbout), .Clock(and_3_out), .Reset(_16bitcontrolint_1_breset),
    .Bus15(_16bitregistercounterint_1_bus9[15]), .Bus14(_16bitregistercounterint_1_bus9[14]),
    .Bus13(_16bitregistercounterint_1_bus9[13]), .Bus12(_16bitregistercounterint_1_bus9[12]),
    .Bus11(_16bitregistercounterint_1_bus9[11]), .Bus10(_16bitregistercounterint_1_bus9[10]),
    .Bus9(_16bitregistercounterint_1_bus9[9]), .Bus8(_16bitregistercounterint_1_bus9[8]),
    .Bus7(_16bitregistercounterint_1_bus9[7]), .Bus6(_16bitregistercounterint_1_bus9[6]),
    .Bus5(_16bitregistercounterint_1_bus9[5]), .Bus4(_16bitregistercounterint_1_bus9[4]),
    .Bus3(_16bitregistercounterint_1_bus9[3]), .Bus2(_16bitregistercounterint_1_bus9[2]),
    .Bus1(_16bitregistercounterint_1_bus9[1]), .Bus0(_16bitregistercounterint_1_bus9[0]),
    .SignalOut(_16bitregisterswitchingint_3_signalout));
  Seven_Seg_Hex seven_seg_hex_32 (.d(_16bitdisplayint_8_digit2), .dp(_16bitdisplayint_8_dec2));
  Seven_Seg_Hex seven_seg_hex_33 (.d(_16bitdisplayint_9_digit3), .dp(_16bitdisplayint_9_dec3));
  Seven_Seg_Hex seven_seg_hex_34 (.d(_16bitdisplayint_8_digit1), .dp(_16bitdisplayint_8_dec1));
  Seven_Seg_Hex seven_seg_hex_35 (.d(_16bitdisplayint_9_digit2), .dp(_16bitdisplayint_9_dec2));
  Seven_Seg_Hex seven_seg_hex_36 (.d(_16bitdisplayint_9_digit1), .dp(_16bitdisplayint_9_dec1));
  Seven_Seg_Hex seven_seg_hex_37 (.d(_16bitdisplayint_10_digit4), .dp(_16bitdisplayint_10_dec4));
  _16BitDisplayInt _16bitdisplayint_10 (
    .Digit4(_16bitdisplayint_10_digit4), .Dec4(_16bitdisplayint_10_dec4),
    .Digit3(_16bitdisplayint_10_digit3), .Dec3(_16bitdisplayint_10_dec3),
    .Digit2(_16bitdisplayint_10_digit2), .Dec2(_16bitdisplayint_10_dec2),
    .Digit1(_16bitdisplayint_10_digit1), .Dec1(_16bitdisplayint_10_dec1),
    .Input(_16bitregisterint2_3_signalout));
  _16BitRegisterInt2 _16bitregisterint2_3 (
    .RegOut(1'b1), .RegIn(_16bitcontrolint_1_nirin), .Clock(and_3_out), .Reset(Reset),
    .BusOut15(_16bitregistercounterint_1_bus9[15]), .BusOut14(_16bitregistercounterint_1_bus9[14]),
    .BusOut13(_16bitregistercounterint_1_bus9[13]), .BusOut12(_16bitregistercounterint_1_bus9[12]),
    .BusOut11(_16bitregistercounterint_1_bus9[11]), .BusOut10(_16bitregistercounterint_1_bus9[10]),
    .BusOut9(_16bitregistercounterint_1_bus9[9]), .BusOut8(_16bitregistercounterint_1_bus9[8]),
    .BusOut7(_16bitregistercounterint_1_bus9[7]), .BusOut6(_16bitregistercounterint_1_bus9[6]),
    .BusOut5(_16bitregistercounterint_1_bus9[5]), .BusOut4(_16bitregistercounterint_1_bus9[4]),
    .BusOut3(_16bitregistercounterint_1_bus9[3]), .BusOut2(_16bitregistercounterint_1_bus9[2]),
    .BusOut1(_16bitregistercounterint_1_bus9[1]), .BusOut0(_16bitregistercounterint_1_bus9[0]),
    .SignalOut(_16bitregisterint2_3_signalout));
  Seven_Seg_Hex seven_seg_hex_38 (.d(_16bitdisplayint_10_digit3), .dp(_16bitdisplayint_10_dec3));
  Seven_Seg_Hex seven_seg_hex_39 (.d(_16bitdisplayint_10_digit2), .dp(_16bitdisplayint_10_dec2));
  Seven_Seg_Hex seven_seg_hex_40 (.d(_16bitdisplayint_10_digit1), .dp(_16bitdisplayint_10_dec1));
  not not_3 (not_3_out, _16bitcontrolint_1_naout);
  not not_4 (not_4_out, _16bitcontrolint_1_naoutll);
  LED nAout (.in(not_3_out));
  LED nAoutLL (.in(not_4_out));
  not not_5 (not_5_out, _16bitcontrolint_1_naouthh);
  not not_6 (not_6_out, _16bitcontrolint_1_naoutswap);
  LED nAoutHH (.in(not_5_out));
  LED nAoutSwap (.in(not_6_out));
  LED Carry (.in(_16bitaluint_1_carryout));
  LED Neg (.in(_16bitaluint_1_negout));
  LED led_5 (.in(_16bitaluint_1_neg));
  LED led_6 (.in(_16bitaluint_1_zero));
  not not_7 (not_7_out, _16bitcontrolint_1_nain);
  not not_8 (not_8_out, _16bitcontrolint_1_nall);
  LED nAin (.in(not_7_out));
  LED nAinLL (.in(not_8_out));
  LED Zero (.in(_16bitaluint_1_zeroout));
  LED led_7 (.in(_16bitaluint_1_carry));
  not not_9 (not_9_out, and_3_out);
  not not_10 (not_10_out, _16bitcontrolint_1_nahh);
  not not_11 (not_11_out, _16bitcontrolint_1_nainlh);
  LED nAinHH (.in(not_10_out));
  LED nAinLH (.in(not_11_out));
  Seven_Seg_Hex seven_seg_hex_41 (.d(_16bitdisplayint_11_digit4), .dp(_16bitdisplayint_11_dec4));
  _16BitDisplayInt _16bitdisplayint_11 (
    .Digit4(_16bitdisplayint_11_digit4), .Dec4(_16bitdisplayint_11_dec4),
    .Digit3(_16bitdisplayint_11_digit3), .Dec3(_16bitdisplayint_11_dec3),
    .Digit2(_16bitdisplayint_11_digit2), .Dec2(_16bitdisplayint_11_dec2),
    .Digit1(_16bitdisplayint_11_digit1), .Dec1(_16bitdisplayint_11_dec1), .Input(_16bitaluint_1_displayout));
  _16BitALUInt _16bitaluint_1 (
    .BusOut15(_16bitregistercounterint_1_bus9[15]), .BusOut14(_16bitregistercounterint_1_bus9[14]),
    .BusOut13(_16bitregistercounterint_1_bus9[13]), .BusOut12(_16bitregistercounterint_1_bus9[12]),
    .BusOut11(_16bitregistercounterint_1_bus9[11]), .BusOut10(_16bitregistercounterint_1_bus9[10]),
    .BusOut9(_16bitregistercounterint_1_bus9[9]), .BusOut8(_16bitregistercounterint_1_bus9[8]),
    .BusOut7(_16bitregistercounterint_1_bus9[7]), .BusOut6(_16bitregistercounterint_1_bus9[6]),
    .BusOut5(_16bitregistercounterint_1_bus9[5]), .BusOut4(_16bitregistercounterint_1_bus9[4]),
    .BusOut3(_16bitregistercounterint_1_bus9[3]), .BusOut2(_16bitregistercounterint_1_bus9[2]),
    .BusOut1(_16bitregistercounterint_1_bus9[1]), .BusOut0(_16bitregistercounterint_1_bus9[0]),
    .ALUOut(_16bitcontrolint_1_naluout), .DisplayOut(_16bitaluint_1_displayout),
    .ALU0(_16bitcontrolint_1_alu0), .ALU1(_16bitcontrolint_1_alu1), .ALU2(_16bitcontrolint_1_alu2),
    .ALU3(_16bitcontrolint_1_alu3), .Clear(Reset), .CLK(and_3_out), .FlagiIn(_16bitcontrolint_1_nflagin),
    .zeroOut(_16bitaluint_1_zeroout), .negOut(_16bitaluint_1_negout), .carryOut(_16bitaluint_1_carryout),
    .zero(_16bitaluint_1_zero), .neg(_16bitaluint_1_neg), .carry(_16bitaluint_1_carry),
    .ASignal(_16bitregisterswitchingint_2_signalout), .BSignal(_16bitregisterswitchingint_3_signalout));
  _74161 _74161_1 (
    .pin1(_74161_1_pin1), .pin2(not_9_out), .pin3(1'b0), .pin4(1'b0), .pin5(1'b1), .pin6(1'b1), .pin7(1'b1),
    .pin8(1'b0), .pin9(_74161_1_pin9), .pin10(1'b1), .pin11(_74161_1_pin11), .pin12(_74161_1_pin12),
    .pin13(_74161_1_pin13), .pin14(_74161_1_pin14), .pin16(1'b1));  // open: pin15
  not not_12 (not_12_out, _16bitcontrolint_1_nainhl);
  LED nAinHL (.in(not_12_out));
  LED Areset (.in(_16bitcontrolint_1_areset));
  Seven_Seg_Hex seven_seg_hex_42 (.d(_16bitdisplayint_11_digit3), .dp(_16bitdisplayint_11_dec3));
  not not_13 (_74161_1_pin9, Reset);
  not not_14 (not_14_out, _16bitcontrolint_1_nbout);
  LED nBout (.in(not_14_out));
  Seven_Seg_Hex seven_seg_hex_43 (.d(_16bitdisplayint_11_digit2), .dp(_16bitdisplayint_11_dec2));
  not not_15 (not_15_out, _16bitcontrolint_1_nboutll);
  not not_16 (not_16_out, _16bitcontrolint_1_nbouthh);
  LED nBoutLL (.in(not_15_out));
  LED nBoutHH (.in(not_16_out));
  Seven_Seg_Hex seven_seg_hex_44 (.d(_16bitdisplayint_11_digit1), .dp(_16bitdisplayint_11_dec1));
  not not_17 (not_17_out, _16bitcontrolint_1_nboutswap);
  not not_18 (not_18_out, _16bitcontrolint_1_nbin);
  LED nBin (.in(not_18_out));
  LED nBoutSwap (.in(not_17_out));
  LED led_8 (.in(_74161_1_pin14));
  LED led_9 (.in(_74161_1_pin13));
  LED led_10 (.in(_74161_1_pin12));
  LED led_11 (.in(_74161_1_pin11));
  not not_19 (not_19_out, _16bitcontrolint_1_nbll);
  not not_20 (not_20_out, _16bitcontrolint_1_nbhh);
  LED nBinLL (.in(not_19_out));
  LED nBinHH (.in(not_20_out));
  _16BitControlInt _16bitcontrolint_1 (
    .Step1(_74161_1_pin14), .Step2(_74161_1_pin13), .Step3(_74161_1_pin12), .Step4(_74161_1_pin11),
    .Ins0(_16bitregisterint2_3_signalout[8]), .Ins1(_16bitregisterint2_3_signalout[9]),
    .Ins2(_16bitregisterint2_3_signalout[10]), .Ins3(_16bitregisterint2_3_signalout[11]),
    .Ins4(_16bitregisterint2_3_signalout[12]), .Ins5(_16bitregisterint2_3_signalout[13]),
    .Ins6(_16bitregisterint2_3_signalout[14]), .Ins7(_16bitregisterint2_3_signalout[15]),
    .Zero(_16bitaluint_1_zeroout), .Carry(_16bitaluint_1_carryout), .Neg(_16bitaluint_1_negout),
    .Interupt(1'b0), .Extra(1'b0), .nAOut(_16bitcontrolint_1_naout), .nAoutLL(_16bitcontrolint_1_naoutll),
    .nAOutHH(_16bitcontrolint_1_naouthh), .nAoutSwap(_16bitcontrolint_1_naoutswap),
    .nAin(_16bitcontrolint_1_nain), .nALL(_16bitcontrolint_1_nall), .nAHH(_16bitcontrolint_1_nahh),
    .nAInLH(_16bitcontrolint_1_nainlh), .nAInHL(_16bitcontrolint_1_nainhl),
    .Areset(_16bitcontrolint_1_areset), .nBOut(_16bitcontrolint_1_nbout),
    .nBoutLL(_16bitcontrolint_1_nboutll), .nBOutHH(_16bitcontrolint_1_nbouthh),
    .nBoutSwap(_16bitcontrolint_1_nboutswap), .nBin(_16bitcontrolint_1_nbin), .nBLL(_16bitcontrolint_1_nbll),
    .nBHH(_16bitcontrolint_1_nbhh), .nBInLH(_16bitcontrolint_1_nbinlh), .nBInHL(_16bitcontrolint_1_nbinhl),
    .Breset(_16bitcontrolint_1_breset), .nCout(_16bitcontrolint_1_ncout), .nCin(_16bitcontrolint_1_ncin),
    .nCinc(_16bitcontrolint_1_ncinc), .nCdec(_16bitcontrolint_1_ncdec), .Creset(_16bitcontrolint_1_creset),
    .nDout(_16bitcontrolint_1_ndout), .nDoutLL(_16bitcontrolint_1_ndoutll),
    .nDoutHH(_16bitcontrolint_1_ndouthh), .nDoutSwap(_16bitcontrolint_1_ndoutswap),
    .nDinHH(_16bitcontrolint_1_ndinhh), .nDinLL(_16bitcontrolint_1_ndinll),
    .Dreset(_16bitcontrolint_1_dreset), .nXout(_16bitcontrolint_1_nxout), .nXin(_16bitcontrolint_1_nxin),
    .nPCout(_16bitcontrolint_1_npcout), .nPCin(_16bitcontrolint_1_npcin), .nPCinc(_16bitcontrolint_1_npcinc),
    .nPCdec(_16bitcontrolint_1_npcdec), .nSTACKout(_16bitcontrolint_1_nstackout),
    .nSTACKin(_16bitcontrolint_1_nstackin), .nSTACKinc(_16bitcontrolint_1_nstackinc),
    .nSTACKdec(_16bitcontrolint_1_nstackdec), .nRAMout(_16bitcontrolint_1_nramout),
    .nRAMinL(_16bitcontrolint_1_nraminl), .nRAMinH(_16bitcontrolint_1_nraminh),
    .nMARin(_16bitcontrolint_1_nmarin), .nIRin(_16bitcontrolint_1_nirin),
    .nALUout(_16bitcontrolint_1_naluout), .ALU0(_16bitcontrolint_1_alu0), .ALU1(_16bitcontrolint_1_alu1),
    .ALU2(_16bitcontrolint_1_alu2), .ALU3(_16bitcontrolint_1_alu3), .nFLAGin(_16bitcontrolint_1_nflagin),
    .RESET(_16bitcontrolint_1_reset), .HALT(_16bitcontrolint_1_halt), .NEXTins(_74161_1_pin1));  // open: nEout, nEin, nFout, nFin, nGout, nGin, nHout, nHin, Extra1, Extra4, Extra2, Extra3, INTERpause, INTERplay, ClearINTER, INTERen, INTERdis, nEXTRAout1, nEXTRAout2, nEXTRAout3, nEXTRAout4, nINTERflagOut, nINTERregOut
  not not_21 (not_21_out, _16bitcontrolint_1_nbinlh);
  not not_22 (not_22_out, _16bitcontrolint_1_nbinhl);
  LED nBinLH (.in(not_21_out));
  LED nBinHL (.in(not_22_out));
  not not_23 (not_23_out, _16bitcontrolint_1_ncout);
  LED Breset (.in(_16bitcontrolint_1_breset));
  LED nCout (.in(not_23_out));
  not not_24 (not_24_out, _16bitcontrolint_1_ncinc);
  not not_25 (not_25_out, _16bitcontrolint_1_ncin);
  LED nCin (.in(not_25_out));
  LED nCinc (.in(not_24_out));
  _16BitDisplayInt _16bitdisplayint_12 (
    .Digit4(_16bitdisplayint_12_digit4), .Dec4(_16bitdisplayint_12_dec4),
    .Digit3(_16bitdisplayint_12_digit3), .Dec3(_16bitdisplayint_12_dec3),
    .Digit2(_16bitdisplayint_12_digit2), .Dec2(_16bitdisplayint_12_dec2),
    .Digit1(_16bitdisplayint_12_digit1), .Dec1(_16bitdisplayint_12_dec1),
    .Input(_16bitregistercounterint_3_signalout));
  _16BitRegisterCounterInt _16bitregistercounterint_3 (
    .RegOut(_16bitcontrolint_1_ncout), .RegIn(_16bitcontrolint_1_ncin), .Reset(_16bitcontrolint_1_creset),
    .Dec(_16bitcontrolint_1_ncdec), .Inc(_16bitcontrolint_1_ncinc),
    .SignalOut(_16bitregistercounterint_3_signalout), .Bus15(_16bitregistercounterint_1_bus9[15]),
    .Bus14(_16bitregistercounterint_1_bus9[14]), .Bus13(_16bitregistercounterint_1_bus9[13]),
    .Bus12(_16bitregistercounterint_1_bus9[12]), .Bus11(_16bitregistercounterint_1_bus9[11]),
    .Bus10(_16bitregistercounterint_1_bus9[10]), .Bus9(_16bitregistercounterint_1_bus9[9]),
    .Bus8(_16bitregistercounterint_1_bus9[8]), .Bus7(_16bitregistercounterint_1_bus9[7]),
    .Bus6(_16bitregistercounterint_1_bus9[6]), .Bus5(_16bitregistercounterint_1_bus9[5]),
    .Bus4(_16bitregistercounterint_1_bus9[4]), .Bus3(_16bitregistercounterint_1_bus9[3]),
    .Bus2(_16bitregistercounterint_1_bus9[2]), .Bus1(_16bitregistercounterint_1_bus9[1]),
    .Bus0(_16bitregistercounterint_1_bus9[0]));
  not not_26 (not_26_out, _16bitcontrolint_1_ncdec);
  LED Creset (.in(_16bitcontrolint_1_creset));
  LED nCdec (.in(not_26_out));
  Seven_Seg_Hex seven_seg_hex_45 (.d(_16bitdisplayint_12_digit4), .dp(_16bitdisplayint_12_dec4));
  not not_27 (not_27_out, _16bitcontrolint_1_ndout);
  LED nDout (.in(not_27_out));
  Seven_Seg_Hex seven_seg_hex_46 (.d(_16bitdisplayint_12_digit3), .dp(_16bitdisplayint_12_dec3));
  not not_28 (not_28_out, _16bitcontrolint_1_ndoutll);
  not not_29 (not_29_out, _16bitcontrolint_1_ndouthh);
  LED nDoutLL (.in(not_28_out));
  LED nDoutHH (.in(not_29_out));
  Seven_Seg_Hex seven_seg_hex_47 (.d(_16bitdisplayint_12_digit2), .dp(_16bitdisplayint_12_dec2));
  not not_30 (not_30_out, _16bitcontrolint_1_ndoutswap);
  not not_31 (not_31_out, _16bitcontrolint_1_ndinhh);
  LED nDoutSwap (.in(not_30_out));
  LED nDinH (.in(not_31_out));
  Seven_Seg_Hex seven_seg_hex_48 (.d(_16bitdisplayint_12_digit1), .dp(_16bitdisplayint_12_dec1));
  not not_32 (not_32_out, _16bitcontrolint_1_ndinll);
  LED nDinL (.in(not_32_out));
  LED Dreset (.in(_16bitcontrolint_1_dreset));
  not not_33 (not_33_out, _16bitcontrolint_1_nxout);
  not not_34 (not_34_out, _16bitcontrolint_1_nxin);
  LED nXout (.in(not_33_out));
  LED nXin (.in(not_34_out));
  not not_35 (not_35_out, _16bitcontrolint_1_npcout);
  LED nPCout (.in(not_35_out));
  not not_36 (not_36_out, _16bitcontrolint_1_npcin);
  not not_37 (not_37_out, _16bitcontrolint_1_npcinc);
  LED nPCin (.in(not_36_out));
  LED nPCinc (.in(not_37_out));
  not not_38 (not_38_out, _16bitcontrolint_1_npcdec);
  LED nPCdec (.in(not_38_out));
  not not_39 (not_39_out, _16bitcontrolint_1_nstackout);
  not not_40 (not_40_out, _16bitcontrolint_1_nstackin);
  LED nSTACKout (.in(not_39_out));
  LED nSTACKin (.in(not_40_out));
  not not_41 (not_41_out, _16bitcontrolint_1_nstackinc);
  not not_42 (not_42_out, _16bitcontrolint_1_nstackdec);
  LED nSTACKinc (.in(not_41_out));
  LED nSTACKdec (.in(not_42_out));
  not not_43 (not_43_out, _16bitcontrolint_1_nirin);
  not not_44 (not_44_out, _16bitcontrolint_1_nmarin);
  LED nIRin (.in(not_43_out));
  LED nMARin (.in(not_44_out));
  not not_45 (not_45_out, _16bitcontrolint_1_nramout);
  LED nRAMout (.in(not_45_out));
  not not_46 (not_46_out, _16bitcontrolint_1_nraminl);
  not not_47 (not_47_out, _16bitcontrolint_1_nraminh);
  LED nRAMinL (.in(not_46_out));
  LED nRAMinH (.in(not_47_out));
  not not_48 (not_48_out, _16bitcontrolint_1_naluout);
  LED nALUout (.in(not_48_out));
  not not_49 (not_49_out, _16bitcontrolint_1_nflagin);
  LED nFLAGin (.in(not_49_out));
  LED ALU1 (.in(_16bitcontrolint_1_alu0));
  LED ALU2 (.in(_16bitcontrolint_1_alu1));
  LED ALU3 (.in(_16bitcontrolint_1_alu2));
  LED nALU4 (.in(_16bitcontrolint_1_alu3));
  LED u_RESET (.in(_16bitcontrolint_1_reset));
  LED HALT (.in(_16bitcontrolint_1_halt));
  LED NEXTins (.in(_74161_1_pin1));
endmodule
