// Digital circuit 16Bit2.dig as structural Verilog
module _16Bit2 (
  input  nPCIn,
  input  nPCOut,
  input  nPCInc,
  input  nPCDec,
  input  nSTACKIn,
  input  nSTACKOut,
  input  nSTACKInc,
  input  nSTACKDec,
  input  nCIn,
  input  nCOut,
  input  nCInc,
  input  nCDec,
  input  CReset,
  input  nAOut,
  input  AReset,
  input  nAOutLL,
  input  nAOutHH,
  input  nAOutSwap,
  input  nAIn,
  input  nAInLL,
  input  nAInHH,
  input  nAInLH,
  input  nAInHL,
  input  nBOut,
  input  BReset,
  input  nBOutLL,
  input  nBOutHH,
  input  nBOutSwap,
  input  nBIn,
  input  nBInLL,
  input  nBInHH,
  input  nBInLH,
  input  nBInHL,
  input  nACLOut,
  input  ALU3,
  input  ALU2,
  input  ALU1,
  input  ALU0,
  input  nFLAGin,
  input  nDOut,
  input  DReset,
  input  nDOutLL,
  input  nDOutHH,
  input  nDOutSwap,
  input  nDInLL,
  input  nDInHH,
  input  nXin,
  input  nXOut,
  input  nMARin,
  input  nIRin,
  input  nIROut,
  input  clk,
  input  Pulse,
  input  Source,
  input  Reset,
  input  Halt,
  input  Pulse_2
);

  wire _16bitaluint_1_carry, _16bitaluint_1_carryout, _16bitaluint_1_neg, _16bitaluint_1_negout,
       _16bitaluint_1_zero, _16bitaluint_1_zeroout, _16bitdisplayint_1_dec1, _16bitdisplayint_1_dec2,
       _16bitdisplayint_1_dec3, _16bitdisplayint_1_dec4, _16bitdisplayint_2_dec1, _16bitdisplayint_2_dec2,
       _16bitdisplayint_2_dec3, _16bitdisplayint_2_dec4, _16bitdisplayint_3_dec1, _16bitdisplayint_3_dec2,
       _16bitdisplayint_3_dec3, _16bitdisplayint_3_dec4, _16bitdisplayint_4_dec1, _16bitdisplayint_4_dec2,
       _16bitdisplayint_4_dec3, _16bitdisplayint_4_dec4, _16bitdisplayint_5_dec1, _16bitdisplayint_5_dec2,
       _16bitdisplayint_5_dec3, _16bitdisplayint_5_dec4, _16bitdisplayint_6_dec1, _16bitdisplayint_6_dec2,
       _16bitdisplayint_6_dec3, _16bitdisplayint_6_dec4, _16bitdisplayint_7_dec1, _16bitdisplayint_7_dec2,
       _16bitdisplayint_7_dec3, _16bitdisplayint_7_dec4, _16bitdisplayint_8_dec1, _16bitdisplayint_8_dec2,
       _16bitdisplayint_8_dec3, _16bitdisplayint_8_dec4, _16bitdisplayint_9_dec1, _16bitdisplayint_9_dec2,
       _16bitdisplayint_9_dec3, _16bitdisplayint_9_dec4, _16bitdisplayint_10_dec1, _16bitdisplayint_10_dec2,
       _16bitdisplayint_10_dec3, _16bitdisplayint_10_dec4, _16bitdisplayint_11_dec1,
       _16bitdisplayint_11_dec2, _16bitdisplayint_11_dec3, _16bitdisplayint_11_dec4,
       _16bitdisplayint_12_dec1, _16bitdisplayint_12_dec2, _16bitdisplayint_12_dec3,
       _16bitdisplayint_12_dec4, _74161_1_pin9, _74161_1_pin11, _74161_1_pin12, _74161_1_pin13,
       _74161_1_pin14, and_1_out, and_2_out, and_3_out, not_1_out, not_2_out, not_3_out, or_1_out, or_2_out;
  wire [3:0] _16bitdisplayint_1_digit1, _16bitdisplayint_1_digit2, _16bitdisplayint_1_digit3,
       _16bitdisplayint_1_digit4, _16bitdisplayint_2_digit1, _16bitdisplayint_2_digit2,
       _16bitdisplayint_2_digit3, _16bitdisplayint_2_digit4, _16bitdisplayint_3_digit1,
       _16bitdisplayint_3_digit2, _16bitdisplayint_3_digit3, _16bitdisplayint_3_digit4,
       _16bitdisplayint_4_digit1, _16bitdisplayint_4_digit2, _16bitdisplayint_4_digit3,
       _16bitdisplayint_4_digit4, _16bitdisplayint_5_digit1, _16bitdisplayint_5_digit2,
       _16bitdisplayint_5_digit3, _16bitdisplayint_5_digit4, _16bitdisplayint_6_digit1,
       _16bitdisplayint_6_digit2, _16bitdisplayint_6_digit3, _16bitdisplayint_6_digit4,
       _16bitdisplayint_7_digit1, _16bitdisplayint_7_digit2, _16bitdisplayint_7_digit3,
       _16bitdisplayint_7_digit4, _16bitdisplayint_8_digit1, _16bitdisplayint_8_digit2,
       _16bitdisplayint_8_digit3, _16bitdisplayint_8_digit4, _16bitdisplayint_9_digit1,
       _16bitdisplayint_9_digit2, _16bitdisplayint_9_digit3, _16bitdisplayint_9_digit4,
       _16bitdisplayint_10_digit1, _16bitdisplayint_10_digit2, _16bitdisplayint_10_digit3,
       _16bitdisplayint_10_digit4, _16bitdisplayint_11_digit1, _16bitdisplayint_11_digit2,
       _16bitdisplayint_11_digit3, _16bitdisplayint_11_digit4, _16bitdisplayint_12_digit1,
       _16bitdisplayint_12_digit2, _16bitdisplayint_12_digit3, _16bitdisplayint_12_digit4;
  wire [15:0] _16bitaluint_1_displayout, _16bitregistercounterint_1_bus9,
       _16bitregistercounterint_1_signalout, _16bitregistercounterint_2_signalout,
       _16bitregistercounterint_3_signalout, _16bitregisterint2_1_signalout, _16bitregisterint2_2_signalout,
       _16bitregisterint2_3_signalout, _16bitregisterswitchingint_1_signalout,
       _16bitregisterswitchingint_2_signalout, _16bitregisterswitchingint_3_signalout;

  or or_1 (or_1_out, Pulse, Pulse_2);
  not not_1 (not_1_out, Source);
  Seven_Seg_Hex seven_seg_hex_1 (.d(_16bitdisplayint_1_digit4), .dp(_16bitdisplayint_1_dec4));
  _16BitDisplayInt _16bitdisplayint_1 (
    .Digit4(_16bitdisplayint_1_digit4), .Dec4(_16bitdisplayint_1_dec4), .Digit3(_16bitdisplayint_1_digit3),
    .Dec3(_16bitdisplayint_1_dec3), .Digit2(_16bitdisplayint_1_digit2), .Dec2(_16bitdisplayint_1_dec2),
    .Digit1(_16bitdisplayint_1_digit1), .Dec1(_16bitdisplayint_1_dec1),
    .Input(_16bitregistercounterint_1_bus9));
  and and_1 (and_1_out, or_1_out, not_1_out);
  and and_2 (and_2_out, Source, clk);
  not not_2 (not_2_out, Halt);
  Seven_Seg_Hex seven_seg_hex_2 (.d(_16bitdisplayint_1_digit3), .dp(_16bitdisplayint_1_dec3));
  or or_2 (or_2_out, and_1_out, and_2_out);
  Seven_Seg_Hex seven_seg_hex_3 (.d(_16bitdisplayint_1_digit2), .dp(_16bitdisplayint_1_dec2));
  Seven_Seg_Hex seven_seg_hex_4 (.d(_16bitdisplayint_1_digit1), .dp(_16bitdisplayint_1_dec1));
  and and_3 (and_3_out, or_2_out, not_2_out);
  LED led_1 (.in(and_3_out));
  _16BitDisplayInt _16bitdisplayint_2 (
    .Digit4(_16bitdisplayint_2_digit4), .Dec4(_16bitdisplayint_2_dec4), .Digit3(_16bitdisplayint_2_digit3),
    .Dec3(_16bitdisplayint_2_dec3), .Digit2(_16bitdisplayint_2_digit2), .Dec2(_16bitdisplayint_2_dec2),
    .Digit1(_16bitdisplayint_2_digit1), .Dec1(_16bitdisplayint_2_dec1),
    .Input(_16bitregistercounterint_1_signalout));
  _16BitRegisterCounterInt _16bitregistercounterint_1 (
    .RegOut(nPCOut), .RegIn(nPCIn), .Reset(Reset), .Dec(nPCDec), .Inc(nPCInc),
    .SignalOut(_16bitregistercounterint_1_signalout), .Bus15(_16bitregistercounterint_1_bus9[15]),
    .Bus14(_16bitregistercounterint_1_bus9[14]), .Bus13(_16bitregistercounterint_1_bus9[13]),
    .Bus12(_16bitregistercounterint_1_bus9[12]), .Bus11(_16bitregistercounterint_1_bus9[11]),
    .Bus10(_16bitregistercounterint_1_bus9[10]), .Bus9(_16bitregistercounterint_1_bus9[9]),
    .Bus8(_16bitregistercounterint_1_bus9[8]), .Bus7(_16bitregistercounterint_1_bus9[7]),
    .Bus6(_16bitregistercounterint_1_bus9[6]), .Bus5(_16bitregistercounterint_1_bus9[5]),
    .Bus4(_16bitregistercounterint_1_bus9[4]), .Bus3(_16bitregistercounterint_1_bus9[3]),
    .Bus2(_16bitregistercounterint_1_bus9[2]), .Bus1(_16bitregistercounterint_1_bus9[1]),
    .Bus0(_16bitregistercounterint_1_bus9[0]));
  _16BitDisplayInt _16bitdisplayint_3 (
    .Digit4(_16bitdisplayint_3_digit4), .Dec4(_16bitdisplayint_3_dec4), .Digit3(_16bitdisplayint_3_digit3),
    .Dec3(_16bitdisplayint_3_dec3), .Digit2(_16bitdisplayint_3_digit2), .Dec2(_16bitdisplayint_3_dec2),
    .Digit1(_16bitdisplayint_3_digit1), .Dec1(_16bitdisplayint_3_dec1),
    .Input(_16bitregisterswitchingint_1_signalout));
  _16BitRegisterSwitchingInt _16bitregisterswitchingint_1 (
    .ninHL(1'b1), .ninLH(1'b1), .ninHH(nDInHH), .ninLL(nDInLL), .nIn(1'b1), .noutSwap(nDOutSwap),
    .noutHH(nDOutHH), .noutLL(nDOutLL), .nOut(nDOut), .Clock(and_3_out), .Reset(DReset),
    .Bus15(_16bitregistercounterint_1_bus9[15]), .Bus14(_16bitregistercounterint_1_bus9[14]),
    .Bus13(_16bitregistercounterint_1_bus9[13]), .Bus12(_16bitregistercounterint_1_bus9[12]),
    .Bus11(_16bitregistercounterint_1_bus9[11]), .Bus10(_16bitregistercounterint_1_bus9[10]),
    .Bus9(_16bitregistercounterint_1_bus9[9]), .Bus8(_16bitregistercounterint_1_bus9[8]),
    .Bus7(_16bitregistercounterint_1_bus9[7]), .Bus6(_16bitregistercounterint_1_bus9[6]),
    .Bus5(_16bitregistercounterint_1_bus9[5]), .Bus4(_16bitregistercounterint_1_bus9[4]),
    .Bus3(_16bitregistercounterint_1_bus9[3]), .Bus2(_16bitregistercounterint_1_bus9[2]),
    .Bus1(_16bitregistercounterint_1_bus9[1]), .Bus0(_16bitregistercounterint_1_bus9[0]),
    .SignalOut(_16bitregisterswitchingint_1_signalout));
  Seven_Seg_Hex seven_seg_hex_5 (.d(_16bitdisplayint_2_digit4), .dp(_16bitdisplayint_2_dec4));
  Seven_Seg_Hex seven_seg_hex_6 (.d(_16bitdisplayint_3_digit4), .dp(_16bitdisplayint_3_dec4));
  Seven_Seg_Hex seven_seg_hex_7 (.d(_16bitdisplayint_2_digit3), .dp(_16bitdisplayint_2_dec3));
  Seven_Seg_Hex seven_seg_hex_8 (.d(_16bitdisplayint_3_digit3), .dp(_16bitdisplayint_3_dec3));
  Seven_Seg_Hex seven_seg_hex_9 (.d(_16bitdisplayint_2_digit2), .dp(_16bitdisplayint_2_dec2));
  Seven_Seg_Hex seven_seg_hex_10 (.d(_16bitdisplayint_3_digit2), .dp(_16bitdisplayint_3_dec2));
  Seven_Seg_Hex seven_seg_hex_11 (.d(_16bitdisplayint_2_digit1), .dp(_16bitdisplayint_2_dec1));
  Seven_Seg_Hex seven_seg_hex_12 (.d(_16bitdisplayint_3_digit1), .dp(_16bitdisplayint_3_dec1));
  _16BitDisplayInt _16bitdisplayint_4 (
    .Digit4(_16bitdisplayint_4_digit4), .Dec4(_16bitdisplayint_4_dec4), .Digit3(_16bitdisplayint_4_digit3),
    .Dec3(_16bitdisplayint_4_dec3), .Digit2(_16bitdisplayint_4_digit2), .Dec2(_16bitdisplayint_4_dec2),
    .Digit1(_16bitdisplayint_4_digit1), .Dec1(_16bitdisplayint_4_dec1),
    .Input(_16bitregistercounterint_2_signalout));
  _16BitRegisterCounterInt _16bitregistercounterint_2 (
    .RegOut(nSTACKOut), .RegIn(nSTACKIn), .Reset(Reset), .Dec(nSTACKDec), .Inc(nSTACKInc),
    .SignalOut(_16bitregistercounterint_2_signalout), .Bus15(_16bitregistercounterint_1_bus9[15]),
    .Bus14(_16bitregistercounterint_1_bus9[14]), .Bus13(_16bitregistercounterint_1_bus9[13]),
    .Bus12(_16bitregistercounterint_1_bus9[12]), .Bus11(_16bitregistercounterint_1_bus9[11]),
    .Bus10(_16bitregistercounterint_1_bus9[10]), .Bus9(_16bitregistercounterint_1_bus9[9]),
    .Bus8(_16bitregistercounterint_1_bus9[8]), .Bus7(_16bitregistercounterint_1_bus9[7]),
    .Bus6(_16bitregistercounterint_1_bus9[6]), .Bus5(_16bitregistercounterint_1_bus9[5]),
    .Bus4(_16bitregistercounterint_1_bus9[4]), .Bus3(_16bitregistercounterint_1_bus9[3]),
    .Bus2(_16bitregistercounterint_1_bus9[2]), .Bus1(_16bitregistercounterint_1_bus9[1]),
    .Bus0(_16bitregistercounterint_1_bus9[0]));
  Seven_Seg_Hex seven_seg_hex_13 (.d(_16bitdisplayint_4_digit4), .dp(_16bitdisplayint_4_dec4));
  Seven_Seg_Hex seven_seg_hex_14 (.d(_16bitdisplayint_5_digit4), .dp(_16bitdisplayint_5_dec4));
  _16BitDisplayInt _16bitdisplayint_5 (
    .Digit4(_16bitdisplayint_5_digit4), .Dec4(_16bitdisplayint_5_dec4), .Digit3(_16bitdisplayint_5_digit3),
    .Dec3(_16bitdisplayint_5_dec3), .Digit2(_16bitdisplayint_5_digit2), .Dec2(_16bitdisplayint_5_dec2),
    .Digit1(_16bitdisplayint_5_digit1), .Dec1(_16bitdisplayint_5_dec1), .Input(_16bitregisterint2_1_signalout));
  _16BitRegisterInt2 _16bitregisterint2_1 (
    .RegOut(nXOut), .RegIn(nXin), .Clock(and_3_out), .Reset(Reset),
    .BusOut15(_16bitregistercounterint_1_bus9[15]), .BusOut14(_16bitregistercounterint_1_bus9[14]),
    .BusOut13(_16bitregistercounterint_1_bus9[13]), .BusOut12(_16bitregistercounterint_1_bus9[12]),
    .BusOut11(_16bitregistercounterint_1_bus9[11]), .BusOut10(_16bitregistercounterint_1_bus9[10]),
    .BusOut9(_16bitregistercounterint_1_bus9[9]), .BusOut8(_16bitregistercounterint_1_bus9[8]),
    .BusOut7(_16bitregistercounterint_1_bus9[7]), .BusOut6(_16bitregistercounterint_1_bus9[6]),
    .BusOut5(_16bitregistercounterint_1_bus9[5]), .BusOut4(_16bitregistercounterint_1_bus9[4]),
    .BusOut3(_16bitregistercounterint_1_bus9[3]), .BusOut2(_16bitregistercounterint_1_bus9[2]),
    .BusOut1(_16bitregistercounterint_1_bus9[1]), .BusOut0(_16bitregistercounterint_1_bus9[0]),
    .SignalOut(_16bitregisterint2_1_signalout));
  Seven_Seg_Hex seven_seg_hex_15 (.d(_16bitdisplayint_4_digit3), .dp(_16bitdisplayint_4_dec3));
  Seven_Seg_Hex seven_seg_hex_16 (.d(_16bitdisplayint_5_digit3), .dp(_16bitdisplayint_5_dec3));
  Seven_Seg_Hex seven_seg_hex_17 (.d(_16bitdisplayint_4_digit2), .dp(_16bitdisplayint_4_dec2));
  Seven_Seg_Hex seven_seg_hex_18 (.d(_16bitdisplayint_5_digit2), .dp(_16bitdisplayint_5_dec2));
  Seven_Seg_Hex seven_seg_hex_19 (.d(_16bitdisplayint_4_digit1), .dp(_16bitdisplayint_4_dec1));
  Seven_Seg_Hex seven_seg_hex_20 (.d(_16bitdisplayint_5_digit1), .dp(_16bitdisplayint_5_dec1));
  _16BitDisplayInt _16bitdisplayint_6 (
    .Digit4(_16bitdisplayint_6_digit4), .Dec4(_16bitdisplayint_6_dec4), .Digit3(_16bitdisplayint_6_digit3),
    .Dec3(_16bitdisplayint_6_dec3), .Digit2(_16bitdisplayint_6_digit2), .Dec2(_16bitdisplayint_6_dec2),
    .Digit1(_16bitdisplayint_6_digit1), .Dec1(_16bitdisplayint_6_dec1), .Input(_16bitregisterint2_2_signalout));
  _16BitRegisterInt2 _16bitregisterint2_2 (
    .RegOut(1'b1), .RegIn(nMARin), .Clock(and_3_out), .Reset(Reset),
    .BusOut15(_16bitregistercounterint_1_bus9[15]), .BusOut14(_16bitregistercounterint_1_bus9[14]),
    .BusOut13(_16bitregistercounterint_1_bus9[13]), .BusOut12(_16bitregistercounterint_1_bus9[12]),
    .BusOut11(_16bitregistercounterint_1_bus9[11]), .BusOut10(_16bitregistercounterint_1_bus9[10]),
    .BusOut9(_16bitregistercounterint_1_bus9[9]), .BusOut8(_16bitregistercounterint_1_bus9[8]),
    .BusOut7(_16bitregistercounterint_1_bus9[7]), .BusOut6(_16bitregistercounterint_1_bus9[6]),
    .BusOut5(_16bitregistercounterint_1_bus9[5]), .BusOut4(_16bitregistercounterint_1_bus9[4]),
    .BusOut3(_16bitregistercounterint_1_bus9[3]), .BusOut2(_16bitregistercounterint_1_bus9[2]),
    .BusOut1(_16bitregistercounterint_1_bus9[1]), .BusOut0(_16bitregistercounterint_1_bus9[0]),
    .SignalOut(_16bitregisterint2_2_signalout));
  _16BitDisplayInt _16bitdisplayint_7 (
    .Digit4(_16bitdisplayint_7_digit4), .Dec4(_16bitdisplayint_7_dec4), .Digit3(_16bitdisplayint_7_digit3),
    .Dec3(_16bitdisplayint_7_dec3), .Digit2(_16bitdisplayint_7_digit2), .Dec2(_16bitdisplayint_7_dec2),
    .Digit1(_16bitdisplayint_7_digit1), .Dec1(_16bitdisplayint_7_dec1),
    .Input(_16bitregisterswitchingint_2_signalout));
  _16BitRegisterSwitchingInt _16bitregisterswitchingint_2 (
    .ninHL(nAInHL), .ninLH(nAInLH), .ninHH(nAInHH), .ninLL(nAInLL), .nIn(nAIn), .noutSwap(nAOutSwap),
    .noutHH(nAOutHH), .noutLL(nAOutLL), .nOut(nAOut), .Clock(and_3_out), .Reset(AReset),
    .Bus15(_16bitregistercounterint_1_bus9[15]), .Bus14(_16bitregistercounterint_1_bus9[14]),
    .Bus13(_16bitregistercounterint_1_bus9[13]), .Bus12(_16bitregistercounterint_1_bus9[12]),
    .Bus11(_16bitregistercounterint_1_bus9[11]), .Bus10(_16bitregistercounterint_1_bus9[10]),
    .Bus9(_16bitregistercounterint_1_bus9[9]), .Bus8(_16bitregistercounterint_1_bus9[8]),
    .Bus7(_16bitregistercounterint_1_bus9[7]), .Bus6(_16bitregistercounterint_1_bus9[6]),
    .Bus5(_16bitregistercounterint_1_bus9[5]), .Bus4(_16bitregistercounterint_1_bus9[4]),
    .Bus3(_16bitregistercounterint_1_bus9[3]), .Bus2(_16bitregistercounterint_1_bus9[2]),
    .Bus1(_16bitregistercounterint_1_bus9[1]), .Bus0(_16bitregistercounterint_1_bus9[0]),
    .SignalOut(_16bitregisterswitchingint_2_signalout));
  Seven_Seg_Hex seven_seg_hex_21 (.d(_16bitdisplayint_6_digit4), .dp(_16bitdisplayint_6_dec4));
  Seven_Seg_Hex seven_seg_hex_22 (.d(_16bitdisplayint_7_digit4), .dp(_16bitdisplayint_7_dec4));
  Seven_Seg_Hex seven_seg_hex_23 (.d(_16bitdisplayint_6_digit3), .dp(_16bitdisplayint_6_dec3));
  Seven_Seg_Hex seven_seg_hex_24 (.d(_16bitdisplayint_7_digit3), .dp(_16bitdisplayint_7_dec3));
  Seven_Seg_Hex seven_seg_hex_25 (.d(_16bitdisplayint_6_digit2), .dp(_16bitdisplayint_6_dec2));
  Seven_Seg_Hex seven_seg_hex_26 (.d(_16bitdisplayint_7_digit2), .dp(_16bitdisplayint_7_dec2));
  Seven_Seg_Hex seven_seg_hex_27 (.d(_16bitdisplayint_6_digit1), .dp(_16bitdisplayint_6_dec1));
  Seven_Seg_Hex seven_seg_hex_28 (.d(_16bitdisplayint_7_digit1), .dp(_16bitdisplayint_7_dec1));
  Seven_Seg_Hex seven_seg_hex_29 (.d(_16bitdisplayint_8_digit4), .dp(_16bitdisplayint_8_dec4));
  _16BitDisplayInt _16bitdisplayint_8 (
    .Digit4(_16bitdisplayint_8_digit4), .Dec4(_16bitdisplayint_8_dec4), .Digit3(_16bitdisplayint_8_digit3),
    .Dec3(_16bitdisplayint_8_dec3), .Digit2(_16bitdisplayint_8_digit2), .Dec2(_16bitdisplayint_8_dec2),
    .Digit1(_16bitdisplayint_8_digit1), .Dec1(_16bitdisplayint_8_dec1), .Input(_16bitregisterint2_2_signalout));
  Seven_Seg_Hex seven_seg_hex_30 (.d(_16bitdisplayint_8_digit3), .dp(_16bitdisplayint_8_dec3));
  Seven_Seg_Hex seven_seg_hex_31 (.d(_16bitdisplayint_8_digit2), .dp(_16bitdisplayint_8_dec2));
  Seven_Seg_Hex seven_seg_hex_32 (.d(_16bitdisplayint_9_digit4), .dp(_16bitdisplayint_9_dec4));
  _16BitDisplayInt _16bitdisplayint_9 (
    .Digit4(_16bitdisplayint_9_digit4), .Dec4(_16bitdisplayint_9_dec4), .Digit3(_16bitdisplayint_9_digit3),
    .Dec3(_16bitdisplayint_9_dec3), .Digit2(_16bitdisplayint_9_digit2), .Dec2(_16bitdisplayint_9_dec2),
    .Digit1(_16bitdisplayint_9_digit1), .Dec1(_16bitdisplayint_9_dec1),
    .Input(_16bitregisterswitchingint_3_signalout));
  _16BitRegisterSwitchingInt _16bitregisterswitchingint_3 (
    .ninHL(nBInHL), .ninLH(nBInLH), .ninHH(nBInHH), .ninLL(nBInLL), .nIn(nBIn), .noutSwap(nBOutSwap),
    .noutHH(nBOutHH), .noutLL(nBOutLL), .nOut(nBOut), .Clock(and_3_out), .Reset(BReset),
    .Bus15(_16bitregistercounterint_1_bus9[15]), .Bus14(_16bitregistercounterint_1_bus9[14]),
    .Bus13(_16bitregistercounterint_1_bus9[13]), .Bus12(_16bitregistercounterint_1_bus9[12]),
    .Bus11(_16bitregistercounterint_1_bus9[11]), .Bus10(_16bitregistercounterint_1_bus9[10]),
    .Bus9(_16bitregistercounterint_1_bus9[9]), .Bus8(_16bitregistercounterint_1_bus9[8]),
    .Bus7(_16bitregistercounterint_1_bus9[7]), .Bus6(_16bitregistercounterint_1_bus9[6]),
    .Bus5(_16bitregistercounterint_1_bus9[5]), .Bus4(_16bitregistercounterint_1_bus9[4]),
    .Bus3(_16bitregistercounterint_1_bus9[3]), .Bus2(_16bitregistercounterint_1_bus9[2]),
    .Bus1(_16bitregistercounterint_1_bus9[1]), .Bus0(_16bitregistercounterint_1_bus9[0]),
    .SignalOut(_16bitregisterswitchingint_3_signalout));
  Seven_Seg_Hex seven_seg_hex_33 (.d(_16bitdisplayint_8_digit1), .dp(_16bitdisplayint_8_dec1));
  Seven_Seg_Hex seven_seg_hex_34 (.d(_16bitdisplayint_9_digit3), .dp(_16bitdisplayint_9_dec3));
  Seven_Seg_Hex seven_seg_hex_35 (.d(_16bitdisplayint_9_digit2), .dp(_16bitdisplayint_9_dec2));
  Seven_Seg_Hex seven_seg_hex_36 (.d(_16bitdisplayint_9_digit1), .dp(_16bitdisplayint_9_dec1));
  Seven_Seg_Hex seven_seg_hex_37 (.d(_16bitdisplayint_10_digit4), .dp(_16bitdisplayint_10_dec4));
  _16BitDisplayInt _16bitdisplayint_10 (
    .Digit4(_16bitdisplayint_10_digit4), .Dec4(_16bitdisplayint_10_dec4),
    .Digit3(_16bitdisplayint_10_digit3), .Dec3(_16bitdisplayint_10_dec3),
    .Digit2(_16bitdisplayint_10_digit2), .Dec2(_16bitdisplayint_10_dec2),
    .Digit1(_16bitdisplayint_10_digit1), .Dec1(_16bitdisplayint_10_dec1),
    .Input(_16bitregisterint2_3_signalout));
  _16BitRegisterInt2 _16bitregisterint2_3 (
    .RegOut(nIROut), .RegIn(nIRin), .Clock(and_3_out), .Reset(Reset),
    .BusOut15(_16bitregistercounterint_1_bus9[15]), .BusOut14(_16bitregistercounterint_1_bus9[14]),
    .BusOut13(_16bitregistercounterint_1_bus9[13]), .BusOut12(_16bitregistercounterint_1_bus9[12]),
    .BusOut11(_16bitregistercounterint_1_bus9[11]), .BusOut10(_16bitregistercounterint_1_bus9[10]),
    .BusOut9(_16bitregistercounterint_1_bus9[9]), .BusOut8(_16bitregistercounterint_1_bus9[8]),
    .BusOut7(_16bitregistercounterint_1_bus9[7]), .BusOut6(_16bitregistercounterint_1_bus9[6]),
    .BusOut5(_16bitregistercounterint_1_bus9[5]), .BusOut4(_16bitregistercounterint_1_bus9[4]),
    .BusOut3(_16bitregistercounterint_1_bus9[3]), .BusOut2(_16bitregistercounterint_1_bus9[2]),
    .BusOut1(_16bitregistercounterint_1_bus9[1]), .BusOut0(_16bitregistercounterint_1_bus9[0]),
    .SignalOut(_16bitregisterint2_3_signalout));
  Seven_Seg_Hex seven_seg_hex_38 (.d(_16bitdisplayint_10_digit3), .dp(_16bitdisplayint_10_dec3));
  Seven_Seg_Hex seven_seg_hex_39 (.d(_16bitdisplayint_10_digit2), .dp(_16bitdisplayint_10_dec2));
  Seven_Seg_Hex seven_seg_hex_40 (.d(_16bitdisplayint_10_digit1), .dp(_16bitdisplayint_10_dec1));
  LED Carry (.in(_16bitaluint_1_carryout));
  LED Neg (.in(_16bitaluint_1_negout));
  LED led_2 (.in(_16bitaluint_1_neg));
  LED led_3 (.in(_16bitaluint_1_zero));
  LED Zero (.in(_16bitaluint_1_zeroout));
  LED led_4 (.in(_16bitaluint_1_carry));
  not not_3 (not_3_out, and_3_out);
  Seven_Seg_Hex seven_seg_hex_41 (.d(_16bitdisplayint_11_digit4), .dp(_16bitdisplayint_11_dec4));
  _16BitDisplayInt _16bitdisplayint_11 (
    .Digit4(_16bitdisplayint_11_digit4), .Dec4(_16bitdisplayint_11_dec4),
    .Digit3(_16bitdisplayint_11_digit3), .Dec3(_16bitdisplayint_11_dec3),
    .Digit2(_16bitdisplayint_11_digit2), .Dec2(_16bitdisplayint_11_dec2),
    .Digit1(_16bitdisplayint_11_digit1), .Dec1(_16bitdisplayint_11_dec1), .Input(_16bitaluint_1_displayout));
  _16BitALUInt _16bitaluint_1 (
    .BusOut15(_16bitregistercounterint_1_bus9[15]), .BusOut14(_16bitregistercounterint_1_bus9[14]),
    .BusOut13(_16bitregistercounterint_1_bus9[13]), .BusOut12(_16bitregistercounterint_1_bus9[12]),
    .BusOut11(_16bitregistercounterint_1_bus9[11]), .BusOut10(_16bitregistercounterint_1_bus9[10]),
    .BusOut9(_16bitregistercounterint_1_bus9[9]), .BusOut8(_16bitregistercounterint_1_bus9[8]),
    .BusOut7(_16bitregistercounterint_1_bus9[7]), .BusOut6(_16bitregistercounterint_1_bus9[6]),
    .BusOut5(_16bitregistercounterint_1_bus9[5]), .BusOut4(_16bitregistercounterint_1_bus9[4]),
    .BusOut3(_16bitregistercounterint_1_bus9[3]), .BusOut2(_16bitregistercounterint_1_bus9[2]),
    .BusOut1(_16bitregistercounterint_1_bus9[1]), .BusOut0(_16bitregistercounterint_1_bus9[0]),
    .ALUOut(nACLOut), .DisplayOut(_16bitaluint_1_displayout), .ALU0(ALU0), .ALU1(ALU1), .ALU2(ALU2),
    .ALU3(ALU3), .Clear(Reset), .CLK(and_3_out), .FlagiIn(nFLAGin), .zeroOut(_16bitaluint_1_zeroout),
    .negOut(_16bitaluint_1_negout), .carryOut(_16bitaluint_1_carryout), .zero(_16bitaluint_1_zero),
    .neg(_16bitaluint_1_neg), .carry(_16bitaluint_1_carry), .ASignal(_16bitregisterswitchingint_2_signalout),
    .BSignal(_16bitregisterswitchingint_3_signalout));
  _74161 _74161_1 (
    .pin1(1'b0), .pin2(not_3_out), .pin3(1'b0), .pin4(1'b0), .pin5(1'b1), .pin6(1'b1), .pin7(1'b1),
    .pin8(1'b0), .pin9(_74161_1_pin9), .pin10(1'b1), .pin11(_74161_1_pin11), .pin12(_74161_1_pin12),
    .pin13(_74161_1_pin13), .pin14(_74161_1_pin14), .pin16(1'b1));  // open: pin15
  Seven_Seg_Hex seven_seg_hex_42 (.d(_16bitdisplayint_11_digit3), .dp(_16bitdisplayint_11_dec3));
  not not_4 (_74161_1_pin9, Reset);
  Seven_Seg_Hex seven_seg_hex_43 (.d(_16bitdisplayint_11_digit2), .dp(_16bitdisplayint_11_dec2));
  Seven_Seg_Hex seven_seg_hex_44 (.d(_16bitdisplayint_11_digit1), .dp(_16bitdisplayint_11_dec1));
  LED led_5 (.in(_74161_1_pin14));
  LED led_6 (.in(_74161_1_pin13));
  LED led_7 (.in(_74161_1_pin12));
  LED led_8 (.in(_74161_1_pin11));
  // _16BitControlInt _16bitcontrolint_1: pin names not known; wires that end beside it: _74161_1_pin14, _74161_1_pin13, _74161_1_pin12, _74161_1_pin11, 1'b0, 1'b0, 1'b0, 1'b0, 1'b0, 1'b0, 1'b0, 1'b0, 1'b0, 1'b0
  _16BitDisplayInt _16bitdisplayint_12 (
    .Digit4(_16bitdisplayint_12_digit4), .Dec4(_16bitdisplayint_12_dec4),
    .Digit3(_16bitdisplayint_12_digit3), .Dec3(_16bitdisplayint_12_dec3),
    .Digit2(_16bitdisplayint_12_digit2), .Dec2(_16bitdisplayint_12_dec2),
    .Digit1(_16bitdisplayint_12_digit1), .Dec1(_16bitdisplayint_12_dec1),
    .Input(_16bitregistercounterint_3_signalout));
  _16BitRegisterCounterInt _16bitregistercounterint_3 (
    .RegOut(nCOut), .RegIn(nCIn), .Reset(CReset), .Dec(nCDec), .Inc(nCInc),
    .SignalOut(_16bitregistercounterint_3_signalout), .Bus15(_16bitregistercounterint_1_bus9[15]),
    .Bus14(_16bitregistercounterint_1_bus9[14]), .Bus13(_16bitregistercounterint_1_bus9[13]),
    .Bus12(_16bitregistercounterint_1_bus9[12]), .Bus11(_16bitregistercounterint_1_bus9[11]),
    .Bus10(_16bitregistercounterint_1_bus9[10]), .Bus9(_16bitregistercounterint_1_bus9[9]),
    .Bus8(_16bitregistercounterint_1_bus9[8]), .Bus7(_16bitregistercounterint_1_bus9[7]),
    .Bus6(_16bitregistercounterint_1_bus9[6]), .Bus5(_16bitregistercounterint_1_bus9[5]),
    .Bus4(_16bitregistercounterint_1_bus9[4]), .Bus3(_16bitregistercounterint_1_bus9[3]),
    .Bus2(_16bitregistercounterint_1_bus9[2]), .Bus1(_16bitregistercounterint_1_bus9[1]),
    .Bus0(_16bitregistercounterint_1_bus9[0]));
  Seven_Seg_Hex seven_seg_hex_45 (.d(_16bitdisplayint_12_digit4), .dp(_16bitdisplayint_12_dec4));
  Seven_Seg_Hex seven_seg_hex_46 (.d(_16bitdisplayint_12_digit3), .dp(_16bitdisplayint_12_dec3));
  Seven_Seg_Hex seven_seg_hex_47 (.d(_16bitdisplayint_12_digit2), .dp(_16bitdisplayint_12_dec2));
  Seven_Seg_Hex seven_seg_hex_48 (.d(_16bitdisplayint_12_digit1), .dp(_16bitdisplayint_12_dec1));

  // Notes on the sheet:
  //   nPCIn: default 1
  //   nPCOut: default 1
  //   nPCInc: default 1
  //   nPCDec: default 1
  //   nSTACKIn: default 1
  //   nSTACKOut: default 1
  //   nSTACKInc: default 1
  //   nSTACKDec: default 1
  //   nCIn: default 1
  //   nCOut: default 1
  //   nCInc: default 1
  //   nCDec: default 1
  //   nAOut: default 1
  //   nAOutLL: default 1
  //   nAOutHH: default 1
  //   nAOutSwap: default 1
  //   nAIn: default 1
  //   nAInLL: default 1
  //   nAInHH: default 1
  //   nAInLH: default 1
  //   nAInHL: default 1
  //   nBOut: default 1
  //   nBOutLL: default 1
  //   nBOutHH: default 1
  //   nBOutSwap: default 1
  //   nBIn: default 1
  //   nBInLL: default 1
  //   nBInHH: default 1
  //   nBInLH: default 1
  //   nBInHL: default 1
  //   nACLOut: default 1
  //   nDOut: default 1
  //   nDOutLL: default 1
  //   nDOutHH: default 1
  //   nDOutSwap: default 1
  //   nDInLL: default 1
  //   nDInHH: default 1
  //   nXin: default 1
  //   nXOut: default 1
  //   nMARin: default 1
  //   nIRin: default 1
  //   nIROut: default 1
endmodule
