// Digital circuit 16BitALU.dig as structural Verilog
module _16BitALU (
  input  in_1,
  input  in_2,
  input  in_3,
  input  in_4,
  input  in_5,
  input  in_6,
  input  in_7,
  input  in_8,
  input  busOut,
  input  in_10,
  input  in_11,
  input  in_12,
  input  in_13,
  input  in_14,
  input  in_15,
  input  in_16,
  input  in_17,
  input  RegAOut,
  input  RegAIn,
  input  Clock,
  input  Reset,
  input  RegBOut,
  input  RegBIn,
  input  ALU3,
  input  Out,
  input  FlagIn,
  input  ALU2,
  input  ALU1,
  input  ALU0
);

  wire _16bitaluint_1_p15, _16bitaluint_1_p16, _16bitaluint_1_p17, _16bitaluint_1_p18, _16bitaluint_1_p19,
       _16bitaluint_1_p20, _16bitaluint_1_p25, _16bitaluint_1_p27, _16bitaluint_1_p29, _16bitaluint_1_p32,
       _16bitaluint_1_p34, _16bitaluint_1_p36, _16bitaluint_1_p38, _16bitaluint_1_p40, _16bitaluint_1_p42,
       _16bitaluint_1_p44, _16bitaluint_1_p46, _74245_1_pin11, _74245_1_pin12, _74245_1_pin13,
       _74245_1_pin14, _74245_1_pin15, _74245_1_pin16, _74245_1_pin17, _74245_1_pin18, _74245_2_pin11,
       _74245_2_pin12, _74245_2_pin13, _74245_2_pin14, _74245_2_pin15, _74245_2_pin16, _74245_2_pin17,
       _74245_2_pin18, RegA_sig0, RegA_sig1, RegA_sig2, RegA_sig3, RegA_sig4, RegA_sig5, RegA_sig6,
       RegA_sig7, RegA_sig8, RegA_sig9, RegA_sig10, RegA_sig11, RegA_sig12, RegA_sig13, RegA_sig14,
       RegA_sig15, RegB_sig0, RegB_sig1, RegB_sig2, RegB_sig3, RegB_sig4, RegB_sig5, RegB_sig6, RegB_sig7,
       RegB_sig8, RegB_sig9, RegB_sig10, RegB_sig11, RegB_sig12, RegB_sig13, RegB_sig14, RegB_sig15,
       undriven, undriven_2, undriven_3, undriven_4, undriven_5;

  _74245 _74245_1 (
    .pin1(1'b1), .pin2(in_8), .pin3(in_7), .pin4(in_6), .pin5(in_5), .pin6(in_4), .pin7(in_3), .pin8(in_2),
    .pin9(in_1), .pin10(1'b0), .pin11(_74245_1_pin11), .pin12(_74245_1_pin12), .pin13(_74245_1_pin13),
    .pin14(_74245_1_pin14), .pin15(_74245_1_pin15), .pin16(_74245_1_pin16), .pin17(_74245_1_pin17),
    .pin18(_74245_1_pin18), .pin19(busOut), .pin20(1'b1));
  LED Bus14 (.in(_74245_1_pin17));
  LED Bus15 (.in(_74245_1_pin18));
  LED Bus12 (.in(_74245_1_pin15));
  LED Bus13 (.in(_74245_1_pin16));
  LED Bus10 (.in(_74245_1_pin13));
  LED Bus11 (.in(_74245_1_pin14));
  LED Bus8 (.in(_74245_1_pin11));
  LED Bus9 (.in(_74245_1_pin12));
  _74245 _74245_2 (
    .pin1(1'b1), .pin2(in_17), .pin3(in_16), .pin4(in_15), .pin5(in_14), .pin6(in_13), .pin7(in_12),
    .pin8(in_11), .pin9(in_10), .pin10(1'b0), .pin11(_74245_2_pin11), .pin12(_74245_2_pin12),
    .pin13(_74245_2_pin13), .pin14(_74245_2_pin14), .pin15(_74245_2_pin15), .pin16(_74245_2_pin16),
    .pin17(_74245_2_pin17), .pin18(_74245_2_pin18), .pin19(busOut), .pin20(1'b1));
  LED Bus6 (.in(_74245_2_pin17));
  LED Bus7 (.in(_74245_2_pin18));
  LED Bus4 (.in(_74245_2_pin15));
  LED Bus5 (.in(_74245_2_pin16));
  LED Bus2 (.in(_74245_2_pin13));
  LED Bus3 (.in(_74245_2_pin14));
  LED Bus0 (.in(_74245_2_pin11));
  LED Bus1 (.in(_74245_2_pin12));
  _16BitRegisterInt RegB (
    .RegOut(RegBOut), .RegIn(RegBIn), .Clock(Clock), .Reset(Reset), .BusIn0(_74245_2_pin11),
    .BusIn1(_74245_2_pin12), .BusIn2(_74245_2_pin13), .BusIn3(_74245_2_pin14), .BusIn4(_74245_2_pin15),
    .BusIn5(_74245_2_pin16), .BusIn6(_74245_2_pin17), .BusIn7(_74245_2_pin18), .BusIn8(_74245_1_pin11),
    .BusIn9(_74245_1_pin12), .BusIn10(_74245_1_pin13), .BusIn11(_74245_1_pin14), .BusIn12(_74245_1_pin15),
    .BusIn13(_74245_1_pin16), .BusIn14(_74245_1_pin17), .BusIn15(_74245_1_pin18), .Sig15(RegB_sig15),
    .Sig14(RegB_sig14), .Sig13(RegB_sig13), .Sig12(RegB_sig12), .Sig11(RegB_sig11), .Sig10(RegB_sig10),
    .Sig9(RegB_sig9), .Sig8(RegB_sig8), .Sig7(RegB_sig7), .Sig6(RegB_sig6), .Sig5(RegB_sig5),
    .Sig4(RegB_sig4), .Sig3(RegB_sig3), .Sig2(RegB_sig2), .Sig1(RegB_sig1), .Sig0(RegB_sig0),
    .BusOut15(_74245_1_pin18), .BusOut14(_74245_1_pin17), .BusOut13(_74245_1_pin16),
    .BusOut12(_74245_1_pin15), .BusOut11(_74245_1_pin14), .BusOut10(_74245_1_pin13),
    .BusOut9(_74245_1_pin12), .BusOut8(_74245_1_pin11), .BusOut7(_74245_2_pin18), .BusOut6(_74245_2_pin17),
    .BusOut5(_74245_2_pin16), .BusOut4(_74245_2_pin15), .BusOut3(_74245_2_pin14), .BusOut2(_74245_2_pin13),
    .BusOut1(_74245_2_pin12), .BusOut0(_74245_2_pin11));
  _16BitRegisterInt RegA (
    .RegOut(RegAOut), .RegIn(RegAIn), .Clock(Clock), .Reset(Reset), .BusIn0(_74245_2_pin11),
    .BusIn1(_74245_2_pin12), .BusIn2(_74245_2_pin13), .BusIn3(_74245_2_pin14), .BusIn4(_74245_2_pin15),
    .BusIn5(_74245_2_pin16), .BusIn6(_74245_2_pin17), .BusIn7(_74245_2_pin18), .BusIn8(_74245_1_pin11),
    .BusIn9(_74245_1_pin12), .BusIn10(_74245_1_pin13), .BusIn11(_74245_1_pin14), .BusIn12(_74245_1_pin15),
    .BusIn13(_74245_1_pin16), .BusIn14(_74245_1_pin17), .BusIn15(_74245_1_pin18), .Sig15(RegA_sig15),
    .Sig14(RegA_sig14), .Sig13(RegA_sig13), .Sig12(RegA_sig12), .Sig11(RegA_sig11), .Sig10(RegA_sig10),
    .Sig9(RegA_sig9), .Sig8(RegA_sig8), .Sig7(RegA_sig7), .Sig6(RegA_sig6), .Sig5(RegA_sig5),
    .Sig4(RegA_sig4), .Sig3(RegA_sig3), .Sig2(RegA_sig2), .Sig1(RegA_sig1), .Sig0(RegA_sig0),
    .BusOut15(_74245_1_pin18), .BusOut14(_74245_1_pin17), .BusOut13(_74245_1_pin16),
    .BusOut12(_74245_1_pin15), .BusOut11(_74245_1_pin14), .BusOut10(_74245_1_pin13),
    .BusOut9(_74245_1_pin12), .BusOut8(_74245_1_pin11), .BusOut7(_74245_2_pin18), .BusOut6(_74245_2_pin17),
    .BusOut5(_74245_2_pin16), .BusOut4(_74245_2_pin15), .BusOut3(_74245_2_pin14), .BusOut2(_74245_2_pin13),
    .BusOut1(_74245_2_pin12), .BusOut0(_74245_2_pin11));
  LED RegB15 (.in(RegB_sig15));
  LED RegB14 (.in(RegB_sig14));
  LED RegB13 (.in(RegB_sig13));
  LED RegB12 (.in(RegB_sig12));
  LED RegB11 (.in(RegB_sig11));
  LED RegB10 (.in(RegB_sig10));
  LED RegB9 (.in(RegB_sig9));
  LED RegB8 (.in(RegB_sig8));
  LED RegB7 (.in(RegB_sig7));
  LED RegB6 (.in(RegB_sig6));
  LED RegB5 (.in(RegB_sig5));
  LED RegB4 (.in(RegB_sig4));
  LED RegB3 (.in(RegB_sig3));
  LED RegB2 (.in(RegB_sig2));
  LED RegB1 (.in(RegB_sig1));
  LED RegB0 (.in(RegB_sig0));
  LED RegA15 (.in(RegA_sig15));
  LED RegA14 (.in(RegA_sig14));
  LED RegA13 (.in(RegA_sig13));
  LED RegA12 (.in(RegA_sig12));
  LED RegA11 (.in(RegA_sig11));
  LED RegA10 (.in(RegA_sig10));
  LED RegA9 (.in(RegA_sig9));
  LED RegA8 (.in(RegA_sig8));
  LED RegA7 (.in(RegA_sig7));
  LED RegA6 (.in(RegA_sig6));
  LED RegA5 (.in(RegA_sig5));
  LED RegA4 (.in(RegA_sig4));
  LED RegA3 (.in(RegA_sig3));
  LED RegA2 (.in(RegA_sig2));
  LED RegA1 (.in(RegA_sig1));
  LED RegA0 (.in(RegA_sig0));
  LED led_1 (.in(_16bitaluint_1_p15));
  LED led_2 (.in(_16bitaluint_1_p16));
  LED led_3 (.in(_16bitaluint_1_p17));
  LED led_4 (.in(_16bitaluint_1_p18));
  LED led_5 (.in(_16bitaluint_1_p19));
  LED led_6 (.in(_16bitaluint_1_p20));
  // _16BitALUInt _16bitaluint_1: pin names not known; wires that end beside it: RegA_sig2, RegA_sig3, RegA_sig4, RegA_sig5, RegA_sig6, RegA_sig7, RegA_sig8, RegA_sig9, RegA_sig10, RegA_sig11, RegA_sig12, RegA_sig13, RegA_sig14, RegA_sig15, _16bitaluint_1_p15, _16bitaluint_1_p16, _16bitaluint_1_p17, _16bitaluint_1_p18, _16bitaluint_1_p19, _16bitaluint_1_p20, FlagIn, Clock, Reset, _74245_2_pin14, _16bitaluint_1_p25, _74245_2_pin15, _16bitaluint_1_p27, _74245_2_pin16, _16bitaluint_1_p29, _74245_2_pin17, _74245_2_pin18, _16bitaluint_1_p32, _74245_1_pin11, _16bitaluint_1_p34, _74245_1_pin12, _16bitaluint_1_p36, _74245_1_pin13, _16bitaluint_1_p38, _74245_1_pin14, _16bitaluint_1_p40, _74245_1_pin15, _16bitaluint_1_p42, _74245_1_pin16, _16bitaluint_1_p44, _74245_1_pin17, _16bitaluint_1_p46, _74245_1_pin18
  LED Signal0 (.in(undriven));
  LED Signal1 (.in(undriven_2));
  LED Signal2 (.in(undriven_3));
  LED Signal3 (.in(undriven_4));
  LED Signal4 (.in(undriven_5));
  LED Signal5 (.in(_16bitaluint_1_p25));
  LED Signal6 (.in(_16bitaluint_1_p27));
  LED Signal7 (.in(_16bitaluint_1_p29));
  LED Signal8 (.in(_16bitaluint_1_p32));
  LED Signal9 (.in(_16bitaluint_1_p34));
  LED Signal10 (.in(_16bitaluint_1_p36));
  LED Signal11 (.in(_16bitaluint_1_p38));
  LED Signal12 (.in(_16bitaluint_1_p40));
  LED Signal13 (.in(_16bitaluint_1_p42));
  LED Signal14 (.in(_16bitaluint_1_p44));
  LED Signal15 (.in(_16bitaluint_1_p46));

  // Notes on the sheet:
  //   busOut: default 1
  //   RegAOut: default 1
  //   RegAIn: default 1
  //   RegBOut: default 1
  //   RegBIn: default 1
  //   Out: default 1
  //   FlagIn: default 1
endmodule
