// Digital circuit 16BitALUAdder.dig as structural Verilog
module _16BitALUAdder (
  input  And,
  input  BusAIn8,
  input  BusAIn9,
  input  BusAIn10,
  input  BusAIn7,
  input  BusAIn6,
  input  BusAIn5,
  input  BusAIn4,
  input  BusAIn11,
  input  BusAIn12,
  input  BusAIn3,
  input  BusAIn2,
  input  BusAIn1,
  input  BusAIn13,
  input  BusAIn14,
  input  BusAIn15,
  input  BusAIn0,
  input  BusBIn8,
  input  BusBIn9,
  input  BusBIn10,
  input  BusBIn7,
  input  BusBIn6,
  input  BusBIn5,
  input  BusBIn4,
  input  BusBIn11,
  input  BusBIn12,
  input  BusBIn3,
  input  BusBIn2,
  input  BusBIn1,
  input  BusBIn13,
  input  BusBIn14,
  input  BusBIn15,
  input  BusBIn0,
  input  sub,
  output BusOut0,
  output BusOut1,
  output BusOut2,
  output BusOut3,
  output BusOut4,
  output BusOut5,
  output BusOut6,
  output BusOut7,
  output BusOut8,
  output BusOut9,
  output BusOut10,
  output BusOut11,
  output BusOut12,
  output BusOut13,
  output BusOut14,
  output BusOut15,
  output carry,
  output Zero
);

  wire _74283_1_pin1, _74283_1_pin2, _74283_1_pin4, _74283_1_pin6, _74283_1_pin7, _74283_1_pin10,
       _74283_1_pin11, _74283_1_pin13, _74283_1_pin15, _74283_2_pin1, _74283_2_pin2, _74283_2_pin4,
       _74283_2_pin6, _74283_2_pin7, _74283_2_pin10, _74283_2_pin11, _74283_2_pin13, _74283_2_pin15,
       _74283_3_pin1, _74283_3_pin2, _74283_3_pin4, _74283_3_pin6, _74283_3_pin7, _74283_3_pin10,
       _74283_3_pin11, _74283_3_pin13, _74283_3_pin15, _74283_4_pin1, _74283_4_pin2, _74283_4_pin4,
       _74283_4_pin6, _74283_4_pin7, _74283_4_pin10, _74283_4_pin11, _74283_4_pin13, _74283_4_pin15,
       and_2_out, and_3_out, and_4_out, and_5_out, and_6_out, and_7_out, and_8_out, nor_1_out, nor_2_out,
       nor_3_out, nor_4_out, nor_5_out, nor_6_out, nor_7_out, nor_8_out;

  and and_1 (Zero, and_3_out, and_2_out);
  and and_2 (and_2_out, and_5_out, and_4_out);
  and and_3 (and_3_out, and_7_out, and_6_out);
  and and_4 (and_4_out, nor_2_out, nor_1_out);
  and and_5 (and_5_out, nor_4_out, nor_3_out);
  and and_6 (and_6_out, nor_6_out, nor_5_out);
  and and_7 (and_7_out, nor_8_out, nor_7_out);
  nor nor_1 (nor_1_out, BusOut14, BusOut15);
  nor nor_2 (nor_2_out, BusOut12, BusOut13);
  nor nor_3 (nor_3_out, BusOut10, BusOut11);
  nor nor_4 (nor_4_out, BusOut8, BusOut9);
  nor nor_5 (nor_5_out, BusOut6, BusOut7);
  nor nor_6 (nor_6_out, BusOut4, BusOut5);
  nor nor_7 (nor_7_out, BusOut2, BusOut3);
  nor nor_8 (nor_8_out, BusOut0, BusOut1);
  _16BitBusOut _16bitbusout_1 (
    .RegOut(and_8_out), .BusOut15(BusOut15), .BusOut14(BusOut14), .BusOut13(BusOut13), .BusOut12(BusOut12),
    .BusOut11(BusOut11), .BusOut10(BusOut10), .BusOut9(BusOut9), .BusOut8(BusOut8), .BusOut7(BusOut7),
    .BusOut6(BusOut6), .BusOut5(BusOut5), .BusOut4(BusOut4), .BusOut3(BusOut3), .BusOut2(BusOut2),
    .BusOut1(BusOut1), .BusOut0(BusOut0), .BusIn15(_74283_1_pin10), .BusIn14(_74283_1_pin13),
    .BusIn13(_74283_1_pin1), .BusIn12(_74283_1_pin4), .BusIn11(_74283_2_pin10), .BusIn10(_74283_2_pin13),
    .BusIn9(_74283_2_pin1), .BusIn8(_74283_2_pin4), .BusIn7(_74283_3_pin10), .BusIn6(_74283_3_pin13),
    .BusIn5(_74283_3_pin1), .BusIn4(_74283_3_pin4), .BusIn3(_74283_4_pin10), .BusIn2(_74283_4_pin13),
    .BusIn1(_74283_4_pin1), .BusIn0(_74283_4_pin4));
  and and_8 (and_8_out, And, sub);
  _74283 _74283_1 (
    .pin1(_74283_1_pin1), .pin2(_74283_1_pin2), .pin3(BusAIn13), .pin4(_74283_1_pin4), .pin5(BusAIn12),
    .pin6(_74283_1_pin6), .pin7(_74283_1_pin7), .pin8(1'b0), .pin9(carry), .pin10(_74283_1_pin10),
    .pin11(_74283_1_pin11), .pin12(BusAIn15), .pin13(_74283_1_pin13), .pin14(BusAIn14),
    .pin15(_74283_1_pin15), .pin16(1'b1));
  _74283 _74283_2 (
    .pin1(_74283_2_pin1), .pin2(_74283_2_pin2), .pin3(BusAIn9), .pin4(_74283_2_pin4), .pin5(BusAIn8),
    .pin6(_74283_2_pin6), .pin7(_74283_2_pin7), .pin8(1'b0), .pin9(_74283_1_pin7), .pin10(_74283_2_pin10),
    .pin11(_74283_2_pin11), .pin12(BusAIn11), .pin13(_74283_2_pin13), .pin14(BusAIn10),
    .pin15(_74283_2_pin15), .pin16(1'b1));
  _74283 _74283_3 (
    .pin1(_74283_3_pin1), .pin2(_74283_3_pin2), .pin3(BusAIn5), .pin4(_74283_3_pin4), .pin5(BusAIn4),
    .pin6(_74283_3_pin6), .pin7(_74283_3_pin7), .pin8(1'b0), .pin9(_74283_2_pin7), .pin10(_74283_3_pin10),
    .pin11(_74283_3_pin11), .pin12(BusAIn7), .pin13(_74283_3_pin13), .pin14(BusAIn6), .pin15(_74283_3_pin15),
    .pin16(1'b1));
  _74283 _74283_4 (
    .pin1(_74283_4_pin1), .pin2(_74283_4_pin2), .pin3(BusAIn1), .pin4(_74283_4_pin4), .pin5(BusAIn0),
    .pin6(_74283_4_pin6), .pin7(_74283_4_pin7), .pin8(1'b0), .pin9(_74283_3_pin7), .pin10(_74283_4_pin10),
    .pin11(_74283_4_pin11), .pin12(BusAIn3), .pin13(_74283_4_pin13), .pin14(BusAIn2), .pin15(_74283_4_pin15),
    .pin16(1'b1));
  xor xor_1 (_74283_1_pin11, _74283_4_pin7, BusBIn15);
  xor xor_2 (_74283_1_pin15, _74283_4_pin7, BusBIn14);
  xor xor_3 (_74283_1_pin2, _74283_4_pin7, BusBIn13);
  xor xor_4 (_74283_1_pin6, _74283_4_pin7, BusBIn12);
  xor xor_5 (_74283_2_pin11, _74283_4_pin7, BusBIn11);
  xor xor_6 (_74283_2_pin15, _74283_4_pin7, BusBIn10);
  xor xor_7 (_74283_2_pin2, _74283_4_pin7, BusBIn9);
  xor xor_8 (_74283_2_pin6, _74283_4_pin7, BusBIn8);
  xor xor_9 (_74283_3_pin11, _74283_4_pin7, BusBIn7);
  xor xor_10 (_74283_3_pin15, _74283_4_pin7, BusBIn6);
  xor xor_11 (_74283_3_pin2, _74283_4_pin7, BusBIn5);
  xor xor_12 (_74283_3_pin6, _74283_4_pin7, BusBIn4);
  xor xor_13 (_74283_4_pin11, _74283_4_pin7, BusBIn3);
  xor xor_14 (_74283_4_pin15, _74283_4_pin7, BusBIn2);
  xor xor_15 (_74283_4_pin2, _74283_4_pin7, BusBIn1);
  xor xor_16 (_74283_4_pin6, _74283_4_pin7, BusBIn0);
  not not_1 (_74283_4_pin7, sub);

  // Notes on the sheet:
  //   And: default 1
  //   sub: default 1
endmodule
