// Digital circuit 16BitALUAnd.dig as structural Verilog
module _16BitALUAnd (
  input  And,
  input  BusAIn8,
  input  BusAIn9,
  input  BusAIn10,
  input  BusAIn7,
  input  BusAIn6,
  input  BusAIn5,
  input  BusAIn4,
  input  BusAIn11,
  input  BusAIn12,
  input  BusAIn3,
  input  BusAIn2,
  input  BusAIn1,
  input  BusAIn13,
  input  BusAIn14,
  input  BusAIn15,
  input  BusAIn0,
  input  BusBIn8,
  input  BusBIn9,
  input  BusBIn10,
  input  BusBIn7,
  input  BusBIn6,
  input  BusBIn5,
  input  BusBIn4,
  input  BusBIn11,
  input  BusBIn12,
  input  BusBIn3,
  input  BusBIn2,
  input  BusBIn1,
  input  BusBIn13,
  input  BusBIn14,
  input  BusBIn15,
  input  BusBIn0,
  output BusOut0,
  output BusOut1,
  output BusOut2,
  output BusOut3,
  output BusOut4,
  output BusOut5,
  output BusOut6,
  output BusOut7,
  output BusOut8,
  output BusOut9,
  output BusOut10,
  output BusOut11,
  output BusOut12,
  output BusOut13,
  output BusOut14,
  output BusOut15
);

  wire and_1_out, and_2_out, and_3_out, and_4_out, and_5_out, and_6_out, and_7_out, and_8_out, and_9_out,
       and_10_out, and_11_out, and_12_out, and_13_out, and_14_out, and_15_out, and_16_out;

  _16BitBusOut _16bitbusout_1 (
    .RegOut(And), .BusOut15(BusOut15), .BusOut14(BusOut14), .BusOut13(BusOut13), .BusOut12(BusOut12),
    .BusOut11(BusOut11), .BusOut10(BusOut10), .BusOut9(BusOut9), .BusOut8(BusOut8), .BusOut7(BusOut7),
    .BusOut6(BusOut6), .BusOut5(BusOut5), .BusOut4(BusOut4), .BusOut3(BusOut3), .BusOut2(BusOut2),
    .BusOut1(BusOut1), .BusOut0(BusOut0), .BusIn15(and_1_out), .BusIn14(and_2_out), .BusIn13(and_3_out),
    .BusIn12(and_4_out), .BusIn11(and_5_out), .BusIn10(and_6_out), .BusIn9(and_7_out), .BusIn8(and_8_out),
    .BusIn7(and_9_out), .BusIn6(and_10_out), .BusIn5(and_11_out), .BusIn4(and_12_out), .BusIn3(and_13_out),
    .BusIn2(and_14_out), .BusIn1(and_15_out), .BusIn0(and_16_out));
  and and_1 (and_1_out, BusAIn15, BusBIn15);
  and and_2 (and_2_out, BusAIn14, BusBIn14);
  and and_3 (and_3_out, BusAIn13, BusBIn13);
  and and_4 (and_4_out, BusAIn12, BusBIn12);
  and and_5 (and_5_out, BusAIn11, BusBIn11);
  and and_6 (and_6_out, BusAIn10, BusBIn10);
  and and_7 (and_7_out, BusAIn9, BusBIn9);
  and and_8 (and_8_out, BusAIn8, BusBIn8);
  and and_9 (and_9_out, BusAIn7, BusBIn7);
  and and_10 (and_10_out, BusAIn6, BusBIn6);
  and and_11 (and_11_out, BusAIn5, BusBIn5);
  and and_12 (and_12_out, BusAIn4, BusBIn4);
  and and_13 (and_13_out, BusAIn3, BusBIn3);
  and and_14 (and_14_out, BusAIn2, BusBIn2);
  and and_15 (and_15_out, BusAIn1, BusBIn1);
  and and_16 (and_16_out, BusAIn0, BusBIn0);

  // Notes on the sheet:
  //   And: default 1
endmodule
