// Digital circuit 16BitALUInt.dig as structural Verilog
module _16BitALUInt (
  input  ALUOut,
  input  FlagiIn,
  input  CLK,
  input  Clear,
  input  ALU3,
  input  ALU2,
  input  ALU1,
  input  ALU0,
  output BusOut0,
  output BusOut1,
  output BusOut2,
  output BusOut3,
  output BusOut4,
  output BusOut5,
  output BusOut6,
  output BusOut7,
  output BusOut8,
  output BusOut9,
  output BusOut10,
  output BusOut11,
  output BusOut12,
  output BusOut13,
  output BusOut14,
  output BusOut15,
  output zeroOut,
  output carryOut,
  output negOut,
  output zero,
  output neg,
  output carry,
  output [15:0] BSignal,
  output [15:0] ASignal,
  output [15:0] DisplayOut
);

  wire _16bitaluadder_1_carry, _16bitalushl_1_shlcarry, _16bitalushr_1_shrcarry, _74138_1_pin10,
       _74138_1_pin11, _74138_1_pin12, _74138_1_pin13, _74138_1_pin14, _74138_1_pin15, _74138_2_pin4,
       _74138_2_pin7, _74138_2_pin9, _74138_2_pin10, _74138_2_pin11, and_2_out, and_3_out, and_4_out,
       not_1_out, or_1_out, or_2_out;

  _74173 _74173_1 (
    .pin1(1'b0), .pin2(1'b0), .pin3(zeroOut), .pin4(negOut), .pin5(carryOut), .pin7(CLK), .pin8(1'b0),
    .pin9(FlagiIn), .pin10(FlagiIn), .pin11(1'b0), .pin12(carry), .pin13(DisplayOut[15]), .pin14(zero),
    .pin15(Clear), .pin16(1'b1));  // open: pin6
  _16BitBusOut _16bitbusout_1 (
    .RegOut(ALUOut), .BusOut15(BusOut15), .BusOut14(BusOut14), .BusOut13(BusOut13), .BusOut12(BusOut12),
    .BusOut11(BusOut11), .BusOut10(BusOut10), .BusOut9(BusOut9), .BusOut8(BusOut8), .BusOut7(BusOut7),
    .BusOut6(BusOut6), .BusOut5(BusOut5), .BusOut4(BusOut4), .BusOut3(BusOut3), .BusOut2(BusOut2),
    .BusOut1(BusOut1), .BusOut0(BusOut0), .BusIn15(DisplayOut[15]), .BusIn14(DisplayOut[14]),
    .BusIn13(DisplayOut[13]), .BusIn12(DisplayOut[12]), .BusIn11(DisplayOut[11]), .BusIn10(DisplayOut[10]),
    .BusIn9(DisplayOut[9]), .BusIn8(DisplayOut[8]), .BusIn7(DisplayOut[7]), .BusIn6(DisplayOut[6]),
    .BusIn5(DisplayOut[5]), .BusIn4(DisplayOut[4]), .BusIn3(DisplayOut[3]), .BusIn2(DisplayOut[2]),
    .BusIn1(DisplayOut[1]), .BusIn0(DisplayOut[0]));
  and and_1 (carry, not_1_out, or_2_out);
  or or_1 (or_1_out, _16bitalushl_1_shlcarry, _16bitalushr_1_shrcarry);
  or or_2 (or_2_out, or_1_out, _16bitaluadder_1_carry);
  not not_1 (not_1_out, and_2_out);
  _16BitALUSHR _16bitalushr_1 (
    .SHR(_74138_1_pin12), .BusOut15(DisplayOut[15]), .BusOut14(DisplayOut[14]), .BusOut13(DisplayOut[13]),
    .BusOut12(DisplayOut[12]), .BusOut11(DisplayOut[11]), .BusOut10(DisplayOut[10]), .BusOut9(DisplayOut[9]),
    .BusOut8(DisplayOut[8]), .BusOut7(DisplayOut[7]), .BusOut6(DisplayOut[6]), .BusOut5(DisplayOut[5]),
    .BusOut4(DisplayOut[4]), .BusOut3(DisplayOut[3]), .BusOut2(DisplayOut[2]), .BusOut1(DisplayOut[1]),
    .BusOut0(DisplayOut[0]), .BusIn15(ASignal[15]), .BusIn14(ASignal[14]), .BusIn13(ASignal[13]),
    .BusIn12(ASignal[12]), .BusIn11(ASignal[11]), .BusIn10(ASignal[10]), .BusIn9(ASignal[9]),
    .BusIn8(ASignal[8]), .BusIn7(ASignal[7]), .BusIn6(ASignal[6]), .BusIn5(ASignal[5]), .BusIn4(ASignal[4]),
    .BusIn3(ASignal[3]), .BusIn2(ASignal[2]), .BusIn1(ASignal[1]), .BusIn0(ASignal[0]),
    .SHRCarry(_16bitalushr_1_shrcarry));
  _16BitALUSHL _16bitalushl_1 (
    .SHL(_74138_1_pin13), .BusOut15(DisplayOut[15]), .BusOut14(DisplayOut[14]), .BusOut13(DisplayOut[13]),
    .BusOut12(DisplayOut[12]), .BusOut11(DisplayOut[11]), .BusOut10(DisplayOut[10]), .BusOut9(DisplayOut[9]),
    .BusOut8(DisplayOut[8]), .BusOut7(DisplayOut[7]), .BusOut6(DisplayOut[6]), .BusOut5(DisplayOut[5]),
    .BusOut4(DisplayOut[4]), .BusOut3(DisplayOut[3]), .BusOut2(DisplayOut[2]), .BusOut1(DisplayOut[1]),
    .BusOut0(DisplayOut[0]), .BusIn15(ASignal[15]), .BusIn14(ASignal[14]), .BusIn13(ASignal[13]),
    .BusIn12(ASignal[12]), .BusIn11(ASignal[11]), .BusIn10(ASignal[10]), .BusIn9(ASignal[9]),
    .BusIn8(ASignal[8]), .BusIn7(ASignal[7]), .BusIn6(ASignal[6]), .BusIn5(ASignal[5]), .BusIn4(ASignal[4]),
    .BusIn3(ASignal[3]), .BusIn2(ASignal[2]), .BusIn1(ASignal[1]), .BusIn0(ASignal[0]),
    .SHLCarry(_16bitalushl_1_shlcarry));
  _16BitALUROR _16bitaluror_1 (
    .ROL(_74138_1_pin10), .BusOut15(DisplayOut[15]), .BusOut14(DisplayOut[14]), .BusOut13(DisplayOut[13]),
    .BusOut12(DisplayOut[12]), .BusOut11(DisplayOut[11]), .BusOut10(DisplayOut[10]), .BusOut9(DisplayOut[9]),
    .BusOut8(DisplayOut[8]), .BusOut7(DisplayOut[7]), .BusOut6(DisplayOut[6]), .BusOut5(DisplayOut[5]),
    .BusOut4(DisplayOut[4]), .BusOut3(DisplayOut[3]), .BusOut2(DisplayOut[2]), .BusOut1(DisplayOut[1]),
    .BusOut0(DisplayOut[0]), .BusIn15(ASignal[15]), .BusIn14(ASignal[14]), .BusIn13(ASignal[13]),
    .BusIn12(ASignal[12]), .BusIn11(ASignal[11]), .BusIn10(ASignal[10]), .BusIn9(ASignal[9]),
    .BusIn8(ASignal[8]), .BusIn7(ASignal[7]), .BusIn6(ASignal[6]), .BusIn5(ASignal[5]), .BusIn4(ASignal[4]),
    .BusIn3(ASignal[3]), .BusIn2(ASignal[2]), .BusIn1(ASignal[1]), .BusIn0(ASignal[0]));
  _16BitALUROL _16bitalurol_1 (
    .ROL(_74138_1_pin11), .BusOut15(DisplayOut[15]), .BusOut14(DisplayOut[14]), .BusOut13(DisplayOut[13]),
    .BusOut12(DisplayOut[12]), .BusOut11(DisplayOut[11]), .BusOut10(DisplayOut[10]), .BusOut9(DisplayOut[9]),
    .BusOut8(DisplayOut[8]), .BusOut7(DisplayOut[7]), .BusOut6(DisplayOut[6]), .BusOut5(DisplayOut[5]),
    .BusOut4(DisplayOut[4]), .BusOut3(DisplayOut[3]), .BusOut2(DisplayOut[2]), .BusOut1(DisplayOut[1]),
    .BusOut0(DisplayOut[0]), .BusIn15(ASignal[15]), .BusIn14(ASignal[14]), .BusIn13(ASignal[13]),
    .BusIn12(ASignal[12]), .BusIn11(ASignal[11]), .BusIn10(ASignal[10]), .BusIn9(ASignal[9]),
    .BusIn8(ASignal[8]), .BusIn7(ASignal[7]), .BusIn6(ASignal[6]), .BusIn5(ASignal[5]), .BusIn4(ASignal[4]),
    .BusIn3(ASignal[3]), .BusIn2(ASignal[2]), .BusIn1(ASignal[1]), .BusIn0(ASignal[0]));
  _16BitALUNot _16bitalunot_1 (
    .Not(_74138_2_pin11), .BusOut15(DisplayOut[15]), .BusOut14(DisplayOut[14]), .BusOut13(DisplayOut[13]),
    .BusOut12(DisplayOut[12]), .BusOut11(DisplayOut[11]), .BusOut10(DisplayOut[10]), .BusOut9(DisplayOut[9]),
    .BusOut8(DisplayOut[8]), .BusOut7(DisplayOut[7]), .BusOut6(DisplayOut[6]), .BusOut5(DisplayOut[5]),
    .BusOut4(DisplayOut[4]), .BusOut3(DisplayOut[3]), .BusOut2(DisplayOut[2]), .BusOut1(DisplayOut[1]),
    .BusOut0(DisplayOut[0]), .BusIn15(ASignal[15]), .BusIn14(ASignal[14]), .BusIn13(ASignal[13]),
    .BusIn12(ASignal[12]), .BusIn11(ASignal[11]), .BusIn10(ASignal[10]), .BusIn9(ASignal[9]),
    .BusIn8(ASignal[8]), .BusIn7(ASignal[7]), .BusIn6(ASignal[6]), .BusIn5(ASignal[5]), .BusIn4(ASignal[4]),
    .BusIn3(ASignal[3]), .BusIn2(ASignal[2]), .BusIn1(ASignal[1]), .BusIn0(ASignal[0]));
  _16BitALUAnd _16bitaluand_1 (
    .And(_74138_2_pin10), .BusOut15(DisplayOut[15]), .BusOut14(DisplayOut[14]), .BusOut13(DisplayOut[13]),
    .BusOut12(DisplayOut[12]), .BusOut11(DisplayOut[11]), .BusOut10(DisplayOut[10]), .BusOut9(DisplayOut[9]),
    .BusOut8(DisplayOut[8]), .BusOut7(DisplayOut[7]), .BusOut6(DisplayOut[6]), .BusOut5(DisplayOut[5]),
    .BusOut4(DisplayOut[4]), .BusOut3(DisplayOut[3]), .BusOut2(DisplayOut[2]), .BusOut1(DisplayOut[1]),
    .BusOut0(DisplayOut[0]), .BusBIn15(BSignal[15]), .BusAIn15(ASignal[15]), .BusBIn14(BSignal[14]),
    .BusAIn14(ASignal[14]), .BusBIn13(BSignal[13]), .BusAIn13(ASignal[13]), .BusBIn12(BSignal[12]),
    .BusAIn12(ASignal[12]), .BusBIn11(BSignal[11]), .BusAIn11(ASignal[11]), .BusBIn10(BSignal[10]),
    .BusAIn10(ASignal[10]), .BusBIn9(BSignal[9]), .BusAIn9(ASignal[9]), .BusBIn8(BSignal[8]),
    .BusAIn8(ASignal[8]), .BusBIn7(BSignal[7]), .BusAIn7(ASignal[7]), .BusBIn6(BSignal[6]),
    .BusAIn6(ASignal[6]), .BusBIn5(BSignal[5]), .BusAIn5(ASignal[5]), .BusBIn4(BSignal[4]),
    .BusAIn4(ASignal[4]), .BusBIn3(BSignal[3]), .BusAIn3(ASignal[3]), .BusBIn2(BSignal[2]),
    .BusAIn2(ASignal[2]), .BusBIn1(BSignal[1]), .BusAIn1(ASignal[1]), .BusBIn0(BSignal[0]),
    .BusAIn0(ASignal[0]));
  _16BitALUOr _16bitaluor_1 (
    .Or(_74138_2_pin9), .BusOut15(DisplayOut[15]), .BusOut14(DisplayOut[14]), .BusOut13(DisplayOut[13]),
    .BusOut12(DisplayOut[12]), .BusOut11(DisplayOut[11]), .BusOut10(DisplayOut[10]), .BusOut9(DisplayOut[9]),
    .BusOut8(DisplayOut[8]), .BusOut7(DisplayOut[7]), .BusOut6(DisplayOut[6]), .BusOut5(DisplayOut[5]),
    .BusOut4(DisplayOut[4]), .BusOut3(DisplayOut[3]), .BusOut2(DisplayOut[2]), .BusOut1(DisplayOut[1]),
    .BusOut0(DisplayOut[0]), .BusBIn15(BSignal[15]), .BusAIn15(ASignal[15]), .BusBIn14(BSignal[14]),
    .BusAIn14(ASignal[14]), .BusBIn13(BSignal[13]), .BusAIn13(ASignal[13]), .BusBIn12(BSignal[12]),
    .BusAIn12(ASignal[12]), .BusBIn11(BSignal[11]), .BusAIn11(ASignal[11]), .BusBIn10(BSignal[10]),
    .BusAIn10(ASignal[10]), .BusBIn9(BSignal[9]), .BusAIn9(ASignal[9]), .BusBIn8(BSignal[8]),
    .BusAIn8(ASignal[8]), .BusBIn7(BSignal[7]), .BusAIn7(ASignal[7]), .BusBIn6(BSignal[6]),
    .BusAIn6(ASignal[6]), .BusBIn5(BSignal[5]), .BusAIn5(ASignal[5]), .BusBIn4(BSignal[4]),
    .BusAIn4(ASignal[4]), .BusBIn3(BSignal[3]), .BusAIn3(ASignal[3]), .BusBIn2(BSignal[2]),
    .BusAIn2(ASignal[2]), .BusBIn1(BSignal[1]), .BusAIn1(ASignal[1]), .BusBIn0(BSignal[0]),
    .BusAIn0(ASignal[0]));
  _16BitALUXor _16bitaluxor_1 (
    .Xor(_74138_2_pin7), .BusOut15(DisplayOut[15]), .BusOut14(DisplayOut[14]), .BusOut13(DisplayOut[13]),
    .BusOut12(DisplayOut[12]), .BusOut11(DisplayOut[11]), .BusOut10(DisplayOut[10]), .BusOut9(DisplayOut[9]),
    .BusOut8(DisplayOut[8]), .BusOut7(DisplayOut[7]), .BusOut6(DisplayOut[6]), .BusOut5(DisplayOut[5]),
    .BusOut4(DisplayOut[4]), .BusOut3(DisplayOut[3]), .BusOut2(DisplayOut[2]), .BusOut1(DisplayOut[1]),
    .BusOut0(DisplayOut[0]), .BusBIn15(BSignal[15]), .BusAIn15(ASignal[15]), .BusBIn14(BSignal[14]),
    .BusAIn14(ASignal[14]), .BusBIn13(BSignal[13]), .BusAIn13(ASignal[13]), .BusBIn12(BSignal[12]),
    .BusAIn12(ASignal[12]), .BusBIn11(BSignal[11]), .BusAIn11(ASignal[11]), .BusBIn10(BSignal[10]),
    .BusAIn10(ASignal[10]), .BusBIn9(BSignal[9]), .BusAIn9(ASignal[9]), .BusBIn8(BSignal[8]),
    .BusAIn8(ASignal[8]), .BusBIn7(BSignal[7]), .BusAIn7(ASignal[7]), .BusBIn6(BSignal[6]),
    .BusAIn6(ASignal[6]), .BusBIn5(BSignal[5]), .BusAIn5(ASignal[5]), .BusBIn4(BSignal[4]),
    .BusAIn4(ASignal[4]), .BusBIn3(BSignal[3]), .BusAIn3(ASignal[3]), .BusBIn2(BSignal[2]),
    .BusAIn2(ASignal[2]), .BusBIn1(BSignal[1]), .BusAIn1(ASignal[1]), .BusBIn0(BSignal[0]),
    .BusAIn0(ASignal[0]));
  _16BitALUAdder _16bitaluadder_1 (
    .And(_74138_1_pin15), .sub(_74138_1_pin14), .BusOut15(DisplayOut[15]), .BusOut14(DisplayOut[14]),
    .BusOut13(DisplayOut[13]), .BusOut12(DisplayOut[12]), .BusOut11(DisplayOut[11]),
    .BusOut10(DisplayOut[10]), .BusOut9(DisplayOut[9]), .BusOut8(DisplayOut[8]), .BusOut7(DisplayOut[7]),
    .BusOut6(DisplayOut[6]), .BusOut5(DisplayOut[5]), .BusOut4(DisplayOut[4]), .BusOut3(DisplayOut[3]),
    .BusOut2(DisplayOut[2]), .BusOut1(DisplayOut[1]), .BusOut0(DisplayOut[0]), .BusBIn15(BSignal[15]),
    .BusBIn14(BSignal[14]), .BusBIn13(BSignal[13]), .BusBIn12(BSignal[12]), .BusBIn11(BSignal[11]),
    .BusBIn10(BSignal[10]), .BusBIn9(BSignal[9]), .BusBIn8(BSignal[8]), .BusBIn7(BSignal[7]),
    .BusBIn6(BSignal[6]), .BusBIn5(BSignal[5]), .BusBIn4(BSignal[4]), .BusBIn3(BSignal[3]),
    .BusBIn2(BSignal[2]), .BusBIn1(BSignal[1]), .BusBIn0(BSignal[0]), .BusAIn15(ASignal[15]),
    .BusAIn14(ASignal[14]), .BusAIn13(ASignal[13]), .BusAIn12(ASignal[12]), .BusAIn11(ASignal[11]),
    .BusAIn10(ASignal[10]), .BusAIn9(ASignal[9]), .BusAIn8(ASignal[8]), .BusAIn7(ASignal[7]),
    .BusAIn6(ASignal[6]), .BusAIn5(ASignal[5]), .BusAIn4(ASignal[4]), .BusAIn3(ASignal[3]),
    .BusAIn2(ASignal[2]), .BusAIn1(ASignal[1]), .BusAIn0(ASignal[0]), .Zero(zero),
    .carry(_16bitaluadder_1_carry));
  and and_2 (and_2_out, and_4_out, and_3_out);
  and and_3 (and_3_out, _74138_1_pin13, _74138_1_pin12);
  and and_4 (and_4_out, _74138_1_pin15, _74138_1_pin14);
  _74138 _74138_1 (
    .pin1(ALU0), .pin2(ALU1), .pin3(ALU2), .pin4(ALU3), .pin5(1'b0), .pin6(1'b1), .pin8(1'b0),
    .pin10(_74138_1_pin10), .pin11(_74138_1_pin11), .pin12(_74138_1_pin12), .pin13(_74138_1_pin13),
    .pin14(_74138_1_pin14), .pin15(_74138_1_pin15), .pin16(1'b1));  // open: pin7, pin9
  _74138 _74138_2 (
    .pin1(ALU0), .pin2(ALU1), .pin3(ALU2), .pin4(_74138_2_pin4), .pin5(1'b0), .pin6(1'b1),
    .pin7(_74138_2_pin7), .pin8(1'b0), .pin9(_74138_2_pin9), .pin10(_74138_2_pin10), .pin11(_74138_2_pin11),
    .pin16(1'b1));  // open: pin12, pin13, pin14, pin15
  not not_2 (_74138_2_pin4, ALU3);

  assign neg = DisplayOut[15];

  // Notes on the sheet:
  //   !Add
  //   !AND
  //   !Not
  //   !Sub
  //   !OR
  //   !XOR
  //   !SHL
  //   !SHR
  //   !ROL
  //   !ROR
endmodule
