// Digital circuit 16BitALUNot.dig as structural Verilog
module _16BitALUNot (
  input  Not,
  input  BusIn8,
  input  BusIn9,
  input  BusIn10,
  input  BusIn7,
  input  BusIn6,
  input  BusIn5,
  input  BusIn4,
  input  BusIn11,
  input  BusIn12,
  input  BusIn3,
  input  BusIn2,
  input  BusIn1,
  input  BusIn13,
  input  BusIn14,
  input  BusIn15,
  input  BusIn0,
  output BusOut0,
  output BusOut1,
  output BusOut2,
  output BusOut3,
  output BusOut4,
  output BusOut5,
  output BusOut6,
  output BusOut7,
  output BusOut8,
  output BusOut9,
  output BusOut10,
  output BusOut11,
  output BusOut12,
  output BusOut13,
  output BusOut14,
  output BusOut15
);

  wire not_1_out, not_2_out, not_3_out, not_4_out, not_5_out, not_6_out, not_7_out, not_8_out, not_9_out,
       not_10_out, not_11_out, not_12_out, not_13_out, not_14_out, not_15_out, not_16_out;

  _16BitBusOut _16bitbusout_1 (
    .RegOut(Not), .BusOut15(BusOut15), .BusOut14(BusOut14), .BusOut13(BusOut13), .BusOut12(BusOut12),
    .BusOut11(BusOut11), .BusOut10(BusOut10), .BusOut9(BusOut9), .BusOut8(BusOut8), .BusOut7(BusOut7),
    .BusOut6(BusOut6), .BusOut5(BusOut5), .BusOut4(BusOut4), .BusOut3(BusOut3), .BusOut2(BusOut2),
    .BusOut1(BusOut1), .BusOut0(BusOut0), .BusIn15(not_1_out), .BusIn14(not_2_out), .BusIn13(not_3_out),
    .BusIn12(not_4_out), .BusIn11(not_5_out), .BusIn10(not_6_out), .BusIn9(not_7_out), .BusIn8(not_8_out),
    .BusIn7(not_9_out), .BusIn6(not_10_out), .BusIn5(not_11_out), .BusIn4(not_12_out), .BusIn3(not_13_out),
    .BusIn2(not_14_out), .BusIn1(not_15_out), .BusIn0(not_16_out));
  not not_1 (not_1_out, BusIn15);
  not not_2 (not_2_out, BusIn14);
  not not_3 (not_3_out, BusIn13);
  not not_4 (not_4_out, BusIn12);
  not not_5 (not_5_out, BusIn11);
  not not_6 (not_6_out, BusIn10);
  not not_7 (not_7_out, BusIn9);
  not not_8 (not_8_out, BusIn8);
  not not_9 (not_9_out, BusIn7);
  not not_10 (not_10_out, BusIn6);
  not not_11 (not_11_out, BusIn5);
  not not_12 (not_12_out, BusIn4);
  not not_13 (not_13_out, BusIn3);
  not not_14 (not_14_out, BusIn2);
  not not_15 (not_15_out, BusIn1);
  not not_16 (not_16_out, BusIn0);

  // Notes on the sheet:
  //   Not: default 1
endmodule
