// Digital circuit 16BitALUOr.dig as structural Verilog
module _16BitALUOr (
  input  Or,
  input  BusAIn8,
  input  BusAIn9,
  input  BusAIn10,
  input  BusAIn7,
  input  BusAIn6,
  input  BusAIn5,
  input  BusAIn4,
  input  BusAIn11,
  input  BusAIn12,
  input  BusAIn3,
  input  BusAIn2,
  input  BusAIn1,
  input  BusAIn13,
  input  BusAIn14,
  input  BusAIn15,
  input  BusAIn0,
  input  BusBIn8,
  input  BusBIn9,
  input  BusBIn10,
  input  BusBIn7,
  input  BusBIn6,
  input  BusBIn5,
  input  BusBIn4,
  input  BusBIn11,
  input  BusBIn12,
  input  BusBIn3,
  input  BusBIn2,
  input  BusBIn1,
  input  BusBIn13,
  input  BusBIn14,
  input  BusBIn15,
  input  BusBIn0,
  output BusOut0,
  output BusOut1,
  output BusOut2,
  output BusOut3,
  output BusOut4,
  output BusOut5,
  output BusOut6,
  output BusOut7,
  output BusOut8,
  output BusOut9,
  output BusOut10,
  output BusOut11,
  output BusOut12,
  output BusOut13,
  output BusOut14,
  output BusOut15
);

  wire or_1_out, or_2_out, or_3_out, or_4_out, or_5_out, or_6_out, or_7_out, or_8_out, or_9_out, or_10_out,
       or_11_out, or_12_out, or_13_out, or_14_out, or_15_out, or_16_out;

  _16BitBusOut _16bitbusout_1 (
    .RegOut(Or), .BusOut15(BusOut15), .BusOut14(BusOut14), .BusOut13(BusOut13), .BusOut12(BusOut12),
    .BusOut11(BusOut11), .BusOut10(BusOut10), .BusOut9(BusOut9), .BusOut8(BusOut8), .BusOut7(BusOut7),
    .BusOut6(BusOut6), .BusOut5(BusOut5), .BusOut4(BusOut4), .BusOut3(BusOut3), .BusOut2(BusOut2),
    .BusOut1(BusOut1), .BusOut0(BusOut0), .BusIn15(or_1_out), .BusIn14(or_2_out), .BusIn13(or_3_out),
    .BusIn12(or_4_out), .BusIn11(or_5_out), .BusIn10(or_6_out), .BusIn9(or_7_out), .BusIn8(or_8_out),
    .BusIn7(or_9_out), .BusIn6(or_10_out), .BusIn5(or_11_out), .BusIn4(or_12_out), .BusIn3(or_13_out),
    .BusIn2(or_14_out), .BusIn1(or_15_out), .BusIn0(or_16_out));
  or or_1 (or_1_out, BusAIn15, BusBIn15);
  or or_2 (or_2_out, BusAIn14, BusBIn14);
  or or_3 (or_3_out, BusAIn13, BusBIn13);
  or or_4 (or_4_out, BusAIn12, BusBIn12);
  or or_5 (or_5_out, BusAIn11, BusBIn11);
  or or_6 (or_6_out, BusAIn10, BusBIn10);
  or or_7 (or_7_out, BusAIn9, BusBIn9);
  or or_8 (or_8_out, BusAIn8, BusBIn8);
  or or_9 (or_9_out, BusAIn7, BusBIn7);
  or or_10 (or_10_out, BusAIn6, BusBIn6);
  or or_11 (or_11_out, BusAIn5, BusBIn5);
  or or_12 (or_12_out, BusAIn4, BusBIn4);
  or or_13 (or_13_out, BusAIn3, BusBIn3);
  or or_14 (or_14_out, BusAIn2, BusBIn2);
  or or_15 (or_15_out, BusAIn1, BusBIn1);
  or or_16 (or_16_out, BusAIn0, BusBIn0);

  // Notes on the sheet:
  //   Or: default 1
endmodule
