// Digital circuit 16BitALUROL.dig as structural Verilog
module _16BitALUROL (
  input  ROL,
  input  BusIn8,
  input  BusIn9,
  input  BusIn10,
  input  BusIn7,
  input  BusIn6,
  input  BusIn5,
  input  BusIn4,
  input  BusIn11,
  input  BusIn12,
  input  BusIn3,
  input  BusIn2,
  input  BusIn1,
  input  BusIn13,
  input  BusIn14,
  input  BusIn15,
  input  BusIn0,
  output BusOut0,
  output BusOut1,
  output BusOut2,
  output BusOut3,
  output BusOut4,
  output BusOut5,
  output BusOut6,
  output BusOut7,
  output BusOut8,
  output BusOut9,
  output BusOut10,
  output BusOut11,
  output BusOut12,
  output BusOut13,
  output BusOut14,
  output BusOut15
);

  _16BitBusOut _16bitbusout_1 (
    .RegOut(ROL), .BusOut15(BusOut15), .BusOut14(BusOut14), .BusOut13(BusOut13), .BusOut12(BusOut12),
    .BusOut11(BusOut11), .BusOut10(BusOut10), .BusOut9(BusOut9), .BusOut8(BusOut8), .BusOut7(BusOut7),
    .BusOut6(BusOut6), .BusOut5(BusOut5), .BusOut4(BusOut4), .BusOut3(BusOut3), .BusOut2(BusOut2),
    .BusOut1(BusOut1), .BusOut0(BusOut0), .BusIn15(BusIn14), .BusIn14(BusIn13), .BusIn13(BusIn12),
    .BusIn12(BusIn11), .BusIn11(BusIn10), .BusIn10(BusIn9), .BusIn9(BusIn8), .BusIn8(BusIn7),
    .BusIn7(BusIn6), .BusIn6(BusIn5), .BusIn5(BusIn4), .BusIn4(BusIn3), .BusIn3(BusIn2), .BusIn2(BusIn1),
    .BusIn1(BusIn0), .BusIn0(BusIn15));

  // Notes on the sheet:
  //   ROL: default 1
endmodule
