// Digital circuit 16BitALUSHR.dig as structural Verilog
module _16BitALUSHR (
  input  SHR,
  input  BusIn8,
  input  BusIn9,
  input  BusIn10,
  input  BusIn7,
  input  BusIn6,
  input  BusIn5,
  input  BusIn4,
  input  BusIn11,
  input  BusIn12,
  input  BusIn3,
  input  BusIn2,
  input  BusIn1,
  input  BusIn13,
  input  BusIn14,
  input  BusIn15,
  input  BusIn0,
  output BusOut1,
  output BusOut2,
  output BusOut3,
  output BusOut4,
  output BusOut5,
  output BusOut6,
  output BusOut7,
  output BusOut8,
  output BusOut9,
  output BusOut10,
  output BusOut11,
  output BusOut12,
  output BusOut13,
  output BusOut14,
  output BusOut0,
  output SHRCarry,
  output BusOut15
);

  wire _16bitbusout_1_busout1, _16bitbusout_1_busout2, _16bitbusout_1_busout3, _16bitbusout_1_busout4,
       _16bitbusout_1_busout5, _16bitbusout_1_busout6, _16bitbusout_1_busout7, _16bitbusout_1_busout8,
       _16bitbusout_1_busout9, _16bitbusout_1_busout10, _16bitbusout_1_busout11, _16bitbusout_1_busout12,
       _16bitbusout_1_busout13, _16bitbusout_1_busout14, _16bitbusout_1_busout15, undriven;

  _16BitBusOut _16bitbusout_1 (
    .RegOut(SHR), .BusOut15(_16bitbusout_1_busout15), .BusOut14(_16bitbusout_1_busout14),
    .BusOut13(_16bitbusout_1_busout13), .BusOut12(_16bitbusout_1_busout12),
    .BusOut11(_16bitbusout_1_busout11), .BusOut10(_16bitbusout_1_busout10), .BusOut9(_16bitbusout_1_busout9),
    .BusOut8(_16bitbusout_1_busout8), .BusOut7(_16bitbusout_1_busout7), .BusOut6(_16bitbusout_1_busout6),
    .BusOut5(_16bitbusout_1_busout5), .BusOut4(_16bitbusout_1_busout4), .BusOut3(_16bitbusout_1_busout3),
    .BusOut2(_16bitbusout_1_busout2), .BusOut1(_16bitbusout_1_busout1), .BusOut0(SHRCarry),
    .BusIn15(undriven), .BusIn14(undriven), .BusIn13(undriven), .BusIn12(undriven), .BusIn11(undriven),
    .BusIn10(undriven), .BusIn9(undriven), .BusIn8(undriven), .BusIn7(undriven), .BusIn6(undriven),
    .BusIn5(undriven), .BusIn4(undriven), .BusIn3(undriven), .BusIn2(undriven), .BusIn1(undriven),
    .BusIn0(BusIn0));
  _16BitBusOut _16bitbusout_2 (
    .RegOut(SHR), .BusOut15(BusOut15), .BusOut14(BusOut14), .BusOut13(BusOut13), .BusOut12(BusOut12),
    .BusOut11(BusOut11), .BusOut10(BusOut10), .BusOut9(BusOut9), .BusOut8(BusOut8), .BusOut7(BusOut7),
    .BusOut6(BusOut6), .BusOut5(BusOut5), .BusOut4(BusOut4), .BusOut3(BusOut3), .BusOut2(BusOut2),
    .BusOut1(BusOut1), .BusOut0(BusOut0), .BusIn15(undriven), .BusIn14(BusIn15), .BusIn13(BusIn14),
    .BusIn12(BusIn13), .BusIn11(BusIn12), .BusIn10(BusIn11), .BusIn9(BusIn10), .BusIn8(BusIn9),
    .BusIn7(BusIn8), .BusIn6(BusIn7), .BusIn5(BusIn6), .BusIn4(BusIn5), .BusIn3(BusIn4), .BusIn2(BusIn3),
    .BusIn1(BusIn2), .BusIn0(BusIn1));

  // Notes on the sheet:
  //   SHR: default 1
endmodule
