// Digital circuit 16BitALUXor.dig as structural Verilog
module _16BitALUXor (
  input  Xor,
  input  BusAIn8,
  input  BusAIn9,
  input  BusAIn10,
  input  BusAIn7,
  input  BusAIn6,
  input  BusAIn5,
  input  BusAIn4,
  input  BusAIn11,
  input  BusAIn12,
  input  BusAIn3,
  input  BusAIn2,
  input  BusAIn1,
  input  BusAIn13,
  input  BusAIn14,
  input  BusAIn15,
  input  BusAIn0,
  input  BusBIn8,
  input  BusBIn9,
  input  BusBIn10,
  input  BusBIn7,
  input  BusBIn6,
  input  BusBIn5,
  input  BusBIn4,
  input  BusBIn11,
  input  BusBIn12,
  input  BusBIn3,
  input  BusBIn2,
  input  BusBIn1,
  input  BusBIn13,
  input  BusBIn14,
  input  BusBIn15,
  input  BusBIn0,
  output BusOut0,
  output BusOut1,
  output BusOut2,
  output BusOut3,
  output BusOut4,
  output BusOut5,
  output BusOut6,
  output BusOut7,
  output BusOut8,
  output BusOut9,
  output BusOut10,
  output BusOut11,
  output BusOut12,
  output BusOut13,
  output BusOut14,
  output BusOut15
);

  wire xor_1_out, xor_2_out, xor_3_out, xor_4_out, xor_5_out, xor_6_out, xor_7_out, xor_8_out, xor_9_out,
       xor_10_out, xor_11_out, xor_12_out, xor_13_out, xor_14_out, xor_15_out, xor_16_out;

  _16BitBusOut _16bitbusout_1 (
    .RegOut(Xor), .BusOut15(BusOut15), .BusOut14(BusOut14), .BusOut13(BusOut13), .BusOut12(BusOut12),
    .BusOut11(BusOut11), .BusOut10(BusOut10), .BusOut9(BusOut9), .BusOut8(BusOut8), .BusOut7(BusOut7),
    .BusOut6(BusOut6), .BusOut5(BusOut5), .BusOut4(BusOut4), .BusOut3(BusOut3), .BusOut2(BusOut2),
    .BusOut1(BusOut1), .BusOut0(BusOut0), .BusIn15(xor_1_out), .BusIn14(xor_2_out), .BusIn13(xor_3_out),
    .BusIn12(xor_4_out), .BusIn11(xor_5_out), .BusIn10(xor_6_out), .BusIn9(xor_7_out), .BusIn8(xor_8_out),
    .BusIn7(xor_9_out), .BusIn6(xor_10_out), .BusIn5(xor_11_out), .BusIn4(xor_12_out), .BusIn3(xor_13_out),
    .BusIn2(xor_14_out), .BusIn1(xor_15_out), .BusIn0(xor_16_out));
  xor xor_1 (xor_1_out, BusAIn15, BusBIn15);
  xor xor_2 (xor_2_out, BusAIn14, BusBIn14);
  xor xor_3 (xor_3_out, BusAIn13, BusBIn13);
  xor xor_4 (xor_4_out, BusAIn12, BusBIn12);
  xor xor_5 (xor_5_out, BusAIn11, BusBIn11);
  xor xor_6 (xor_6_out, BusAIn10, BusBIn10);
  xor xor_7 (xor_7_out, BusAIn9, BusBIn9);
  xor xor_8 (xor_8_out, BusAIn8, BusBIn8);
  xor xor_9 (xor_9_out, BusAIn7, BusBIn7);
  xor xor_10 (xor_10_out, BusAIn6, BusBIn6);
  xor xor_11 (xor_11_out, BusAIn5, BusBIn5);
  xor xor_12 (xor_12_out, BusAIn4, BusBIn4);
  xor xor_13 (xor_13_out, BusAIn3, BusBIn3);
  xor xor_14 (xor_14_out, BusAIn2, BusBIn2);
  xor xor_15 (xor_15_out, BusAIn1, BusBIn1);
  xor xor_16 (xor_16_out, BusAIn0, BusBIn0);

  // Notes on the sheet:
  //   Xor: default 1
endmodule
