// Digital circuit 16BitBusTwo.dig as structural Verilog
module _16BitBusTwo (
  input  RegOutH,
  input  BusIn8,
  input  BusIn9,
  input  BusIn10,
  input  BusIn7,
  input  BusIn6,
  input  BusIn5,
  input  BusIn4,
  input  BusIn11,
  input  BusIn12,
  input  BusIn3,
  input  BusIn2,
  input  BusIn1,
  input  BusIn0,
  input  BusIn13,
  input  BusIn14,
  input  BusIn15,
  input  RegOutL,
  input  Dir,
  output BusOut0,
  output BusOut1,
  output BusOut2,
  output BusOut3,
  output BusOut4,
  output BusOut5,
  output BusOut6,
  output BusOut7,
  output BusOut8,
  output BusOut9,
  output BusOut10,
  output BusOut11,
  output BusOut12,
  output BusOut13,
  output BusOut14,
  output BusOut15
);

  _74245 _74245_1 (
    .pin1(Dir), .pin2(BusOut15), .pin3(BusOut14), .pin4(BusOut13), .pin5(BusOut12), .pin6(BusOut11),
    .pin7(BusOut10), .pin8(BusOut9), .pin9(BusOut8), .pin10(1'b0), .pin11(BusIn8), .pin12(BusIn9),
    .pin13(BusIn10), .pin14(BusIn11), .pin15(BusIn12), .pin16(BusIn13), .pin17(BusIn14), .pin18(BusIn15),
    .pin19(RegOutH), .pin20(1'b1));
  _74245 _74245_2 (
    .pin1(Dir), .pin2(BusOut7), .pin3(BusOut6), .pin4(BusOut5), .pin5(BusOut4), .pin6(BusOut3),
    .pin7(BusOut2), .pin8(BusOut1), .pin9(BusOut0), .pin10(1'b0), .pin11(BusIn0), .pin12(BusIn1),
    .pin13(BusIn2), .pin14(BusIn3), .pin15(BusIn4), .pin16(BusIn5), .pin17(BusIn6), .pin18(BusIn7),
    .pin19(RegOutL), .pin20(1'b1));

  // Notes on the sheet:
  //   RegOutH: default 1
endmodule
