// Digital circuit 16BitCPU.dig as structural Verilog
module _16BitCPU (
  input  in_1,
  input  in_2,
  input  in_3,
  input  in_4,
  input  in_5,
  input  in_6,
  input  in_7,
  input  in_8,
  input  busOut,
  input  in_10,
  input  in_11,
  input  in_12,
  input  in_13,
  input  in_14,
  input  in_15,
  input  in_16,
  input  in_17,
  input  RegOut,
  input  RegIn,
  input  Clock,
  input  Reset
);

  wire _74245_1_pin11, _74245_1_pin12, _74245_1_pin13, _74245_1_pin14, _74245_1_pin15, _74245_1_pin16,
       _74245_1_pin17, _74245_1_pin18, _74245_2_pin11, _74245_2_pin12, _74245_2_pin13, _74245_2_pin14,
       _74245_2_pin15, _74245_2_pin16, _74245_2_pin17, _74245_2_pin18;

  _74245 _74245_1 (
    .pin1(1'b1), .pin2(in_8), .pin3(in_7), .pin4(in_6), .pin5(in_5), .pin6(in_4), .pin7(in_3), .pin8(in_2),
    .pin9(in_1), .pin10(1'b0), .pin11(_74245_1_pin11), .pin12(_74245_1_pin12), .pin13(_74245_1_pin13),
    .pin14(_74245_1_pin14), .pin15(_74245_1_pin15), .pin16(_74245_1_pin16), .pin17(_74245_1_pin17),
    .pin18(_74245_1_pin18), .pin19(busOut), .pin20(1'b1));
  LED Bus14 (.in(_74245_1_pin17));
  LED Bus15 (.in(_74245_1_pin18));
  LED Bus12 (.in(_74245_1_pin15));
  LED Bus13 (.in(_74245_1_pin16));
  LED Bus10 (.in(_74245_1_pin13));
  LED Bus11 (.in(_74245_1_pin14));
  LED Bus8 (.in(_74245_1_pin11));
  LED Bus9 (.in(_74245_1_pin12));
  _74245 _74245_2 (
    .pin1(1'b1), .pin2(in_17), .pin3(in_16), .pin4(in_15), .pin5(in_14), .pin6(in_13), .pin7(in_12),
    .pin8(in_11), .pin9(in_10), .pin10(1'b0), .pin11(_74245_2_pin11), .pin12(_74245_2_pin12),
    .pin13(_74245_2_pin13), .pin14(_74245_2_pin14), .pin15(_74245_2_pin15), .pin16(_74245_2_pin16),
    .pin17(_74245_2_pin17), .pin18(_74245_2_pin18), .pin19(busOut), .pin20(1'b1));
  LED Bus6 (.in(_74245_2_pin17));
  LED Bus7 (.in(_74245_2_pin18));
  LED Bus4 (.in(_74245_2_pin15));
  LED Bus5 (.in(_74245_2_pin16));
  LED Bus2 (.in(_74245_2_pin13));
  LED Bus3 (.in(_74245_2_pin14));
  LED Bus0 (.in(_74245_2_pin11));
  LED Bus1 (.in(_74245_2_pin12));
  _16BitRegisterInt _16bitregisterint_1 ();  // open: RegOut, RegIn, Clock, Reset, BusIn0, BusIn1, BusIn2, BusIn3, BusIn4, BusIn5, BusIn6, BusIn7, BusIn8, BusIn9, BusIn10, BusIn11, BusIn12, BusIn13, BusIn14, BusIn15, Sig15, Sig14, Sig13, Sig12, Sig11, Sig10, Sig9, Sig8, Sig7, Sig6, Sig5, Sig4, Sig3, Sig2, Sig1, Sig0, BusOut15, BusOut14, BusOut13, BusOut12, BusOut11, BusOut10, BusOut9, BusOut8, BusOut7, BusOut6, BusOut5, BusOut4, BusOut3, BusOut2, BusOut1, BusOut0
  LED Signal15 ();  // open: in
  LED Signal14 ();  // open: in
  LED Signal13 ();  // open: in
  LED Signal12 ();  // open: in
  LED Signal11 ();  // open: in
  LED Signal10 ();  // open: in
  LED Signal9 ();  // open: in
  LED Signal8 ();  // open: in
  LED Signal7 ();  // open: in
  LED Signal6 ();  // open: in
  LED Signal5 ();  // open: in
  LED Signal4 ();  // open: in
  LED Signal3 ();  // open: in
  LED Signal2 ();  // open: in
  LED Signal1 ();  // open: in
  LED Signal0 ();  // open: in

  // Notes on the sheet:
  //   busOut: default 1
  //   RegOut: default 1
  //   RegIn: default 1
endmodule
