// Digital circuit 16BitControlInt.dig as structural Verilog
module _16BitControlInt (
  input  Step1,
  input  Step2,
  input  Step3,
  input  Step4,
  input  Ins0,
  input  Ins1,
  input  Ins2,
  input  Ins3,
  input  Ins4,
  input  Ins5,
  input  Ins6,
  input  Ins7,
  input  Zero,
  input  Carry,
  input  Neg,
  input  Interupt,
  input  Extra,
  output nAOut,
  output nAoutLL,
  output nAOutHH,
  output nAoutSwap,
  output nAin,
  output nALL,
  output nAHH,
  output nAInLH,
  output nAInHL,
  output Areset,
  output nBOut,
  output nBoutLL,
  output nBOutHH,
  output nBoutSwap,
  output nBin,
  output nBLL,
  output nBHH,
  output nBInLH,
  output nBInHL,
  output Breset,
  output nCout,
  output nDout,
  output nDoutLL,
  output nDoutSwap,
  output nCin,
  output nCinc,
  output nCdec,
  output Creset,
  output nDoutHH,
  output nDinLL,
  output nDinHH,
  output Dreset,
  output nXout,
  output nXin,
  output nPCout,
  output nPCin,
  output nPCinc,
  output nPCdec,
  output nSTACKout,
  output nSTACKin,
  output nSTACKinc,
  output nSTACKdec,
  output nRAMout,
  output nRAMinL,
  output nINTERflagOut,
  output nINTERregOut,
  output nALUout,
  output ALU0,
  output ALU1,
  output ALU2,
  output ALU3,
  output nEXTRAout1,
  output nEXTRAout2,
  output nEXTRAout3,
  output nEXTRAout4,
  output ClearINTER,
  output INTERplay,
  output INTERpause,
  output Extra1,
  output Extra2,
  output Extra3,
  output Extra4,
  output nIRin,
  output nMARin,
  output nRAMinH,
  output nFLAGin,
  output INTERen,
  output INTERdis,
  output RESET,
  output HALT,
  output NEXTins,
  output nEout,
  output nFout,
  output nGout,
  output nHout,
  output nEin,
  output nFin,
  output nGin,
  output nHin
);

  wire _74138_1_pin1, _74138_1_pin2, _74138_1_pin3, _74138_2_pin4, _74138_3_pin5, _74138_5_pin1,
       _74138_5_pin2, _74138_5_pin3, _74138_6_pin1, _74138_6_pin2, _74138_6_pin3, not_1_out, not_2_out,
       not_3_out, not_4_out;

  not not_1 (not_1_out, _74138_3_pin5);
  not not_2 (not_2_out, _74138_2_pin4);
  _74138 _74138_1 (
    .pin1(_74138_1_pin1), .pin2(_74138_1_pin2), .pin3(_74138_1_pin3), .pin4(not_2_out), .pin5(not_1_out),
    .pin6(1'b1), .pin8(1'b0), .pin12(nEXTRAout4), .pin13(nEXTRAout3), .pin14(nEXTRAout2), .pin15(nEXTRAout1),
    .pin16(1'b1));  // open: pin7, pin9, pin10, pin11
  not not_3 (not_3_out, _74138_3_pin5);
  _74138 _74138_2 (
    .pin1(_74138_1_pin1), .pin2(_74138_1_pin2), .pin3(_74138_1_pin3), .pin4(_74138_2_pin4), .pin5(not_3_out),
    .pin6(1'b1), .pin7(nHout), .pin8(1'b0), .pin9(nGout), .pin10(nFout), .pin11(nEout), .pin12(nALUout),
    .pin13(nINTERflagOut), .pin14(nINTERregOut), .pin15(nRAMout), .pin16(1'b1));
  not not_4 (not_4_out, _74138_2_pin4);
  _74138 _74138_3 (
    .pin1(_74138_1_pin1), .pin2(_74138_1_pin2), .pin3(_74138_1_pin3), .pin4(not_4_out), .pin5(_74138_3_pin5),
    .pin6(1'b1), .pin7(nSTACKout), .pin8(1'b0), .pin9(nPCout), .pin10(nXout), .pin11(nDoutSwap),
    .pin12(nDoutHH), .pin13(nDoutLL), .pin14(nDout), .pin15(nCout), .pin16(1'b1));
  _74138 _74138_4 (
    .pin1(_74138_1_pin1), .pin2(_74138_1_pin2), .pin3(_74138_1_pin3), .pin4(_74138_2_pin4),
    .pin5(_74138_3_pin5), .pin6(1'b1), .pin7(nBoutSwap), .pin8(1'b0), .pin9(nBOutHH), .pin10(nBoutLL),
    .pin11(nBOut), .pin12(nAoutSwap), .pin13(nAOutHH), .pin14(nAoutLL), .pin15(nAOut), .pin16(1'b1));
  _16BitControlAROM _16bitcontrolarom_1 (
    .nCE(1'b0), .nOE(1'b0), .nWE(1'b1), .VCC(1'b1), .GND(1'b0), .I_O0(_74138_3_pin5), .I_O1(_74138_2_pin4),
    .I_O2(_74138_1_pin3), .I_O3(_74138_1_pin2), .I_O4(_74138_1_pin1), .I_O5(Extra1), .I_O6(Extra2),
    .I_O7(Extra3), .A0(Step1), .A1(Step2), .A2(Step3), .A3(Step4), .A4(Ins0), .A5(Ins1), .A6(Ins2),
    .A7(Ins3), .A8(Ins4), .A9(Ins5), .A10(Ins6), .A11(Ins7), .A12(Zero), .A13(Carry), .A14(Neg),
    .A15(Interupt), .A16(Extra));
  _16BitControlBROM _16bitcontrolbrom_1 (
    .nCE(1'b0), .nOE(1'b0), .nWE(1'b1), .VCC(1'b1), .GND(1'b0), .I_O0(Extra4), .I_O1(Areset), .I_O2(Breset),
    .I_O3(Creset), .I_O4(Dreset), .I_O5(ClearINTER), .I_O6(INTERplay), .I_O7(INTERpause), .A0(Step1),
    .A1(Step2), .A2(Step3), .A3(Step4), .A4(Ins0), .A5(Ins1), .A6(Ins2), .A7(Ins3), .A8(Ins4), .A9(Ins5),
    .A10(Ins6), .A11(Ins7), .A12(Zero), .A13(Carry), .A14(Neg), .A15(Interupt), .A16(Extra));
  _74138 _74138_5 (
    .pin1(_74138_5_pin1), .pin2(_74138_5_pin2), .pin3(_74138_5_pin3), .pin4(1'b0), .pin5(1'b0), .pin6(1'b1),
    .pin7(nHin), .pin8(1'b0), .pin9(nGin), .pin10(nBInHL), .pin11(nBInLH), .pin12(nBHH), .pin13(nBLL),
    .pin14(nBin), .pin16(1'b1));  // open: pin15
  _74138 _74138_6 (
    .pin1(_74138_6_pin1), .pin2(_74138_6_pin2), .pin3(_74138_6_pin3), .pin4(1'b0), .pin5(1'b0), .pin6(1'b1),
    .pin7(nFin), .pin8(1'b0), .pin9(nEin), .pin10(nAInHL), .pin11(nAInLH), .pin12(nAHH), .pin13(nALL),
    .pin14(nAin), .pin16(1'b1));  // open: pin15
  _16BitControlCROM _16bitcontrolcrom_1 (
    .nCE(1'b0), .nOE(1'b0), .nWE(1'b1), .VCC(1'b1), .GND(1'b0), .I_O0(_74138_6_pin3), .I_O1(_74138_6_pin2),
    .I_O2(_74138_6_pin1), .I_O3(_74138_5_pin3), .I_O4(_74138_5_pin2), .I_O5(_74138_5_pin1), .I_O6(nCin),
    .I_O7(nDinLL), .A0(Step1), .A1(Step2), .A2(Step3), .A3(Step4), .A4(Ins0), .A5(Ins1), .A6(Ins2),
    .A7(Ins3), .A8(Ins4), .A9(Ins5), .A10(Ins6), .A11(Ins7), .A12(Zero), .A13(Carry), .A14(Neg),
    .A15(Interupt), .A16(Extra));
  _16BitControlDROM _16bitcontroldrom_1 (
    .nCE(1'b0), .nOE(1'b0), .nWE(1'b1), .VCC(1'b1), .GND(1'b0), .I_O0(nDinHH), .I_O1(nXin), .I_O2(nIRin),
    .I_O3(nMARin), .I_O4(nPCin), .I_O5(nSTACKin), .I_O6(nRAMinL), .I_O7(nRAMinH), .A0(Step1), .A1(Step2),
    .A2(Step3), .A3(Step4), .A4(Ins0), .A5(Ins1), .A6(Ins2), .A7(Ins3), .A8(Ins4), .A9(Ins5), .A10(Ins6),
    .A11(Ins7), .A12(Zero), .A13(Carry), .A14(Neg), .A15(Interupt), .A16(Extra));
  _16BitControlEROM _16bitcontrolerom_1 (
    .nCE(1'b0), .nOE(1'b0), .nWE(1'b1), .VCC(1'b1), .GND(1'b0), .I_O0(ALU0), .I_O1(ALU1), .I_O2(ALU2),
    .I_O3(ALU3), .I_O4(nPCinc), .I_O5(nPCdec), .I_O6(nSTACKinc), .I_O7(nSTACKdec), .A0(Step1), .A1(Step2),
    .A2(Step3), .A3(Step4), .A4(Ins0), .A5(Ins1), .A6(Ins2), .A7(Ins3), .A8(Ins4), .A9(Ins5), .A10(Ins6),
    .A11(Ins7), .A12(Zero), .A13(Carry), .A14(Neg), .A15(Interupt), .A16(Extra));
  _16BitControlFROM _16bitcontrolfrom_1 (
    .nCE(1'b0), .nOE(1'b0), .nWE(1'b1), .VCC(1'b1), .GND(1'b0), .I_O0(nCinc), .I_O1(nCdec), .I_O2(nFLAGin),
    .I_O3(INTERen), .I_O4(INTERdis), .I_O5(RESET), .I_O6(HALT), .I_O7(NEXTins), .A0(Step1), .A1(Step2),
    .A2(Step3), .A3(Step4), .A4(Ins0), .A5(Ins1), .A6(Ins2), .A7(Ins3), .A8(Ins4), .A9(Ins5), .A10(Ins6),
    .A11(Ins7), .A12(Zero), .A13(Carry), .A14(Neg), .A15(Interupt), .A16(Extra));
endmodule
