// Digital circuit 16BitControlTest.dig as structural Verilog
module _16BitControlTest (
  input  Step1,
  input  Step2,
  input  Step3,
  input  Step4,
  input  Ins0,
  input  Ins1,
  input  Ins2,
  input  Ins3,
  input  Ins4,
  input  Ins5,
  input  Ins6,
  input  Ins7,
  input  Zero,
  input  Carry,
  input  Neg,
  input  Interupt,
  input  Extra
);

  wire [3:0] undriven, undriven_2, undriven_3, undriven_4, undriven_5, undriven_6, undriven_7, undriven_8,
       undriven_9, undriven_10, undriven_11, undriven_12;

  Seven_Seg_Hex seven_seg_hex_1 (.d(undriven), .dp(1'b0));
  Seven_Seg_Hex seven_seg_hex_2 (.d(undriven_12), .dp(1'b0));
  _16BitControlAROM _16bitcontrolarom_1 (
    .nCE(1'b0), .nOE(1'b0), .nWE(1'b1), .VCC(1'b1), .GND(1'b0), .I_O0(undriven_12[0]), .I_O1(undriven_12[1]),
    .I_O2(undriven_12[2]), .I_O3(undriven_12[3]), .I_O4(undriven[0]), .I_O5(undriven[1]), .I_O6(undriven[2]),
    .I_O7(undriven[3]), .A0(Step1), .A1(Step2), .A2(Step3), .A3(Step4), .A4(Ins0), .A5(Ins1), .A6(Ins2),
    .A7(Ins3), .A8(Ins4), .A9(Ins5), .A10(Ins6), .A11(Ins7), .A12(Zero), .A13(Carry), .A14(Neg),
    .A15(Interupt), .A16(Extra));
  Seven_Seg_Hex seven_seg_hex_3 (.d(undriven_3), .dp(1'b0));
  Seven_Seg_Hex seven_seg_hex_4 (.d(undriven_2), .dp(1'b0));
  _16BitControlBROM _16bitcontrolbrom_1 (
    .nCE(1'b0), .nOE(1'b0), .nWE(1'b1), .VCC(1'b1), .GND(1'b0), .I_O0(undriven_2[0]), .I_O1(undriven_2[1]),
    .I_O2(undriven_2[2]), .I_O3(undriven_2[3]), .I_O4(undriven_3[0]), .I_O5(undriven_3[1]),
    .I_O6(undriven_3[2]), .I_O7(undriven_3[3]), .A0(Step1), .A1(Step2), .A2(Step3), .A3(Step4), .A4(Ins0),
    .A5(Ins1), .A6(Ins2), .A7(Ins3), .A8(Ins4), .A9(Ins5), .A10(Ins6), .A11(Ins7), .A12(Zero), .A13(Carry),
    .A14(Neg), .A15(Interupt), .A16(Extra));
  Seven_Seg_Hex seven_seg_hex_5 (.d(undriven_5), .dp(1'b0));
  Seven_Seg_Hex seven_seg_hex_6 (.d(undriven_4), .dp(1'b0));
  _16BitControlCROM _16bitcontrolcrom_1 (
    .nCE(1'b0), .nOE(1'b0), .nWE(1'b1), .VCC(1'b1), .GND(1'b0), .I_O0(undriven_4[0]), .I_O1(undriven_4[1]),
    .I_O2(undriven_4[2]), .I_O3(undriven_4[3]), .I_O4(undriven_5[0]), .I_O5(undriven_5[1]),
    .I_O6(undriven_5[2]), .I_O7(undriven_5[3]), .A0(Step1), .A1(Step2), .A2(Step3), .A3(Step4), .A4(Ins0),
    .A5(Ins1), .A6(Ins2), .A7(Ins3), .A8(Ins4), .A9(Ins5), .A10(Ins6), .A11(Ins7), .A12(Zero), .A13(Carry),
    .A14(Neg), .A15(Interupt), .A16(Extra));
  Seven_Seg_Hex seven_seg_hex_7 (.d(undriven_7), .dp(1'b0));
  Seven_Seg_Hex seven_seg_hex_8 (.d(undriven_6), .dp(1'b0));
  _16BitControlDROM _16bitcontroldrom_1 (
    .nCE(1'b0), .nOE(1'b0), .nWE(1'b1), .VCC(1'b1), .GND(1'b0), .I_O0(undriven_6[0]), .I_O1(undriven_6[1]),
    .I_O2(undriven_6[2]), .I_O3(undriven_6[3]), .I_O4(undriven_7[0]), .I_O5(undriven_7[1]),
    .I_O6(undriven_7[2]), .I_O7(undriven_7[3]), .A0(Step1), .A1(Step2), .A2(Step3), .A3(Step4), .A4(Ins0),
    .A5(Ins1), .A6(Ins2), .A7(Ins3), .A8(Ins4), .A9(Ins5), .A10(Ins6), .A11(Ins7), .A12(Zero), .A13(Carry),
    .A14(Neg), .A15(Interupt), .A16(Extra));
  Seven_Seg_Hex seven_seg_hex_9 (.d(undriven_8), .dp(1'b0));
  Seven_Seg_Hex seven_seg_hex_10 (.d(undriven_9), .dp(1'b0));
  _16BitControlEROM _16bitcontrolerom_1 (
    .nCE(1'b0), .nOE(1'b0), .nWE(1'b1), .VCC(1'b1), .GND(1'b0), .I_O0(undriven_9[0]), .I_O1(undriven_9[1]),
    .I_O2(undriven_9[2]), .I_O3(undriven_9[3]), .I_O4(undriven_8[0]), .I_O5(undriven_8[1]),
    .I_O6(undriven_8[2]), .I_O7(undriven_8[3]), .A0(Step1), .A1(Step2), .A2(Step3), .A3(Step4), .A4(Ins0),
    .A5(Ins1), .A6(Ins2), .A7(Ins3), .A8(Ins4), .A9(Ins5), .A10(Ins6), .A11(Ins7), .A12(Zero), .A13(Carry),
    .A14(Neg), .A15(Interupt), .A16(Extra));
  Seven_Seg_Hex seven_seg_hex_11 (.d(undriven_10), .dp(1'b0));
  Seven_Seg_Hex seven_seg_hex_12 (.d(undriven_11), .dp(1'b0));
  _16BitControlFROM _16bitcontrolfrom_1 (
    .nCE(1'b0), .nOE(1'b0), .nWE(1'b1), .VCC(1'b1), .GND(1'b0), .I_O0(undriven_11[0]), .I_O1(undriven_11[1]),
    .I_O2(undriven_11[2]), .I_O3(undriven_11[3]), .I_O4(undriven_10[0]), .I_O5(undriven_10[1]),
    .I_O6(undriven_10[2]), .I_O7(undriven_10[3]), .A0(Step1), .A1(Step2), .A2(Step3), .A3(Step4), .A4(Ins0),
    .A5(Ins1), .A6(Ins2), .A7(Ins3), .A8(Ins4), .A9(Ins5), .A10(Ins6), .A11(Ins7), .A12(Zero), .A13(Carry),
    .A14(Neg), .A15(Interupt), .A16(Extra));
endmodule
