// Digital circuit 16BitDisplayInt.dig as structural Verilog
module _16BitDisplayInt (
  input  [15:0] Input,
  output [3:0] Digit4,
  output Dec4,
  output [3:0] Digit3,
  output Dec3,
  output [3:0] Digit2,
  output Dec2,
  output [3:0] Digit1,
  output Dec1
);


  assign Dec1 = 1'b0;
  assign Dec2 = 1'b0;
  assign Dec3 = 1'b0;
  assign Dec4 = 1'b0;
  assign Digit1 = Input[3:0];
  assign Digit2 = Input[7:4];
  assign Digit3 = Input[11:8];
  assign Digit4 = Input[15:12];
endmodule
