// Digital circuit 16BitDisplayInt1.dig as structural Verilog
module _16BitDisplayInt1 (
  input  Input0,
  input  Input1,
  input  Input2,
  input  Input3,
  input  Input4,
  input  Input5,
  input  Input6,
  input  Input7,
  input  Input8,
  input  Input9,
  input  Input10,
  input  Input11,
  input  Input12,
  input  Input13,
  input  Input14,
  input  Input15,
  output [3:0] Digit4,
  output Dec4,
  output [3:0] Digit3,
  output Dec3,
  output [3:0] Digit2,
  output Dec2,
  output [3:0] Digit1,
  output Dec1
);


  assign Dec1 = 1'b0;
  assign Dec2 = 1'b0;
  assign Dec3 = 1'b0;
  assign Dec4 = 1'b0;
  assign Digit1 = {Input0, Input1, Input2, Input3};
  assign Digit2 = {Input4, Input5, Input6, Input7};
  assign Digit3 = {Input8, Input9, Input10, Input11};
  assign Digit4 = {Input12, Input13, Input14, Input15};
endmodule
