// Digital circuit 16BitDisplayRAM.dig as structural Verilog
module _16BitDisplayRAM (
  input  [15:0] Input,
  input  addr0,
  output [3:0] Digit4,
  output Dec4,
  output [3:0] Digit3,
  output Dec3,
  output [3:0] Digit2,
  output Dec2,
  output [3:0] Digit1,
  output Dec1
);

  wire and_1_out, and_2_out, and_3_out, and_4_out, and_5_out, and_6_out, and_7_out, and_8_out, and_9_out,
       and_10_out, and_11_out, and_12_out, and_13_out, and_14_out, and_15_out, and_16_out, and_17_out,
       and_18_out, and_19_out, and_20_out, and_21_out, and_22_out, and_23_out, and_24_out, and_25_out,
       and_26_out, and_27_out, and_28_out, and_29_out, and_30_out, and_31_out, and_32_out, not_1_out;

  not not_1 (not_1_out, addr0);
  and and_1 (and_1_out, Input[0], not_1_out);
  and and_2 (and_2_out, Input[8], addr0);
  and and_3 (and_3_out, Input[1], not_1_out);
  and and_4 (and_4_out, Input[9], addr0);
  and and_5 (and_5_out, Input[2], not_1_out);
  and and_6 (and_6_out, Input[10], addr0);
  and and_7 (and_7_out, Input[3], not_1_out);
  and and_8 (and_8_out, Input[11], addr0);
  and and_9 (and_9_out, Input[4], not_1_out);
  and and_10 (and_10_out, Input[12], addr0);
  and and_11 (and_11_out, Input[5], not_1_out);
  and and_12 (and_12_out, Input[13], addr0);
  and and_13 (and_13_out, Input[6], not_1_out);
  and and_14 (and_14_out, Input[14], addr0);
  and and_15 (and_15_out, Input[7], not_1_out);
  and and_16 (and_16_out, Input[15], addr0);
  and and_17 (and_17_out, Input[8], not_1_out);
  and and_18 (and_18_out, Input[0], addr0);
  and and_19 (and_19_out, Input[9], not_1_out);
  and and_20 (and_20_out, Input[1], addr0);
  and and_21 (and_21_out, Input[10], not_1_out);
  and and_22 (and_22_out, Input[2], addr0);
  and and_23 (and_23_out, Input[11], not_1_out);
  and and_24 (and_24_out, Input[3], addr0);
  and and_25 (and_25_out, Input[12], not_1_out);
  and and_26 (and_26_out, Input[4], addr0);
  and and_27 (and_27_out, Input[13], not_1_out);
  and and_28 (and_28_out, Input[5], addr0);
  and and_29 (and_29_out, Input[14], not_1_out);
  and and_30 (and_30_out, Input[6], addr0);
  and and_31 (and_31_out, Input[15], not_1_out);
  and and_32 (and_32_out, Input[7], addr0);
  or or_1 (Digit1[0], and_1_out, and_2_out);
  or or_2 (Digit1[1], and_3_out, and_4_out);
  or or_3 (Digit1[2], and_5_out, and_6_out);
  or or_4 (Digit1[3], and_7_out, and_8_out);
  or or_5 (Digit2[0], and_9_out, and_10_out);
  or or_6 (Digit2[1], and_11_out, and_12_out);
  or or_7 (Digit2[2], and_13_out, and_14_out);
  or or_8 (Digit2[3], and_15_out, and_16_out);
  or or_9 (Digit3[0], and_17_out, and_18_out);
  or or_10 (Digit3[1], and_19_out, and_20_out);
  or or_11 (Digit3[2], and_21_out, and_22_out);
  or or_12 (Digit3[3], and_23_out, and_24_out);
  or or_13 (Digit4[0], and_25_out, and_26_out);
  or or_14 (Digit4[1], and_27_out, and_28_out);
  or or_15 (Digit4[2], and_29_out, and_30_out);
  or or_16 (Digit4[3], and_31_out, and_32_out);

  assign Dec1 = 1'b0;
  assign Dec2 = 1'b0;
  assign Dec3 = 1'b0;
  assign Dec4 = 1'b0;
endmodule
