// Digital circuit 16BitInterupt.dig as structural Verilog
module _16BitInterupt (
  input  RESET,
  input  clk,
  input  Pulse,
  input  Source,
  input  Halt,
  input  in_6,
  input  in_7,
  input  in_8,
  input  in_9,
  input  in_10,
  input  in_11,
  input  in_12,
  input  clk_2,
  input  in_14,
  input  in_15,
  input  in_16,
  input  in_17,
  input  in_18,
  input  in_19,
  input  in_20,
  input  in_21,
  input  in_22,
  input  in_23,
  input  in_24,
  input  in_25,
  input  in_26,
  input  in_27,
  input  in_28
);

  wire _74138_1_pin7, _74138_1_pin9, _74138_1_pin10, _74138_1_pin11, _74138_1_pin12, _74138_1_pin13,
       _74138_1_pin14, _74138_1_pin15, _74138_2_pin4, _74138_2_pin7, _74138_3_pin7, _74138_3_pin9,
       _74138_3_pin10, _74138_3_pin11, _74161_1_pin2, _74161_1_pin9, _74161_1_pin11, _74161_1_pin12,
       _74161_1_pin13, _74161_1_pin14, _74161_2_pin11, _74161_2_pin12, _74161_2_pin13, _74161_2_pin14,
       _74173_1_pin3, _74173_1_pin4, _74173_1_pin5, _74173_1_pin6, _74173_1_pin9, _74173_1_pin11,
       _74173_1_pin12, _74173_1_pin13, _74173_1_pin14, and_1_out, and_2_out, and_3_out, and_4_out, and_5_out,
       and_6_out, and_7_out, and_8_out, and_9_out, and_10_out, and_11_out, and_12_out, and_13_out,
       and_14_out, and_15_out, nand_1_out, nand_2_out, nand_3_out, nand_4_out, nand_5_out, nand_6_out,
       nand_7_out, nand_8_out, not_1_out, not_2_out, not_4_out, not_5_out, not_6_out, not_7_out, not_8_out,
       not_9_out, not_10_out, not_11_out, not_12_out, not_13_out, not_14_out, not_15_out, or_1_out, or_2_out,
       or_3_out, or_4_out, or_5_out, or_6_out, or_7_out, or_9_out, xor_1_out, xor_2_out, xor_3_out, xor_4_out;

  or or_1 (or_1_out, in_21, in_22, in_23, in_24);
  or or_2 (or_2_out, in_17, in_18, in_19, in_20);
  _74138 _74138_1 (
    .pin1(in_25), .pin2(in_26), .pin3(in_27), .pin4(in_28), .pin5(1'b0), .pin6(1'b1), .pin7(_74138_1_pin7),
    .pin8(1'b0), .pin9(_74138_1_pin9), .pin10(_74138_1_pin10), .pin11(_74138_1_pin11),
    .pin12(_74138_1_pin12), .pin13(_74138_1_pin13), .pin14(_74138_1_pin14), .pin15(_74138_1_pin15),
    .pin16(1'b1));
  not not_1 (not_1_out, or_1_out);
  not not_2 (not_2_out, or_2_out);
  and and_1 (and_1_out, not_1_out, not_2_out);
  and and_2 (and_2_out, _74138_1_pin15, and_1_out);
  and and_3 (and_3_out, _74138_1_pin14, and_1_out);
  and and_4 (and_4_out, _74138_1_pin13, and_1_out);
  and and_5 (and_5_out, _74138_1_pin12, and_1_out);
  and and_6 (and_6_out, _74138_1_pin11, and_1_out);
  and and_7 (and_7_out, _74138_1_pin10, and_1_out);
  and and_8 (and_8_out, _74138_1_pin9, and_1_out);
  and and_9 (and_9_out, _74138_1_pin7, and_1_out);
  LED led_1 (.in(and_2_out));
  LED led_2 (.in(and_3_out));
  LED led_3 (.in(and_4_out));
  LED led_4 (.in(and_5_out));
  LED led_5 (.in(and_6_out));
  LED led_6 (.in(and_7_out));
  LED led_7 (.in(and_8_out));
  LED led_8 (.in(and_9_out));
  _74161 _74161_1 (
    .pin1(in_6), .pin2(_74161_1_pin2), .pin3(1'b0), .pin4(1'b0), .pin5(1'b0), .pin6(1'b0), .pin7(1'b1),
    .pin8(1'b0), .pin9(_74161_1_pin9), .pin10(1'b1), .pin11(_74161_1_pin11), .pin12(_74161_1_pin12),
    .pin13(_74161_1_pin13), .pin14(_74161_1_pin14), .pin16(1'b1));  // open: pin15
  LED led_9 (.in(_74161_1_pin11));
  LED led_10 (.in(_74161_1_pin13));
  LED led_11 (.in(_74161_1_pin12));
  LED led_12 (.in(_74161_1_pin14));
  not not_3 (_74161_1_pin9, and_12_out);
  not not_4 (not_4_out, in_14);
  not not_5 (not_5_out, in_16);
  not not_6 (not_6_out, in_7);
  not not_7 (not_7_out, in_8);
  and and_10 (and_10_out, not_4_out, in_15, 1'b1, not_5_out);
  not not_8 (not_8_out, in_9);
  not not_9 (not_9_out, in_10);
  xor xor_1 (xor_1_out, _74161_1_pin14, not_9_out);
  xor xor_2 (xor_2_out, not_8_out, _74161_1_pin13);
  xor xor_3 (xor_3_out, not_7_out, _74161_1_pin12);
  xor xor_4 (xor_4_out, not_6_out, _74161_1_pin11);
  not not_10 (not_10_out, and_10_out);
  and and_11 (and_11_out, not_4_out, not_10_out, 1'b1, in_16);
  and and_12 (and_12_out, xor_1_out, xor_2_out, xor_3_out, xor_4_out);
  LED led_13 (.in(in_14));
  LED led_14 (.in(and_10_out));
  LED led_15 (.in(and_11_out));
  not not_11 (not_11_out, Source);
  and and_13 (and_13_out, and_12_out, not_12_out);
  not not_12 (not_12_out, RESET);
  and and_14 (and_14_out, Pulse, not_11_out);
  and and_15 (and_15_out, Source, clk);
  not not_13 (not_13_out, Halt);
  nand nand_1 (nand_1_out, and_13_out, clk_2);
  nand nand_2 (nand_2_out, clk_2, RESET);
  or or_3 (or_3_out, and_14_out, and_15_out);
  nand nand_3 (nand_3_out, nand_1_out, nand_4_out);
  nand nand_4 (nand_4_out, nand_3_out, nand_2_out);
  or or_4 (or_4_out, _74173_1_pin6, _74173_1_pin6);
  LED led_16 (.in(or_4_out));
  and and_16 (_74161_1_pin2, or_3_out, not_13_out);
  not not_14 (not_14_out, clk_2);
  _74173 _74173_1 (
    .pin1(1'b0), .pin2(1'b0), .pin3(_74173_1_pin3), .pin4(_74173_1_pin4), .pin5(_74173_1_pin5),
    .pin6(_74173_1_pin6), .pin7(clk_2), .pin8(1'b0), .pin9(_74173_1_pin9), .pin10(_74173_1_pin9),
    .pin11(_74173_1_pin11), .pin12(_74173_1_pin12), .pin13(_74173_1_pin13), .pin14(_74173_1_pin14),
    .pin15(RESET), .pin16(1'b1));
  or or_5 (or_5_out, _74173_1_pin4, _74173_1_pin5);
  LED led_17 (.in(or_6_out));
  LED led_18 (.in(or_5_out));
  LED led_19 (.in(_74161_1_pin2));
  nand nand_5 (nand_5_out, nand_3_out, not_14_out);
  nand nand_6 (nand_6_out, not_14_out, nand_4_out);
  LED led_20 (.in(_74173_1_pin3));
  or or_6 (or_6_out, _74173_1_pin3, _74173_1_pin5);
  LED led_21 (.in(1'b0));
  LED led_22 (.in(_74173_1_pin5));
  LED led_23 (.in(_74173_1_pin4));
  or or_7 (or_7_out, _74173_1_pin4, _74173_1_pin3);
  or or_8 (_74173_1_pin9, or_9_out, or_7_out);
  LED led_24 (.in(_74173_1_pin9));
  nand nand_7 (nand_7_out, nand_5_out, nand_8_out);
  nand nand_8 (nand_8_out, nand_7_out, nand_6_out);
  LED led_25 (.in(_74173_1_pin6));
  or or_9 (or_9_out, _74173_1_pin6, _74173_1_pin5);
  LED led_26 (.in(nand_7_out));
  LED led_27 (.in(nand_8_out));
  LED led_28 (.in(_74173_1_pin14));
  nor nor_1 (_74173_1_pin14, _74138_3_pin7, nand_8_out);
  nor nor_2 (_74173_1_pin13, in_12, _74138_3_pin9);
  nor nor_3 (_74173_1_pin12, in_12, _74138_3_pin10);
  not not_15 (not_15_out, RESET);
  nor nor_4 (_74173_1_pin11, in_11, _74138_3_pin11);
  _74161 _74161_2 (
    .pin1(not_15_out), .pin2(clk_2), .pin3(1'b0), .pin4(1'b0), .pin5(1'b0), .pin6(1'b0), .pin7(1'b1),
    .pin8(1'b0), .pin9(1'b1), .pin10(1'b1), .pin11(_74161_2_pin11), .pin12(_74161_2_pin12),
    .pin13(_74161_2_pin13), .pin14(_74161_2_pin14), .pin16(1'b1));  // open: pin15
  _74138 _74138_2 (
    .pin1(_74161_2_pin14), .pin2(_74161_2_pin13), .pin3(_74161_2_pin12), .pin4(_74138_2_pin4), .pin5(1'b0),
    .pin6(1'b1), .pin7(_74138_2_pin7), .pin8(1'b0), .pin16(1'b1));  // open: pin9, pin10, pin11, pin12, pin13, pin14, pin15
  _74138 _74138_3 (
    .pin1(_74161_2_pin14), .pin2(_74161_2_pin13), .pin3(_74161_2_pin12), .pin4(_74161_2_pin11), .pin5(1'b0),
    .pin6(1'b1), .pin7(_74138_3_pin7), .pin8(1'b0), .pin9(_74138_3_pin9), .pin10(_74138_3_pin10),
    .pin11(_74138_3_pin11), .pin16(1'b1));  // open: pin12, pin13, pin14, pin15
  not not_16 (_74138_2_pin4, _74161_2_pin11);

  // Notes on the sheet:
  //   in_8: default 1
  //   in_10: default 1
  //   in_11: default 1
  //   in_12: default 1
  //   clk_2: Hz: 50000
  //   contents of Control2 (hex, n*v repeats v):
  //   40,14,0,0,0,0,0,0,40,14,48,12,0,0,0,0,40,14,48,10,2,0,0,0,40,14,48,10,2,0,0,0,40, 14,48,21,
  //   0,0,0,0,40,14,a,0,0,0,0,0,40,14,8,0,0,0,0,0,40,14,0,0,0,0,0,0,40,14,0,0, 0,0,0,0,40,14,0,0,
  //   0,0,0,0,40,14,0,0,0,0,0,0,40,14,0,0,0,0,0,0,40,14,0,0,0,0,0,0,40, 14,0,0,0,0,0,0,40,14,1,0,
  //   0,0,0,0,40,14,80,0,0,0,0,0,4,8,0,0,0,0,0,0,4,8,0,0,0,0,0, 0,4,8,0,20,81,0,0,0,4,8,0,20,c1,0,
  //   0,0,4,8,0,0,0,0,0,0,4,8,0,0,0,0,0,0,4,8,2,0,0,0, 0,0,4,8,0,0,0,0,0,0,4,8,0,0,0,0,0,0,4,8,0,
  //   0,0,0,0,0,4,8,0,0,0,0,0,0,4,8,0,0,0,0,0, 0,4,8,0,0,0,0,0,0,4,8,0,0,0,0,0,0,4,8,10,0,0,0,0,0,
  //   4,8,0,0,0,0,0,0,40,14,0,0,0,0, 0,0,40,14,48,12,0,0,0,0,40,14,48,10,2,0,0,0,40,14,48,10,2,0,
  //   0,0,40,14,48,21,0,0,0, 0,40,14,a,0,0,0,0,0,40,14,8,0,0,0,0,0,40,14,8,0,0,0,0,0,40,14,0,0,0,
  //   0,0,0,40,14,0, 0,0,0,0,0,40,14,0,0,0,0,0,0,40,14,0,0,0,0,0,0,40,14,0,0,0,0,0,0,40,14,0,0,0,
  //   0,0,0, 40,14,1,0,0,0,0,0,40,14,80,0,0,0,0,0,4,8,0,0,0,0,0,0,4,8,0,0,0,0,0,0,4,8,0,20,81, 0,
  //   0,0,4,8,0,20,c1,0,0,0,4,8,0,0,0,0,0,0,4,8,0,0,0,0,0,0,4,8,2,0,0,0,0,0,4,8,2,0,0, 0,0,0,4,8,
  //   0,0,0,0,0,0,4,8,0,0,0,0,0,0,4,8,0,0,0,0,0,0,4,8,0,0,0,0,0,0,4,8,0,0,0,0, 0,0,4,8,0,0,0,0,0,
  //   0,4,8,10,0,0,0,0,0,4,8,0,0,0,0,0,0,40,14,0,0,0,0,0,0,40,14,48,12, 0,0,0,0,40,14,48,10,2,0,0,
  //   0,40,14,48,10,2,0,0,0,40,14,48,21,0,0,0,0,40,14,a,0,0,0, 0,0,40,14,8,0,0,0,0,0,40,14,0,0,0,
  //   0,0,0,40,14,8,0,0,0,0,0,40,14,0,0,0,0,0,0,40,14, 0,0,0,0,0,0,40,14,0,0,0,0,0,0,40,14,0,0,0,
  //   0,0,0,40,14,0,0,0,0,0,0,40,14,1,0,0,0,0, 0,40,14,80,0,0,0,0,0,4,8,0,0,0,0,0,0,4,8,0,0,0,0,0,
  //   0,4,8,0,20,81,0,0,0,4,8,0,20,c1, 0,0,0,4,8,0,0,0,0,0,0,4,8,0,0,0,0,0,0,4,8,2,0,0,0,0,0,4,8,
  //   0,0,0,0,0,0,4,8,2,0,0,0, 0,0,4,8,0,0,0,0,0,0,4,8,0,0,0,0,0,0,4,8,0,0,0,0,0,0,4,8,0,0,0,0,0,
  //   0,4,8,0,0,0,0,0, 0,4,8,10,0,0,0,0,0,4,8,0,0,0,0,0,0,40,14,0,0,0,0,0,0,40,14,48,12,0,0,0,0,40,
  //   14,48, 10,2,0,0,0,40,14,48,10,2,0,0,0,40,14,48,21,0,0,0,0,40,14,a,0,0,0,0,0,40,14,8,0,0, 0,
  //   0,0,40,14,8,0,0,0,0,0,40,14,8,0,0,0,0,0,40,14,0,0,0,0,0,0,40,14,0,0,0,0,0,0,40, 14,0,0,0,0,
  //   0,0,40,14,0,0,0,0,0,0,40,14,0,0,0,0,0,0,40,14,1,0,0,0,0,0,40,14,80,0,0, 0,0,0,4,8,0,0,0,0,0,
  //   0,4,8,0,0,0,0,0,0,4,8,0,20,81,0,0,0,4,8,0,20,c1,0,0,0,4,8,0,0, 0,0,0,0,4,8,0,0,0,0,0,0,4,8,
  //   2,0,0,0,0,0,4,8,2,0,0,0,0,0,4,8,2,0,0,0,0,0,4,8,0,0,0, 0,0,0,4,8,0,0,0,0,0,0,4,8,0,0,0,0,0,
  //   0,4,8,0,0,0,0,0,0,4,8,0,0,0,0,0,0,4,8,10,0,0, 0,0,0,4,8
  //   contents of Control1 (hex, n*v repeats v):
  //   40,14,0,0,0,0,0,0,40,14,48,12,0,0,0,0,40,14,48,10,2,0,0,0,40,14,48,10,2,0,0,0,40, 14,48,21,
  //   0,0,0,0,40,14,a,0,0,0,0,0,40,14,8,0,0,0,0,0,40,14,0,0,0,0,0,0,40,14,0,0, 0,0,0,0,40,14,0,0,
  //   0,0,0,0,40,14,0,0,0,0,0,0,40,14,0,0,0,0,0,0,40,14,0,0,0,0,0,0,40, 14,0,0,0,0,0,0,40,14,1,0,
  //   0,0,0,0,40,14,80,0,0,0,0,0,4,8,0,0,0,0,0,0,4,8,0,0,0,0,0, 0,4,8,0,20,81,0,0,0,4,8,0,20,c1,0,
  //   0,0,4,8,0,0,0,0,0,0,4,8,0,0,0,0,0,0,4,8,2,0,0,0, 0,0,4,8,0,0,0,0,0,0,4,8,0,0,0,0,0,0,4,8,0,
  //   0,0,0,0,0,4,8,0,0,0,0,0,0,4,8,0,0,0,0,0, 0,4,8,0,0,0,0,0,0,4,8,0,0,0,0,0,0,4,8,10,0,0,0,0,0,
  //   4,8,0,0,0,0,0,0,40,14,0,0,0,0, 0,0,40,14,48,12,0,0,0,0,40,14,48,10,2,0,0,0,40,14,48,10,2,0,
  //   0,0,40,14,48,21,0,0,0, 0,40,14,a,0,0,0,0,0,40,14,8,0,0,0,0,0,40,14,8,0,0,0,0,0,40,14,0,0,0,
  //   0,0,0,40,14,0, 0,0,0,0,0,40,14,0,0,0,0,0,0,40,14,0,0,0,0,0,0,40,14,0,0,0,0,0,0,40,14,0,0,0,
  //   0,0,0, 40,14,1,0,0,0,0,0,40,14,80,0,0,0,0,0,4,8,0,0,0,0,0,0,4,8,0,0,0,0,0,0,4,8,0,20,81, 0,
  //   0,0,4,8,0,20,c1,0,0,0,4,8,0,0,0,0,0,0,4,8,0,0,0,0,0,0,4,8,2,0,0,0,0,0,4,8,2,0,0, 0,0,0,4,8,
  //   0,0,0,0,0,0,4,8,0,0,0,0,0,0,4,8,0,0,0,0,0,0,4,8,0,0,0,0,0,0,4,8,0,0,0,0, 0,0,4,8,0,0,0,0,0,
  //   0,4,8,10,0,0,0,0,0,4,8,0,0,0,0,0,0,40,14,0,0,0,0,0,0,40,14,48,12, 0,0,0,0,40,14,48,10,2,0,0,
  //   0,40,14,48,10,2,0,0,0,40,14,48,21,0,0,0,0,40,14,a,0,0,0, 0,0,40,14,8,0,0,0,0,0,40,14,0,0,0,
  //   0,0,0,40,14,8,0,0,0,0,0,40,14,0,0,0,0,0,0,40,14, 0,0,0,0,0,0,40,14,0,0,0,0,0,0,40,14,0,0,0,
  //   0,0,0,40,14,0,0,0,0,0,0,40,14,1,0,0,0,0, 0,40,14,80,0,0,0,0,0,4,8,0,0,0,0,0,0,4,8,0,0,0,0,0,
  //   0,4,8,0,20,81,0,0,0,4,8,0,20,c1, 0,0,0,4,8,0,0,0,0,0,0,4,8,0,0,0,0,0,0,4,8,2,0,0,0,0,0,4,8,
  //   0,0,0,0,0,0,4,8,2,0,0,0, 0,0,4,8,0,0,0,0,0,0,4,8,0,0,0,0,0,0,4,8,0,0,0,0,0,0,4,8,0,0,0,0,0,
  //   0,4,8,0,0,0,0,0, 0,4,8,10,0,0,0,0,0,4,8,0,0,0,0,0,0,40,14,0,0,0,0,0,0,40,14,48,12,0,0,0,0,40,
  //   14,48, 10,2,0,0,0,40,14,48,10,2,0,0,0,40,14,48,21,0,0,0,0,40,14,a,0,0,0,0,0,40,14,8,0,0, 0,
  //   0,0,40,14,8,0,0,0,0,0,40,14,8,0,0,0,0,0,40,14,0,0,0,0,0,0,40,14,0,0,0,0,0,0,40, 14,0,0,0,0,
  //   0,0,40,14,0,0,0,0,0,0,40,14,0,0,0,0,0,0,40,14,1,0,0,0,0,0,40,14,80,0,0, 0,0,0,4,8,0,0,0,0,0,
  //   0,4,8,0,0,0,0,0,0,4,8,0,20,81,0,0,0,4,8,0,20,c1,0,0,0,4,8,0,0, 0,0,0,0,4,8,0,0,0,0,0,0,4,8,
  //   2,0,0,0,0,0,4,8,2,0,0,0,0,0,4,8,2,0,0,0,0,0,4,8,0,0,0, 0,0,0,4,8,0,0,0,0,0,0,4,8,0,0,0,0,0,
  //   0,4,8,0,0,0,0,0,0,4,8,0,0,0,0,0,0,4,8,10,0,0, 0,0,0,4,8
endmodule
