// Digital circuit 16BitRAM.dig as structural Verilog
module _16BitRAM (
  input  BusAIn8,
  input  BusAIn9,
  input  BusAIn10,
  input  BusAIn7,
  input  BusAIn6,
  input  BusAIn5,
  input  BusAIn4,
  input  BusAIn11,
  input  BusAIn12,
  input  BusAIn3,
  input  BusAIn2,
  input  BusAIn1,
  input  BusAIn13,
  input  BusAIn14,
  input  BusAIn15,
  input  BusAIn0,
  input  RAMInH,
  input  RAMInL,
  input  RAMOut,
  input  in_74,
  input  in_75,
  input  in_76,
  input  in_77,
  input  in_78,
  input  in_79,
  input  in_80,
  input  in_81,
  input  busOut,
  input  in_83,
  input  in_84,
  input  in_85,
  input  in_86,
  input  in_87,
  input  in_88,
  input  in_89,
  input  in_90,
  output Sig15,
  output Sig14,
  output Sig13,
  output Sig12,
  output Sig11,
  output Sig10,
  output Sig9,
  output Sig8,
  output Sig7,
  output Sig6,
  output Sig5,
  output Sig4,
  output Sig3,
  output Sig2,
  output Sig1,
  output Sig0,
  output LOWADDR1,
  output LOWADDR2,
  output LOWADDR3,
  output LOWADDR4,
  output LOWADDR5,
  output LOWADDR6,
  output LOWADDR7,
  output LOWADDR8,
  output LOWADDR9,
  output LOWADDR10,
  output LOWADDR11,
  output LOWADDR12,
  output LOWADDR13,
  output LOWADDR14,
  output LOWADDR15,
  output SRAM,
  output FLASH,
  output PREF,
  output Databus0,
  output Databus1,
  output Databus2,
  output Databus3,
  output Databus4,
  output Databus5,
  output Databus6,
  output Databus7,
  output Databus8,
  output Databus9,
  output Databus10,
  output Databus11,
  output Databus12,
  output Databus13,
  output Databus14,
  output Databus15,
  output HighHighEn,
  output LowLowEn,
  output HighLowEn,
  output LowHighEn
);

  wire _74283_1_pin7, _74283_2_pin7, _74283_3_pin7, and_2_out, and_3_out, and_5_out, and_6_out, and_8_out,
       and_10_out, nor_1_out, not_1_out, not_2_out, or_1_out, or_2_out, or_3_out, or_4_out, or_5_out,
       or_6_out, xor_1_out;

  _74245 _74245_1 (
    .pin1(1'b1), .pin2(in_81), .pin3(in_80), .pin4(in_79), .pin5(in_78), .pin6(in_77), .pin7(in_76),
    .pin8(in_75), .pin9(in_74), .pin10(1'b0), .pin11(Sig8), .pin12(Sig9), .pin13(Sig10), .pin14(Sig11),
    .pin15(Sig12), .pin16(Sig13), .pin17(Sig14), .pin18(Sig15), .pin19(busOut), .pin20(1'b1));
  LED Bus15 (.in(Sig15));
  LED Bus13 (.in(Sig13));
  LED Bus14 (.in(Sig14));
  LED Bus11 (.in(Sig11));
  LED Bus12 (.in(Sig12));
  LED Bus9 (.in(Sig9));
  LED Bus10 (.in(Sig10));
  LED Bus8 (.in(Sig8));
  _74245 _74245_2 (
    .pin1(1'b1), .pin2(in_90), .pin3(in_89), .pin4(in_88), .pin5(in_87), .pin6(in_86), .pin7(in_85),
    .pin8(in_84), .pin9(in_83), .pin10(1'b0), .pin11(Sig0), .pin12(Sig1), .pin13(Sig2), .pin14(Sig3),
    .pin15(Sig4), .pin16(Sig5), .pin17(Sig6), .pin18(Sig7), .pin19(busOut), .pin20(1'b1));
  LED Bus7 (.in(Sig7));
  LED Bus5 (.in(Sig5));
  LED Bus6 (.in(Sig6));
  LED Bus3 (.in(Sig3));
  LED Bus4 (.in(Sig4));
  LED Bus1 (.in(Sig1));
  LED Bus2 (.in(Sig2));
  LED Bus0 (.in(Sig0));
  _74245 HighHigh (
    .pin1(RAMOut), .pin2(Sig15), .pin3(Sig14), .pin4(Sig13), .pin5(Sig12), .pin6(Sig11), .pin7(Sig10),
    .pin8(Sig9), .pin9(Sig8), .pin10(1'b0), .pin11(Databus8), .pin12(Databus9), .pin13(Databus10),
    .pin14(Databus11), .pin15(Databus12), .pin16(Databus13), .pin17(Databus14), .pin18(Databus15),
    .pin19(HighHighEn), .pin20(1'b1));
  _74245 LowLow (
    .pin1(RAMOut), .pin2(Sig7), .pin3(Sig6), .pin4(Sig5), .pin5(Sig4), .pin6(Sig3), .pin7(Sig2), .pin8(Sig1),
    .pin9(Sig0), .pin10(1'b0), .pin11(Databus0), .pin12(Databus1), .pin13(Databus2), .pin14(Databus3),
    .pin15(Databus4), .pin16(Databus5), .pin17(Databus6), .pin18(Databus7), .pin19(LowLowEn), .pin20(1'b1));
  _74245 HighLow (
    .pin1(RAMOut), .pin2(Sig15), .pin3(Sig14), .pin4(Sig13), .pin5(Sig12), .pin6(Sig11), .pin7(Sig10),
    .pin8(Sig9), .pin9(Sig8), .pin10(1'b0), .pin11(Databus0), .pin12(Databus1), .pin13(Databus2),
    .pin14(Databus3), .pin15(Databus4), .pin16(Databus5), .pin17(Databus6), .pin18(Databus7),
    .pin19(HighLowEn), .pin20(1'b1));
  _74245 LowHigh (
    .pin1(RAMOut), .pin2(Sig7), .pin3(Sig6), .pin4(Sig5), .pin5(Sig4), .pin6(Sig3), .pin7(Sig2), .pin8(Sig1),
    .pin9(Sig0), .pin10(1'b0), .pin11(Databus8), .pin12(Databus9), .pin13(Databus10), .pin14(Databus11),
    .pin15(Databus12), .pin16(Databus13), .pin17(Databus14), .pin18(Databus15), .pin19(LowHighEn),
    .pin20(1'b1));
  // _28c256 _28c256_1: pin names not known; wires that end beside it: LOWADDR15, LOWADDR13, LOWADDR8, LOWADDR7, LOWADDR6, LOWADDR5, LOWADDR4, LOWADDR3, LOWADDR2, LOWADDR1, Databus0, 1'b1, 1'b1, LOWADDR14, LOWADDR9, LOWADDR10, LOWADDR12, RAMOut, LOWADDR11, FLASH, Databus7
  // _28c256 _28c256_2: pin names not known; wires that end beside it: Databus1, Databus2, 1'b0, BusAIn15, BusAIn13, BusAIn8, BusAIn7, BusAIn6, BusAIn5, BusAIn4, BusAIn3, BusAIn2, BusAIn1, Databus8, Databus9, Databus10, 1'b0, Databus5, Databus4, Databus3, 1'b1, 1'b1, BusAIn14, BusAIn9, BusAIn10, BusAIn12, RAMOut, BusAIn11, FLASH, Databus15
  _74283 _74283_1 (
    .pin1(LOWADDR14), .pin2(1'b0), .pin3(BusAIn14), .pin4(LOWADDR13), .pin5(BusAIn13), .pin6(1'b0),
    .pin7(_74283_1_pin7), .pin8(1'b0), .pin11(1'b0), .pin12(1'b0), .pin13(LOWADDR15), .pin14(BusAIn15),
    .pin15(1'b0), .pin16(1'b1));  // open: pin9, pin10
  _74283 _74283_2 (
    .pin1(LOWADDR10), .pin2(1'b0), .pin3(BusAIn10), .pin4(LOWADDR9), .pin5(BusAIn9), .pin6(1'b0),
    .pin7(_74283_2_pin7), .pin8(1'b0), .pin9(_74283_1_pin7), .pin10(LOWADDR12), .pin11(1'b0),
    .pin12(BusAIn12), .pin13(LOWADDR11), .pin14(BusAIn11), .pin15(1'b0), .pin16(1'b1));
  _74283 _74283_3 (
    .pin1(LOWADDR6), .pin2(1'b0), .pin3(BusAIn6), .pin4(LOWADDR5), .pin5(BusAIn5), .pin6(1'b0),
    .pin7(_74283_3_pin7), .pin8(1'b0), .pin9(_74283_2_pin7), .pin10(LOWADDR8), .pin11(1'b0), .pin12(BusAIn8),
    .pin13(LOWADDR7), .pin14(BusAIn7), .pin15(1'b0), .pin16(1'b1));
  _74283 _74283_4 (
    .pin1(LOWADDR2), .pin2(1'b0), .pin3(BusAIn2), .pin4(LOWADDR1), .pin5(BusAIn1), .pin6(1'b0),
    .pin7(BusAIn0), .pin8(1'b0), .pin9(_74283_3_pin7), .pin10(LOWADDR4), .pin11(1'b0), .pin12(BusAIn4),
    .pin13(LOWADDR3), .pin14(BusAIn3), .pin15(1'b0), .pin16(1'b1));
  not not_1 (not_1_out, BusAIn0);
  and and_1 (HighHighEn, or_1_out, or_3_out);
  or or_1 (or_1_out, BusAIn0, and_10_out);
  and and_2 (and_2_out, BusAIn15, BusAIn14, BusAIn13, BusAIn12);
  and and_3 (and_3_out, BusAIn15, BusAIn14, BusAIn13, not_2_out);
  not not_2 (not_2_out, BusAIn12);
  and and_4 (LowLowEn, or_1_out, or_5_out);
  or or_2 (or_2_out, not_1_out, and_10_out);
  LED led_1 (.in(xor_1_out));
  and and_5 (and_5_out, RAMInH, xor_1_out);
  xor xor_1 (xor_1_out, and_6_out, RAMOut);
  and and_6 (and_6_out, RAMInH, RAMInL);
  and and_7 (HighLowEn, or_2_out, or_4_out);
  or or_3 (or_3_out, BusAIn0, and_8_out);
  and and_8 (and_8_out, RAMInL, xor_1_out);
  nor nor_1 (nor_1_out, and_2_out, and_3_out);
  and and_9 (LowHighEn, or_2_out, or_6_out);
  or or_4 (or_4_out, not_1_out, and_8_out);
  and and_10 (and_10_out, RAMOut, xor_1_out);
  not not_3 (SRAM, and_2_out);
  not not_4 (PREF, and_3_out);
  or or_5 (or_5_out, BusAIn0, and_5_out);
  not not_5 (FLASH, nor_1_out);
  or or_6 (or_6_out, not_1_out, and_5_out);

  // Notes on the sheet:
  //   RAMInH: default 1
  //   RAMInL: default 1
  //   RAMOut: default 1
  //   busOut: default 1
  //   ODD ADDR
endmodule
