// Digital circuit 16BitRAMControl.dig as structural Verilog
module _16BitRAMControl (
  input  BusAIn0,
  input  RAMInH,
  input  RAMInL,
  input  RAMOut,
  input  BusAIn1,
  input  BusAIn2,
  input  BusAIn3,
  input  BusAIn4,
  input  BusAIn5,
  input  BusAIn6,
  input  BusAIn7,
  input  BusAIn8,
  input  BusAIn9,
  input  BusAIn10,
  input  BusAIn11,
  input  BusAIn12,
  input  BusAIn13,
  input  BusAIn14,
  input  BusAIn15,
  output SRAM,
  output FLASH,
  output PREF,
  output LowIn,
  output HighIn,
  output RAMIn,
  output Out,
  output LOWADDR1,
  output LOWADDR2,
  output LOWADDR3,
  output LOWADDR4,
  output LOWADDR5,
  output LOWADDR6,
  output LOWADDR7,
  output LOWADDR8,
  output LOWADDR9,
  output LOWADDR10,
  output LOWADDR11,
  output LOWADDR12,
  output LOWADDR13,
  output LOWADDR14,
  output LOWADDR15,
  output HighHighEn,
  output LowLowEn,
  output HighLowEn,
  output LowHighEn
);

  wire _74283_1_pin7, _74283_2_pin7, _74283_3_pin7, and_1_out, and_3_out, not_1_out, not_3_out, not_5_out,
       not_6_out, or_3_out, or_6_out, or_7_out, or_8_out, or_9_out, or_10_out, or_11_out, xor_1_out;

  _74283 _74283_1 (
    .pin1(LOWADDR14), .pin2(1'b0), .pin3(BusAIn14), .pin4(LOWADDR13), .pin5(BusAIn13), .pin6(1'b0),
    .pin7(_74283_1_pin7), .pin8(1'b0), .pin11(1'b0), .pin12(1'b0), .pin13(LOWADDR15), .pin14(BusAIn15),
    .pin15(1'b0), .pin16(1'b1));  // open: pin9, pin10
  _74283 _74283_2 (
    .pin1(LOWADDR10), .pin2(1'b0), .pin3(BusAIn10), .pin4(LOWADDR9), .pin5(BusAIn9), .pin6(1'b0),
    .pin7(_74283_2_pin7), .pin8(1'b0), .pin9(_74283_1_pin7), .pin10(LOWADDR12), .pin11(1'b0),
    .pin12(BusAIn12), .pin13(LOWADDR11), .pin14(BusAIn11), .pin15(1'b0), .pin16(1'b1));
  _74283 _74283_3 (
    .pin1(LOWADDR6), .pin2(1'b0), .pin3(BusAIn6), .pin4(LOWADDR5), .pin5(BusAIn5), .pin6(1'b0),
    .pin7(_74283_3_pin7), .pin8(1'b0), .pin9(_74283_2_pin7), .pin10(LOWADDR8), .pin11(1'b0), .pin12(BusAIn8),
    .pin13(LOWADDR7), .pin14(BusAIn7), .pin15(1'b0), .pin16(1'b1));
  _74283 _74283_4 (
    .pin1(LOWADDR2), .pin2(1'b0), .pin3(BusAIn2), .pin4(LOWADDR1), .pin5(BusAIn1), .pin6(1'b0),
    .pin7(BusAIn0), .pin8(1'b0), .pin9(_74283_3_pin7), .pin10(LOWADDR4), .pin11(1'b0), .pin12(BusAIn4),
    .pin13(LOWADDR3), .pin14(BusAIn3), .pin15(1'b0), .pin16(1'b1));
  not not_1 (not_1_out, BusAIn0);
  and and_1 (and_1_out, BusAIn15, BusAIn14, BusAIn13, BusAIn12);
  or or_1 (LowIn, RAMInH, not_5_out);
  and and_2 (RAMIn, RAMInH, RAMInL);
  or or_2 (FLASH, or_3_out, not_5_out);
  not not_2 (SRAM, and_1_out);
  or or_3 (or_3_out, and_1_out, and_3_out);
  or or_4 (HighIn, RAMInL, not_5_out);
  xor xor_1 (xor_1_out, RAMIn, or_3_out);
  not not_3 (not_3_out, RAMIn);
  not not_4 (PREF, and_3_out);
  and and_3 (and_3_out, BusAIn15, BusAIn14, BusAIn13, not_6_out);
  not not_5 (not_5_out, xor_1_out);
  or or_5 (Out, not_3_out, RAMOut);
  not not_6 (not_6_out, BusAIn12);
  and and_4 (HighHighEn, or_6_out, or_8_out);
  or or_6 (or_6_out, BusAIn0, Out);
  and and_5 (LowLowEn, or_6_out, or_10_out);
  or or_7 (or_7_out, not_1_out, Out);
  and and_6 (HighLowEn, or_7_out, or_9_out);
  or or_8 (or_8_out, BusAIn0, HighIn);
  and and_7 (LowHighEn, or_7_out, or_11_out);
  or or_9 (or_9_out, not_1_out, HighIn);
  or or_10 (or_10_out, BusAIn0, LowIn);
  or or_11 (or_11_out, not_1_out, LowIn);

  // Notes on the sheet:
  //   RAMInH: default 1
  //   RAMInL: default 1
  //   RAMOut: default 1
endmodule
