// Digital circuit 16BitRAMTemp.dig as structural Verilog
module _16BitRAMTemp (
  input  RAMInH,
  input  RAMInL,
  input  RAMOut,
  input  [15:0] ADDRin,
  input  in_25,
  input  in_26,
  input  in_27,
  input  in_28,
  input  in_29,
  input  in_30,
  input  in_31,
  input  in_32,
  input  busOut,
  input  in_34,
  input  in_35,
  input  in_36,
  input  in_37,
  input  in_38,
  input  in_39,
  input  in_40,
  input  in_41,
  output Sig15,
  output Sig14,
  output Sig13,
  output Sig12,
  output Sig11,
  output Sig10,
  output Sig9,
  output Sig8,
  output Sig7,
  output Sig6,
  output Sig5,
  output Sig4,
  output Sig3,
  output Sig2,
  output Sig1,
  output Sig0,
  output SRAM,
  output FLASH,
  output PREF,
  output [15:0] Display
);

  wire _74283_1_pin7, _74283_2_pin7, _74283_3_pin7, and_1_out, and_2_out, and_3_out, and_4_out, and_5_out,
       Direction, nHighToHighEnable, nHighToLowEnable, nLowToHighEnable, nLowToLowEnable, nor_1_out,
       not_1_out, not_2_out, not_3_out, not_7_out, or_1_out, or_7_out, or_8_out, or_9_out, or_10_out,
       or_11_out, or_12_out, xor_1_out;
  wire [2:0] _74283_1_pin13;
  wire [3:0] _74283_2_pin10, _74283_3_pin10, _74283_4_pin10;

  _74245 _74245_1 (
    .pin1(1'b1), .pin2(in_32), .pin3(in_31), .pin4(in_30), .pin5(in_29), .pin6(in_28), .pin7(in_27),
    .pin8(in_26), .pin9(in_25), .pin10(1'b0), .pin11(Sig7), .pin12(Sig6), .pin13(Sig5), .pin14(Sig4),
    .pin15(Sig3), .pin16(Sig2), .pin17(Sig1), .pin18(Sig0), .pin19(busOut), .pin20(1'b1));
  _74245 _74245_2 (
    .pin1(1'b1), .pin2(in_41), .pin3(in_40), .pin4(in_39), .pin5(in_38), .pin6(in_37), .pin7(in_36),
    .pin8(in_35), .pin9(in_34), .pin10(1'b0), .pin11(Sig15), .pin12(Sig14), .pin13(Sig13), .pin14(Sig12),
    .pin15(Sig11), .pin16(Sig10), .pin17(Sig9), .pin18(Sig8), .pin19(busOut), .pin20(1'b1));
  _74245 HighToHigh (
    .pin1(Direction), .pin2(Sig15), .pin3(Sig14), .pin4(Sig13), .pin5(Sig12), .pin6(Sig11), .pin7(Sig10),
    .pin8(Sig9), .pin9(Sig8), .pin10(1'b0), .pin11(Display[8]), .pin12(Display[9]), .pin13(Display[10]),
    .pin14(Display[11]), .pin15(Display[12]), .pin16(Display[13]), .pin17(Display[14]), .pin18(Display[15]),
    .pin19(nHighToHighEnable), .pin20(1'b1));
  _74245 HighToLow (
    .pin1(Direction), .pin2(Sig7), .pin3(Sig6), .pin4(Sig5), .pin5(Sig4), .pin6(Sig3), .pin7(Sig2),
    .pin8(Sig1), .pin9(Sig0), .pin10(1'b0), .pin11(Display[8]), .pin12(Display[9]), .pin13(Display[10]),
    .pin14(Display[11]), .pin15(Display[12]), .pin16(Display[13]), .pin17(Display[14]), .pin18(Display[15]),
    .pin19(nHighToLowEnable), .pin20(1'b1));
  _74245 LowToHigh (
    .pin1(Direction), .pin2(Sig15), .pin3(Sig14), .pin4(Sig13), .pin5(Sig12), .pin6(Sig11), .pin7(Sig10),
    .pin8(Sig9), .pin9(Sig8), .pin10(1'b0), .pin11(Display[0]), .pin12(Display[1]), .pin13(Display[2]),
    .pin14(Display[3]), .pin15(Display[4]), .pin16(Display[5]), .pin17(Display[6]), .pin18(Display[7]),
    .pin19(nLowToHighEnable), .pin20(1'b1));
  _74245 LowToLow (
    .pin1(Direction), .pin2(Sig7), .pin3(Sig6), .pin4(Sig5), .pin5(Sig4), .pin6(Sig3), .pin7(Sig2),
    .pin8(Sig1), .pin9(Sig0), .pin10(1'b0), .pin11(Display[0]), .pin12(Display[1]), .pin13(Display[2]),
    .pin14(Display[3]), .pin15(Display[4]), .pin16(Display[5]), .pin17(Display[6]), .pin18(Display[7]),
    .pin19(nLowToLowEnable), .pin20(1'b1));
  _16BitProgramHighROM _16bitprogramhighrom_1 (
    .nCE(FLASH), .nOE(Direction), .nWE(1'b1), .VCC(1'b1), .GND(1'b0), .I_O0(Display[8]), .I_O1(Display[9]),
    .I_O2(Display[10]), .I_O3(Display[11]), .I_O4(Display[12]), .I_O5(Display[13]), .I_O6(Display[14]),
    .I_O7(Display[15]), .A0(_74283_4_pin10[0]), .A1(_74283_4_pin10[1]), .A2(_74283_4_pin10[2]),
    .A3(_74283_4_pin10[3]), .A4(_74283_3_pin10[0]), .A5(_74283_3_pin10[1]), .A6(_74283_3_pin10[2]),
    .A7(_74283_3_pin10[3]), .A8(_74283_2_pin10[0]), .A9(_74283_2_pin10[1]), .A10(_74283_2_pin10[2]),
    .A11(_74283_2_pin10[3]), .A12(_74283_1_pin13[0]), .A13(_74283_1_pin13[1]), .A14(_74283_1_pin13[2]));
  _16BitProgramLowROM _16bitprogramlowrom_1 (
    .nCE(FLASH), .nOE(Direction), .nWE(1'b1), .VCC(1'b1), .GND(1'b0), .I_O0(Display[0]), .I_O1(Display[1]),
    .I_O2(Display[2]), .I_O3(Display[3]), .I_O4(Display[4]), .I_O5(Display[5]), .I_O6(Display[6]),
    .I_O7(Display[7]), .A0(ADDRin[1]), .A1(ADDRin[2]), .A2(ADDRin[3]), .A3(ADDRin[4]), .A4(ADDRin[5]),
    .A5(ADDRin[6]), .A6(ADDRin[7]), .A7(ADDRin[8]), .A8(ADDRin[9]), .A9(ADDRin[10]), .A10(ADDRin[11]),
    .A11(ADDRin[12]), .A12(ADDRin[13]), .A13(ADDRin[14]), .A14(ADDRin[15]));
  _16BitRamA _16bitrama_1 (
    .A0(_74283_4_pin10[0]), .A1(_74283_4_pin10[1]), .A2(_74283_4_pin10[2]), .A3(_74283_4_pin10[3]),
    .A4(_74283_3_pin10[0]), .A5(_74283_3_pin10[1]), .A6(_74283_3_pin10[2]), .A7(_74283_3_pin10[3]),
    .A8(_74283_2_pin10[0]), .A9(_74283_2_pin10[1]), .A10(_74283_2_pin10[2]), .A11(_74283_2_pin10[3]),
    .A12(1'b0), .nCE(SRAM), .nOE(Direction), .nWE(or_9_out), .D0(Display[8]), .D1(Display[9]),
    .D2(Display[10]), .D3(Display[11]), .D4(Display[12]), .D5(Display[13]), .D6(Display[14]),
    .D7(Display[15]), .VCC(1'b1), .GND(1'b0));
  _16BitRamB _16bitramb_1 (
    .A0(ADDRin[1]), .A1(ADDRin[2]), .A2(ADDRin[3]), .A3(ADDRin[4]), .A4(ADDRin[5]), .A5(ADDRin[6]),
    .A6(ADDRin[7]), .A7(ADDRin[8]), .A8(ADDRin[9]), .A9(ADDRin[10]), .A10(ADDRin[11]), .A11(ADDRin[12]),
    .A12(1'b0), .nCE(SRAM), .nOE(Direction), .nWE(or_11_out), .D0(Display[0]), .D1(Display[1]),
    .D2(Display[2]), .D3(Display[3]), .D4(Display[4]), .D5(Display[5]), .D6(Display[6]), .D7(Display[7]),
    .VCC(1'b1), .GND(1'b0));
  _74283 _74283_1 (
    .pin1(_74283_1_pin13[1]), .pin2(1'b0), .pin3(ADDRin[14]), .pin4(_74283_1_pin13[0]), .pin5(ADDRin[13]),
    .pin6(1'b0), .pin7(_74283_1_pin7), .pin8(1'b0), .pin11(1'b0), .pin12(1'b0), .pin13(_74283_1_pin13[2]),
    .pin14(ADDRin[15]), .pin15(1'b0), .pin16(1'b1));  // open: pin9, pin10
  _74283 _74283_2 (
    .pin1(_74283_2_pin10[1]), .pin2(1'b0), .pin3(ADDRin[10]), .pin4(_74283_2_pin10[0]), .pin5(ADDRin[9]),
    .pin6(1'b0), .pin7(_74283_2_pin7), .pin8(1'b0), .pin9(_74283_1_pin7), .pin10(_74283_2_pin10[3]),
    .pin11(1'b0), .pin12(ADDRin[12]), .pin13(_74283_2_pin10[2]), .pin14(ADDRin[11]), .pin15(1'b0),
    .pin16(1'b1));
  _74283 _74283_3 (
    .pin1(_74283_3_pin10[1]), .pin2(1'b0), .pin3(ADDRin[6]), .pin4(_74283_3_pin10[0]), .pin5(ADDRin[5]),
    .pin6(1'b0), .pin7(_74283_3_pin7), .pin8(1'b0), .pin9(_74283_2_pin7), .pin10(_74283_3_pin10[3]),
    .pin11(1'b0), .pin12(ADDRin[8]), .pin13(_74283_3_pin10[2]), .pin14(ADDRin[7]), .pin15(1'b0), .pin16(1'b1));
  _74283 _74283_4 (
    .pin1(_74283_4_pin10[1]), .pin2(1'b0), .pin3(ADDRin[2]), .pin4(_74283_4_pin10[0]), .pin5(ADDRin[1]),
    .pin6(1'b0), .pin7(ADDRin[0]), .pin8(1'b0), .pin9(_74283_3_pin7), .pin10(_74283_4_pin10[3]),
    .pin11(1'b0), .pin12(ADDRin[4]), .pin13(_74283_4_pin10[2]), .pin14(ADDRin[3]), .pin15(1'b0), .pin16(1'b1));
  not not_1 (not_1_out, ADDRin[0]);
  not not_2 (not_2_out, ADDRin[12]);
  and and_1 (and_1_out, ADDRin[15], ADDRin[14], ADDRin[13], ADDRin[12]);
  and and_2 (and_2_out, ADDRin[15], ADDRin[14], ADDRin[13], not_2_out);
  or or_1 (or_1_out, and_3_out, not_3_out);
  and and_3 (and_3_out, RAMInH, RAMInL);
  nor nor_1 (nor_1_out, and_1_out, and_2_out);
  // Or or_2 has open pins: In_1=and_3_out, In_2=RAMOut, out=open
  not not_3 (not_3_out, RAMOut);
  not not_4 (SRAM, and_1_out);
  not not_5 (FLASH, nor_1_out);
  not not_6 (PREF, and_2_out);
  not not_7 (not_7_out, xor_1_out);
  xor xor_1 (xor_1_out, and_3_out, RAMOut);
  or or_3 (nHighToHighEnable, not_7_out, ADDRin[0]);
  or or_4 (nLowToLowEnable, not_7_out, ADDRin[0]);
  or or_5 (nLowToHighEnable, not_7_out, not_1_out);
  or or_6 (nHighToLowEnable, not_7_out, not_1_out);
  not not_8 (Direction, or_1_out);
  or or_7 (or_7_out, RAMInH, nHighToHighEnable);
  or or_8 (or_8_out, RAMInL, nLowToHighEnable);
  and and_4 (and_4_out, or_8_out, or_7_out);
  or or_9 (or_9_out, SRAM, and_4_out);
  or or_10 (or_10_out, RAMInL, nLowToLowEnable);
  and and_5 (and_5_out, or_12_out, or_10_out);
  or or_11 (or_11_out, SRAM, and_5_out);
  or or_12 (or_12_out, RAMInH, nHighToLowEnable);

  // Notes on the sheet:
  //   RAMInH: default 1
  //   RAMInL: default 1
  //   RAMOut: default 1
  //   ADDRin: default 61440
  //   busOut: default 1
  //   ODD ADDR
  //   High
  //   Low
endmodule
