// Digital circuit 16BitRAMTemp2.dig as structural Verilog
module _16BitRAMTemp2 (
  input  in_1,
  input  in_2,
  input  in_3,
  input  in_4,
  input  in_5,
  input  in_6,
  input  in_7,
  input  in_8,
  input  busOut,
  input  in_10,
  input  in_11,
  input  in_12,
  input  in_13,
  input  in_14,
  input  in_15,
  input  in_16,
  input  in_17,
  input  addr0,
  input  addr1,
  input  addr2,
  input  nCE,
  input  nOE,
  input  nWE
);

  wire _74245_1_pin11, _74245_1_pin12, _74245_1_pin13, _74245_1_pin14, _74245_1_pin15, _74245_1_pin16,
       _74245_1_pin17, _74245_1_pin18, _74245_2_pin11, _74245_2_pin12, _74245_2_pin13, _74245_2_pin14,
       _74245_2_pin15, _74245_2_pin16, _74245_2_pin17, _74245_2_pin18;

  _74245 _74245_1 (
    .pin1(1'b1), .pin2(in_8), .pin3(in_7), .pin4(in_6), .pin5(in_5), .pin6(in_4), .pin7(in_3), .pin8(in_2),
    .pin9(in_1), .pin10(1'b0), .pin11(_74245_1_pin11), .pin12(_74245_1_pin12), .pin13(_74245_1_pin13),
    .pin14(_74245_1_pin14), .pin15(_74245_1_pin15), .pin16(_74245_1_pin16), .pin17(_74245_1_pin17),
    .pin18(_74245_1_pin18), .pin19(busOut), .pin20(1'b1));
  _74245 _74245_2 (
    .pin1(1'b1), .pin2(in_17), .pin3(in_16), .pin4(in_15), .pin5(in_14), .pin6(in_13), .pin7(in_12),
    .pin8(in_11), .pin9(in_10), .pin10(1'b0), .pin11(_74245_2_pin11), .pin12(_74245_2_pin12),
    .pin13(_74245_2_pin13), .pin14(_74245_2_pin14), .pin15(_74245_2_pin15), .pin16(_74245_2_pin16),
    .pin17(_74245_2_pin17), .pin18(_74245_2_pin18), .pin19(busOut), .pin20(1'b1));
  _16BitRamA _16bitrama_1 (
    .A0(addr0), .A1(addr1), .A2(addr2), .A3(1'b0), .A4(1'b0), .A5(1'b0), .A6(1'b0), .A7(1'b0), .A8(1'b0),
    .A9(1'b0), .A10(1'b0), .A11(1'b0), .A12(1'b0), .nCE(nCE), .nOE(nOE), .nWE(nWE), .D0(_74245_2_pin18),
    .D1(_74245_2_pin17), .D2(_74245_2_pin16), .D3(_74245_2_pin15), .D4(_74245_2_pin14), .D5(_74245_2_pin13),
    .D6(_74245_2_pin12), .D7(_74245_2_pin11), .VCC(1'b1), .GND(1'b0));
  _16BitRamB _16bitramb_1 (
    .A0(addr0), .A1(addr1), .A2(addr2), .A3(1'b0), .A4(1'b0), .A5(1'b0), .A6(1'b0), .A7(1'b0), .A8(1'b0),
    .A9(1'b0), .A10(1'b0), .A11(1'b0), .A12(1'b0), .nCE(nCE), .nOE(nOE), .nWE(nWE), .D0(_74245_1_pin18),
    .D1(_74245_1_pin17), .D2(_74245_1_pin16), .D3(_74245_1_pin15), .D4(_74245_1_pin14), .D5(_74245_1_pin13),
    .D6(_74245_1_pin12), .D7(_74245_1_pin11), .VCC(1'b1), .GND(1'b0));

  // Notes on the sheet:
  //   busOut: default 1
  //   nOE: default 1
endmodule
