// Digital circuit 16BitRegister.dig as structural Verilog
module _16BitRegister (
  input  in_1,
  input  in_2,
  input  in_3,
  input  in_4,
  input  in_5,
  input  in_6,
  input  in_7,
  input  in_8,
  input  busOut,
  input  in_10,
  input  in_11,
  input  in_12,
  input  in_13,
  input  in_14,
  input  in_15,
  input  in_16,
  input  in_17,
  input  RegOut,
  input  RegIn,
  input  Clock,
  input  Reset
);

  wire _16bitregisterint_1_sig0, _16bitregisterint_1_sig1, _16bitregisterint_1_sig2,
       _16bitregisterint_1_sig3, _16bitregisterint_1_sig4, _16bitregisterint_1_sig5,
       _16bitregisterint_1_sig6, _16bitregisterint_1_sig7, _16bitregisterint_1_sig8,
       _16bitregisterint_1_sig9, _16bitregisterint_1_sig10, _16bitregisterint_1_sig11,
       _16bitregisterint_1_sig12, _16bitregisterint_1_sig13, _16bitregisterint_1_sig14,
       _16bitregisterint_1_sig15, _74245_1_pin11, _74245_1_pin12, _74245_1_pin13, _74245_1_pin14,
       _74245_1_pin15, _74245_1_pin16, _74245_1_pin17, _74245_1_pin18, _74245_2_pin11, _74245_2_pin12,
       _74245_2_pin13, _74245_2_pin14, _74245_2_pin15, _74245_2_pin16, _74245_2_pin17, _74245_2_pin18;

  _74245 _74245_1 (
    .pin1(1'b1), .pin2(in_8), .pin3(in_7), .pin4(in_6), .pin5(in_5), .pin6(in_4), .pin7(in_3), .pin8(in_2),
    .pin9(in_1), .pin10(1'b0), .pin11(_74245_1_pin11), .pin12(_74245_1_pin12), .pin13(_74245_1_pin13),
    .pin14(_74245_1_pin14), .pin15(_74245_1_pin15), .pin16(_74245_1_pin16), .pin17(_74245_1_pin17),
    .pin18(_74245_1_pin18), .pin19(busOut), .pin20(1'b1));
  LED Bus14 (.in(_74245_1_pin17));
  LED Bus15 (.in(_74245_1_pin18));
  LED Bus12 (.in(_74245_1_pin15));
  LED Bus13 (.in(_74245_1_pin16));
  LED Bus10 (.in(_74245_1_pin13));
  LED Bus11 (.in(_74245_1_pin14));
  LED Bus8 (.in(_74245_1_pin11));
  LED Bus9 (.in(_74245_1_pin12));
  _74245 _74245_2 (
    .pin1(1'b1), .pin2(in_17), .pin3(in_16), .pin4(in_15), .pin5(in_14), .pin6(in_13), .pin7(in_12),
    .pin8(in_11), .pin9(in_10), .pin10(1'b0), .pin11(_74245_2_pin11), .pin12(_74245_2_pin12),
    .pin13(_74245_2_pin13), .pin14(_74245_2_pin14), .pin15(_74245_2_pin15), .pin16(_74245_2_pin16),
    .pin17(_74245_2_pin17), .pin18(_74245_2_pin18), .pin19(busOut), .pin20(1'b1));
  LED Bus6 (.in(_74245_2_pin17));
  LED Bus7 (.in(_74245_2_pin18));
  LED Bus4 (.in(_74245_2_pin15));
  LED Bus5 (.in(_74245_2_pin16));
  LED Bus2 (.in(_74245_2_pin13));
  LED Bus3 (.in(_74245_2_pin14));
  LED Bus0 (.in(_74245_2_pin11));
  LED Bus1 (.in(_74245_2_pin12));
  _16BitRegisterInt _16bitregisterint_1 (
    .RegOut(RegOut), .RegIn(RegIn), .Clock(Clock), .Reset(Reset), .BusIn0(_74245_2_pin11),
    .BusIn1(_74245_2_pin12), .BusIn2(_74245_2_pin13), .BusIn3(_74245_2_pin14), .BusIn4(_74245_2_pin15),
    .BusIn5(_74245_2_pin16), .BusIn6(_74245_2_pin17), .BusIn7(_74245_2_pin18), .BusIn8(_74245_1_pin11),
    .BusIn9(_74245_1_pin12), .BusIn10(_74245_1_pin13), .BusIn11(_74245_1_pin14), .BusIn12(_74245_1_pin15),
    .BusIn13(_74245_1_pin16), .BusIn14(_74245_1_pin17), .BusIn15(_74245_1_pin18),
    .Sig15(_16bitregisterint_1_sig15), .Sig14(_16bitregisterint_1_sig14), .Sig13(_16bitregisterint_1_sig13),
    .Sig12(_16bitregisterint_1_sig12), .Sig11(_16bitregisterint_1_sig11), .Sig10(_16bitregisterint_1_sig10),
    .Sig9(_16bitregisterint_1_sig9), .Sig8(_16bitregisterint_1_sig8), .Sig7(_16bitregisterint_1_sig7),
    .Sig6(_16bitregisterint_1_sig6), .Sig5(_16bitregisterint_1_sig5), .Sig4(_16bitregisterint_1_sig4),
    .Sig3(_16bitregisterint_1_sig3), .Sig2(_16bitregisterint_1_sig2), .Sig1(_16bitregisterint_1_sig1),
    .Sig0(_16bitregisterint_1_sig0), .BusOut15(_74245_1_pin18), .BusOut14(_74245_1_pin17),
    .BusOut13(_74245_1_pin16), .BusOut12(_74245_1_pin15), .BusOut11(_74245_1_pin14),
    .BusOut10(_74245_1_pin13), .BusOut9(_74245_1_pin12), .BusOut8(_74245_1_pin11), .BusOut7(_74245_2_pin18),
    .BusOut6(_74245_2_pin17), .BusOut5(_74245_2_pin16), .BusOut4(_74245_2_pin15), .BusOut3(_74245_2_pin14),
    .BusOut2(_74245_2_pin13), .BusOut1(_74245_2_pin12), .BusOut0(_74245_2_pin11));
  LED Signal15 (.in(_16bitregisterint_1_sig15));
  LED Signal14 (.in(_16bitregisterint_1_sig14));
  LED Signal13 (.in(_16bitregisterint_1_sig13));
  LED Signal12 (.in(_16bitregisterint_1_sig12));
  LED Signal11 (.in(_16bitregisterint_1_sig11));
  LED Signal10 (.in(_16bitregisterint_1_sig10));
  LED Signal9 (.in(_16bitregisterint_1_sig9));
  LED Signal8 (.in(_16bitregisterint_1_sig8));
  LED Signal7 (.in(_16bitregisterint_1_sig7));
  LED Signal6 (.in(_16bitregisterint_1_sig6));
  LED Signal5 (.in(_16bitregisterint_1_sig5));
  LED Signal4 (.in(_16bitregisterint_1_sig4));
  LED Signal3 (.in(_16bitregisterint_1_sig3));
  LED Signal2 (.in(_16bitregisterint_1_sig2));
  LED Signal1 (.in(_16bitregisterint_1_sig1));
  LED Signal0 (.in(_16bitregisterint_1_sig0));

  // Notes on the sheet:
  //   busOut: default 1
  //   RegOut: default 1
  //   RegIn: default 1
endmodule
