// Digital circuit 16BitRegister2.dig as structural Verilog
module _16BitRegister2 (
  input  in_1,
  input  in_2,
  input  in_3,
  input  in_4,
  input  in_5,
  input  in_6,
  input  in_7,
  input  in_8,
  input  busOut,
  input  in_10,
  input  in_11,
  input  in_12,
  input  in_13,
  input  in_14,
  input  in_15,
  input  in_16,
  input  in_17,
  input  RegOut,
  input  RegIn,
  input  Clock,
  input  Reset
);

  wire _16bitregisterint2_1_p21, _16bitregisterint2_1_p22, _16bitregisterint2_1_p23,
       _16bitregisterint2_1_p24, _16bitregisterint2_1_p25, _16bitregisterint2_1_p26,
       _16bitregisterint2_1_p27, _16bitregisterint2_1_p28, _16bitregisterint2_1_p29,
       _16bitregisterint2_1_p30, _16bitregisterint2_1_p31, _16bitregisterint2_1_p32,
       _16bitregisterint2_1_p33, _16bitregisterint2_1_p34, _16bitregisterint2_1_p35,
       _16bitregisterint2_1_p36, _74245_1_pin11, _74245_1_pin12, _74245_1_pin13, _74245_1_pin14,
       _74245_1_pin15, _74245_1_pin16, _74245_1_pin17, _74245_1_pin18, _74245_2_pin11, _74245_2_pin12,
       _74245_2_pin13, _74245_2_pin14, _74245_2_pin15, _74245_2_pin16, _74245_2_pin17, _74245_2_pin18;

  _74245 _74245_1 (
    .pin1(1'b1), .pin2(in_8), .pin3(in_7), .pin4(in_6), .pin5(in_5), .pin6(in_4), .pin7(in_3), .pin8(in_2),
    .pin9(in_1), .pin10(1'b0), .pin11(_74245_1_pin11), .pin12(_74245_1_pin12), .pin13(_74245_1_pin13),
    .pin14(_74245_1_pin14), .pin15(_74245_1_pin15), .pin16(_74245_1_pin16), .pin17(_74245_1_pin17),
    .pin18(_74245_1_pin18), .pin19(busOut), .pin20(1'b1));
  LED Bus14 (.in(_74245_1_pin17));
  LED Bus15 (.in(_74245_1_pin18));
  LED Bus12 (.in(_74245_1_pin15));
  LED Bus13 (.in(_74245_1_pin16));
  LED Bus10 (.in(_74245_1_pin13));
  LED Bus11 (.in(_74245_1_pin14));
  LED Bus8 (.in(_74245_1_pin11));
  LED Bus9 (.in(_74245_1_pin12));
  _74245 _74245_2 (
    .pin1(1'b1), .pin2(in_17), .pin3(in_16), .pin4(in_15), .pin5(in_14), .pin6(in_13), .pin7(in_12),
    .pin8(in_11), .pin9(in_10), .pin10(1'b0), .pin11(_74245_2_pin11), .pin12(_74245_2_pin12),
    .pin13(_74245_2_pin13), .pin14(_74245_2_pin14), .pin15(_74245_2_pin15), .pin16(_74245_2_pin16),
    .pin17(_74245_2_pin17), .pin18(_74245_2_pin18), .pin19(busOut), .pin20(1'b1));
  LED Bus6 (.in(_74245_2_pin17));
  LED Bus7 (.in(_74245_2_pin18));
  LED Bus4 (.in(_74245_2_pin15));
  LED Bus5 (.in(_74245_2_pin16));
  LED Bus2 (.in(_74245_2_pin13));
  LED Bus3 (.in(_74245_2_pin14));
  LED Bus0 (.in(_74245_2_pin11));
  LED Bus1 (.in(_74245_2_pin12));
  // _16BitRegisterInt2 _16bitregisterint2_1: pin names not known; wires that end beside it: _74245_2_pin11, _74245_2_pin12, _74245_2_pin13, _74245_2_pin14, _74245_2_pin15, _74245_2_pin16, _74245_2_pin17, _74245_2_pin18, _74245_1_pin11, _74245_1_pin12, _74245_1_pin13, _74245_1_pin14, _74245_1_pin15, _74245_1_pin16, _74245_1_pin17, _74245_1_pin18, RegOut, RegIn, Clock, Reset, _16bitregisterint2_1_p21, _16bitregisterint2_1_p22, _16bitregisterint2_1_p23, _16bitregisterint2_1_p24, _16bitregisterint2_1_p25, _16bitregisterint2_1_p26, _16bitregisterint2_1_p27, _16bitregisterint2_1_p28, _16bitregisterint2_1_p29, _16bitregisterint2_1_p30, _16bitregisterint2_1_p31, _16bitregisterint2_1_p32, _16bitregisterint2_1_p33, _16bitregisterint2_1_p34, _16bitregisterint2_1_p35, _16bitregisterint2_1_p36
  LED Signal15 (.in(_16bitregisterint2_1_p21));
  LED Signal14 (.in(_16bitregisterint2_1_p22));
  LED Signal13 (.in(_16bitregisterint2_1_p23));
  LED Signal12 (.in(_16bitregisterint2_1_p24));
  LED Signal11 (.in(_16bitregisterint2_1_p25));
  LED Signal10 (.in(_16bitregisterint2_1_p26));
  LED Signal9 (.in(_16bitregisterint2_1_p27));
  LED Signal8 (.in(_16bitregisterint2_1_p28));
  LED Signal7 (.in(_16bitregisterint2_1_p29));
  LED Signal6 (.in(_16bitregisterint2_1_p30));
  LED Signal5 (.in(_16bitregisterint2_1_p31));
  LED Signal4 (.in(_16bitregisterint2_1_p32));
  LED Signal3 (.in(_16bitregisterint2_1_p33));
  LED Signal2 (.in(_16bitregisterint2_1_p34));
  LED Signal1 (.in(_16bitregisterint2_1_p35));
  LED Signal0 (.in(_16bitregisterint2_1_p36));

  // Notes on the sheet:
  //   busOut: default 1
  //   RegOut: default 1
  //   RegIn: default 1
endmodule
