// Digital circuit 16BitRegisterALU.dig as structural Verilog
module _16BitRegisterALU (
  input  in_1,
  input  in_2,
  input  in_3,
  input  in_4,
  input  in_5,
  input  in_6,
  input  in_7,
  input  in_8,
  input  busOut,
  input  in_10,
  input  in_11,
  input  in_12,
  input  in_13,
  input  in_14,
  input  in_15,
  input  in_16,
  input  in_17,
  input  RegIn,
  input  RegOut,
  input  Clock,
  input  Reset,
  input  nImc,
  input  nDec,
  input  RegIn_2,
  input  RegOut_2,
  input  nFlagOut
);

  wire _16bitdisplayint_1_p3, _16bitdisplayint_1_p6, _16bitdisplayint_1_p8, _16bitdisplayint_1_p11,
       _16bitdisplayint_1_p13, _16bitdisplayint_2_dec1, _16bitdisplayint_2_dec2, _16bitdisplayint_2_dec3,
       _16bitdisplayint_2_dec4, _16bitregisteraluint_1_p17, _16bitregisteraluint_1_p18,
       _16bitregisteraluint_1_p19, _16bitregisteraluint_1_p20, _74245_1_pin11, _74245_1_pin12,
       _74245_1_pin13, _74245_1_pin14, _74245_1_pin15, _74245_1_pin16, _74245_1_pin17, _74245_1_pin18,
       _74245_2_pin11, _74245_2_pin12, _74245_2_pin13, _74245_2_pin14, _74245_2_pin15, _74245_2_pin16,
       _74245_2_pin17, _74245_2_pin18;
  wire [3:0] _16bitdisplayint_1_p5, _16bitdisplayint_1_p7, _16bitdisplayint_1_p10, _16bitdisplayint_1_p12,
       _16bitdisplayint_2_digit1, _16bitdisplayint_2_digit2, _16bitdisplayint_2_digit3,
       _16bitdisplayint_2_digit4;
  wire [15:0] _16bitregistercounterint_1_p6;

  _74245 _74245_1 (
    .pin1(1'b1), .pin2(in_8), .pin3(in_7), .pin4(in_6), .pin5(in_5), .pin6(in_4), .pin7(in_3), .pin8(in_2),
    .pin9(in_1), .pin10(1'b0), .pin11(_74245_1_pin11), .pin12(_74245_1_pin12), .pin13(_74245_1_pin13),
    .pin14(_74245_1_pin14), .pin15(_74245_1_pin15), .pin16(_74245_1_pin16), .pin17(_74245_1_pin17),
    .pin18(_74245_1_pin18), .pin19(busOut), .pin20(1'b1));
  LED Bus14 (.in(_74245_1_pin17));
  LED Bus15 (.in(_74245_1_pin18));
  LED Bus12 (.in(_74245_1_pin15));
  LED Bus13 (.in(_74245_1_pin16));
  LED Bus10 (.in(_74245_1_pin13));
  LED Bus11 (.in(_74245_1_pin14));
  LED Bus8 (.in(_74245_1_pin11));
  LED Bus9 (.in(_74245_1_pin12));
  _74245 _74245_2 (
    .pin1(1'b1), .pin2(in_17), .pin3(in_16), .pin4(in_15), .pin5(in_14), .pin6(in_13), .pin7(in_12),
    .pin8(in_11), .pin9(in_10), .pin10(1'b0), .pin11(_74245_2_pin11), .pin12(_74245_2_pin12),
    .pin13(_74245_2_pin13), .pin14(_74245_2_pin14), .pin15(_74245_2_pin15), .pin16(_74245_2_pin16),
    .pin17(_74245_2_pin17), .pin18(_74245_2_pin18), .pin19(busOut), .pin20(1'b1));
  LED Bus6 (.in(_74245_2_pin17));
  LED Bus7 (.in(_74245_2_pin18));
  LED Bus4 (.in(_74245_2_pin15));
  LED Bus5 (.in(_74245_2_pin16));
  LED Bus2 (.in(_74245_2_pin13));
  LED Bus3 (.in(_74245_2_pin14));
  LED Bus0 (.in(_74245_2_pin11));
  LED Bus1 (.in(_74245_2_pin12));
  LED led_1 (.in(_16bitregisteraluint_1_p17));
  // _16BitRegisterALUint _16bitregisteraluint_1: pin names not known; wires that end beside it: _74245_1_pin18, _74245_1_pin17, _74245_1_pin16, _74245_1_pin15, _74245_1_pin14, _74245_1_pin13, _74245_1_pin12, _74245_1_pin11, _74245_2_pin18, _74245_2_pin17, _74245_2_pin16, _74245_2_pin15, _74245_2_pin14, _74245_2_pin13, _74245_2_pin12, _74245_2_pin11, _16bitregisteraluint_1_p17, _16bitregisteraluint_1_p18, _16bitregisteraluint_1_p19, _16bitregisteraluint_1_p20
  // _16BitRegisterCounterInt _16bitregistercounterint_1: pin names not known; wires that end beside it: RegOut_2, RegIn, RegIn_2, RegOut, Clock, _16bitregistercounterint_1_p6, Reset, nDec, nImc
  LED led_2 (.in(_16bitregisteraluint_1_p18));
  LED led_3 (.in(_16bitregisteraluint_1_p19));
  LED led_4 (.in(_16bitregisteraluint_1_p20));
  Seven_Seg_Hex seven_seg_hex_1 (.d(_16bitdisplayint_1_p5), .dp(_16bitdisplayint_1_p6));
  // _16BitDisplayInt _16bitdisplayint_1: pin names not known; wires that end beside it: Reset, nFlagOut, _16bitdisplayint_1_p3, _16bitregistercounterint_1_p6, _16bitdisplayint_1_p5, _16bitdisplayint_1_p6, _16bitdisplayint_1_p7, _16bitdisplayint_1_p8, _16bitdisplayint_1_p3, _16bitdisplayint_1_p10, _16bitdisplayint_1_p11, _16bitdisplayint_1_p12, _16bitdisplayint_1_p13
  Seven_Seg_Hex seven_seg_hex_2 (.d(_16bitdisplayint_2_digit4), .dp(_16bitdisplayint_2_dec4));
  _16BitDisplayInt _16bitdisplayint_2 (
    .Digit4(_16bitdisplayint_2_digit4), .Dec4(_16bitdisplayint_2_dec4), .Digit3(_16bitdisplayint_2_digit3),
    .Dec3(_16bitdisplayint_2_dec3), .Digit2(_16bitdisplayint_2_digit2), .Dec2(_16bitdisplayint_2_dec2),
    .Digit1(_16bitdisplayint_2_digit1), .Dec1(_16bitdisplayint_2_dec1), .Input(_16bitregistercounterint_1_p6));
  Seven_Seg_Hex seven_seg_hex_3 (.d(_16bitdisplayint_1_p7), .dp(_16bitdisplayint_1_p8));
  Seven_Seg_Hex seven_seg_hex_4 (.d(_16bitdisplayint_2_digit3), .dp(_16bitdisplayint_2_dec3));
  Seven_Seg_Hex seven_seg_hex_5 (.d(_16bitdisplayint_1_p10), .dp(_16bitdisplayint_1_p11));
  Seven_Seg_Hex seven_seg_hex_6 (.d(_16bitdisplayint_2_digit2), .dp(_16bitdisplayint_2_dec2));
  Seven_Seg_Hex seven_seg_hex_7 (.d(_16bitdisplayint_1_p12), .dp(_16bitdisplayint_1_p13));
  Seven_Seg_Hex seven_seg_hex_8 (.d(_16bitdisplayint_2_digit1), .dp(_16bitdisplayint_2_dec1));

  // Notes on the sheet:
  //   busOut: default 1
  //   RegIn: default 1
  //   RegOut: default 1
  //   nImc: default 1
  //   nDec: default 1
  //   RegIn_2: default 1
  //   RegOut_2: default 1
  //   nFlagOut: default 1
endmodule
