// Digital circuit 16BitRegisterALUint.dig as structural Verilog
module _16BitRegisterALUint (
  input  RegOut,
  input  RegIn,
  input  Clock,
  input  Reset,
  input  FlagiIn,
  input  [15:0] MainSig,
  output BusOut0,
  output BusOut1,
  output BusOut2,
  output BusOut3,
  output BusOut4,
  output BusOut5,
  output BusOut6,
  output BusOut7,
  output BusOut8,
  output BusOut9,
  output BusOut10,
  output BusOut11,
  output BusOut12,
  output BusOut13,
  output BusOut14,
  output BusOut15,
  output zeroOut,
  output carryOut,
  output zero,
  output carry,
  output [15:0] DispSig
);

  wire _74173_1_pin3, _74173_1_pin4, _74173_1_pin5, _74173_1_pin6, _74173_2_pin3, _74173_2_pin4,
       _74173_2_pin5, _74173_2_pin6, _74173_3_pin3, _74173_3_pin4, _74173_3_pin5, _74173_3_pin6,
       _74173_4_pin3, _74173_4_pin4, _74173_4_pin5, _74173_4_pin6, _74283_1_pin7, _74283_2_pin7,
       _74283_3_pin7, and_1_out, and_2_out, and_3_out, and_5_out, and_6_out, and_7_out, nor_1_out, nor_2_out,
       nor_3_out, nor_4_out, nor_5_out, nor_6_out, nor_7_out, nor_8_out, xor_1_out, xor_2_out, xor_3_out,
       xor_4_out, xor_5_out, xor_6_out, xor_7_out, xor_8_out, xor_9_out, xor_10_out, xor_11_out, xor_12_out,
       xor_13_out, xor_14_out, xor_15_out, xor_16_out;

  _74245 _74245_1 (
    .pin1(1'b0), .pin2(BusOut15), .pin3(BusOut14), .pin4(BusOut13), .pin5(BusOut12), .pin6(BusOut11),
    .pin7(BusOut10), .pin8(BusOut9), .pin9(BusOut8), .pin10(1'b0), .pin11(DispSig[8]), .pin12(DispSig[9]),
    .pin13(DispSig[10]), .pin14(DispSig[11]), .pin15(DispSig[12]), .pin16(DispSig[13]), .pin17(DispSig[14]),
    .pin18(DispSig[15]), .pin19(RegOut), .pin20(1'b1));
  _74245 _74245_2 (
    .pin1(1'b0), .pin2(BusOut7), .pin3(BusOut6), .pin4(BusOut5), .pin5(BusOut4), .pin6(BusOut3),
    .pin7(BusOut2), .pin8(BusOut1), .pin9(BusOut0), .pin10(1'b0), .pin11(DispSig[0]), .pin12(DispSig[1]),
    .pin13(DispSig[2]), .pin14(DispSig[3]), .pin15(DispSig[4]), .pin16(DispSig[5]), .pin17(DispSig[6]),
    .pin18(DispSig[7]), .pin19(RegOut), .pin20(1'b1));
  _74173 _74173_1 (
    .pin1(1'b0), .pin2(1'b0), .pin3(_74173_1_pin3), .pin4(_74173_1_pin4), .pin5(_74173_1_pin5),
    .pin6(_74173_1_pin6), .pin7(Clock), .pin8(1'b0), .pin9(RegIn), .pin10(RegIn), .pin11(BusOut15),
    .pin12(BusOut14), .pin13(BusOut13), .pin14(BusOut12), .pin15(Reset), .pin16(1'b1));
  _74173 _74173_2 (
    .pin1(1'b0), .pin2(1'b0), .pin3(_74173_2_pin3), .pin4(_74173_2_pin4), .pin5(_74173_2_pin5),
    .pin6(_74173_2_pin6), .pin7(Clock), .pin8(1'b0), .pin9(RegIn), .pin10(RegIn), .pin11(BusOut7),
    .pin12(BusOut6), .pin13(BusOut5), .pin14(BusOut4), .pin15(Reset), .pin16(1'b1));
  _74173 _74173_3 (
    .pin1(1'b0), .pin2(1'b0), .pin3(_74173_3_pin3), .pin4(_74173_3_pin4), .pin5(_74173_3_pin5),
    .pin6(_74173_3_pin6), .pin7(Clock), .pin8(1'b0), .pin9(RegIn), .pin10(RegIn), .pin11(BusOut11),
    .pin12(BusOut10), .pin13(BusOut9), .pin14(BusOut8), .pin15(Reset), .pin16(1'b1));
  _74173 _74173_4 (
    .pin1(1'b0), .pin2(1'b0), .pin3(_74173_4_pin3), .pin4(_74173_4_pin4), .pin5(_74173_4_pin5),
    .pin6(_74173_4_pin6), .pin7(Clock), .pin8(1'b0), .pin9(RegIn), .pin10(RegIn), .pin11(BusOut3),
    .pin12(BusOut2), .pin13(BusOut1), .pin14(BusOut0), .pin15(Reset), .pin16(1'b1));
  nor nor_1 (nor_1_out, DispSig[0], DispSig[1]);
  xor xor_1 (xor_1_out, _74173_1_pin6, 1'b1);
  xor xor_2 (xor_2_out, _74173_1_pin5, 1'b1);
  xor xor_3 (xor_3_out, _74173_1_pin4, 1'b1);
  xor xor_4 (xor_4_out, _74173_1_pin3, 1'b1);
  xor xor_5 (xor_5_out, _74173_3_pin6, 1'b1);
  xor xor_6 (xor_6_out, _74173_3_pin5, 1'b1);
  xor xor_7 (xor_7_out, _74173_3_pin4, 1'b1);
  xor xor_8 (xor_8_out, _74173_3_pin3, 1'b1);
  xor xor_9 (xor_9_out, _74173_2_pin6, 1'b1);
  xor xor_10 (xor_10_out, _74173_2_pin5, 1'b1);
  xor xor_11 (xor_11_out, _74173_2_pin4, 1'b1);
  xor xor_12 (xor_12_out, _74173_2_pin3, 1'b1);
  xor xor_13 (xor_13_out, _74173_4_pin6, 1'b1);
  xor xor_14 (xor_14_out, _74173_4_pin5, 1'b1);
  xor xor_15 (xor_15_out, _74173_4_pin4, 1'b1);
  xor xor_16 (xor_16_out, _74173_4_pin3, 1'b1);
  and and_1 (and_1_out, nor_1_out, nor_2_out);
  nor nor_2 (nor_2_out, DispSig[2], DispSig[3]);
  and and_2 (and_2_out, and_1_out, and_3_out);
  nor nor_3 (nor_3_out, DispSig[4], DispSig[5]);
  and and_3 (and_3_out, nor_3_out, nor_4_out);
  nor nor_4 (nor_4_out, DispSig[6], DispSig[7]);
  and and_4 (zero, and_2_out, and_6_out);
  and and_5 (and_5_out, nor_5_out, nor_6_out);
  nor nor_5 (nor_5_out, DispSig[15], DispSig[14]);
  and and_6 (and_6_out, and_5_out, and_7_out);
  nor nor_6 (nor_6_out, DispSig[13], DispSig[12]);
  and and_7 (and_7_out, nor_7_out, nor_8_out);
  nor nor_7 (nor_7_out, DispSig[11], DispSig[10]);
  _74173 _74173_5 (
    .pin1(1'b0), .pin2(1'b0), .pin3(zeroOut), .pin5(carryOut), .pin7(Clock), .pin8(1'b0), .pin9(FlagiIn),
    .pin10(FlagiIn), .pin11(1'b0), .pin12(carry), .pin13(1'b0), .pin14(zero), .pin15(Reset), .pin16(1'b1));  // open: pin4, pin6
  nor nor_8 (nor_8_out, DispSig[9], DispSig[8]);
  _74283 _74283_1 (
    .pin1(DispSig[13]), .pin2(xor_3_out), .pin3(MainSig[13]), .pin4(DispSig[12]), .pin5(MainSig[12]),
    .pin6(xor_4_out), .pin7(_74283_1_pin7), .pin8(1'b0), .pin9(carry), .pin10(DispSig[15]),
    .pin11(xor_1_out), .pin12(MainSig[15]), .pin13(DispSig[14]), .pin14(MainSig[14]), .pin15(xor_2_out),
    .pin16(1'b1));
  _74283 _74283_2 (
    .pin1(DispSig[9]), .pin2(xor_7_out), .pin3(MainSig[9]), .pin4(DispSig[8]), .pin5(MainSig[8]),
    .pin6(xor_8_out), .pin7(_74283_2_pin7), .pin8(1'b0), .pin9(_74283_1_pin7), .pin10(DispSig[11]),
    .pin11(xor_5_out), .pin12(MainSig[11]), .pin13(DispSig[10]), .pin14(MainSig[10]), .pin15(xor_6_out),
    .pin16(1'b1));
  _74283 _74283_3 (
    .pin1(DispSig[5]), .pin2(xor_11_out), .pin3(MainSig[5]), .pin4(DispSig[4]), .pin5(MainSig[4]),
    .pin6(xor_12_out), .pin7(_74283_3_pin7), .pin8(1'b0), .pin9(_74283_2_pin7), .pin10(DispSig[7]),
    .pin11(xor_9_out), .pin12(MainSig[7]), .pin13(DispSig[6]), .pin14(MainSig[6]), .pin15(xor_10_out),
    .pin16(1'b1));
  _74283 _74283_4 (
    .pin1(DispSig[1]), .pin2(xor_15_out), .pin3(MainSig[1]), .pin4(DispSig[0]), .pin5(MainSig[0]),
    .pin6(xor_16_out), .pin7(1'b1), .pin8(1'b0), .pin9(_74283_3_pin7), .pin10(DispSig[3]),
    .pin11(xor_13_out), .pin12(MainSig[3]), .pin13(DispSig[2]), .pin14(MainSig[2]), .pin15(xor_14_out),
    .pin16(1'b1));
  // Pins of 1 and 16 bits meet at DispSig

  // Notes on the sheet:
  //   RegOut: default 1
  //   RegIn: default 1
endmodule
