// Digital circuit 16BitRegisterBase.dig as structural Verilog
module _16BitRegisterBase (
  input  in_1,
  input  in_2,
  input  in_3,
  input  in_4,
  input  in_5,
  input  in_6,
  input  in_7,
  input  in_8,
  input  busOut,
  input  in_10,
  input  in_11,
  input  in_12,
  input  in_13,
  input  in_14,
  input  in_15,
  input  in_16,
  input  in_17,
  input  RegIn,
  input  RegOut,
  input  Clock,
  input  Reset
);

  wire _74245_1_pin11, _74245_1_pin12, _74245_1_pin13, _74245_1_pin14, _74245_1_pin15, _74245_1_pin16,
       _74245_1_pin17, _74245_1_pin18, _74245_2_pin11, _74245_2_pin12, _74245_2_pin13, _74245_2_pin14,
       _74245_2_pin15, _74245_2_pin16, _74245_2_pin17, _74245_2_pin18, _74245_3_pin11, _74245_3_pin12,
       _74245_3_pin13, _74245_3_pin14, _74245_3_pin15, _74245_3_pin16, _74245_3_pin17, _74245_3_pin18,
       _74245_4_pin11, _74245_4_pin12, _74245_4_pin13, _74245_4_pin14, _74245_4_pin15, _74245_4_pin16,
       _74245_4_pin17, _74245_4_pin18;

  _74245 _74245_1 (
    .pin1(1'b1), .pin2(in_8), .pin3(in_7), .pin4(in_6), .pin5(in_5), .pin6(in_4), .pin7(in_3), .pin8(in_2),
    .pin9(in_1), .pin10(1'b0), .pin11(_74245_1_pin11), .pin12(_74245_1_pin12), .pin13(_74245_1_pin13),
    .pin14(_74245_1_pin14), .pin15(_74245_1_pin15), .pin16(_74245_1_pin16), .pin17(_74245_1_pin17),
    .pin18(_74245_1_pin18), .pin19(busOut), .pin20(1'b1));
  LED Bus14 (.in(_74245_1_pin17));
  LED Bus15 (.in(_74245_1_pin18));
  LED Bus12 (.in(_74245_1_pin15));
  LED Bus13 (.in(_74245_1_pin16));
  LED Bus10 (.in(_74245_1_pin13));
  LED Bus11 (.in(_74245_1_pin14));
  LED Bus8 (.in(_74245_1_pin11));
  LED Bus9 (.in(_74245_1_pin12));
  _74245 _74245_2 (
    .pin1(1'b1), .pin2(in_17), .pin3(in_16), .pin4(in_15), .pin5(in_14), .pin6(in_13), .pin7(in_12),
    .pin8(in_11), .pin9(in_10), .pin10(1'b0), .pin11(_74245_2_pin11), .pin12(_74245_2_pin12),
    .pin13(_74245_2_pin13), .pin14(_74245_2_pin14), .pin15(_74245_2_pin15), .pin16(_74245_2_pin16),
    .pin17(_74245_2_pin17), .pin18(_74245_2_pin18), .pin19(busOut), .pin20(1'b1));
  LED Bus6 (.in(_74245_2_pin17));
  LED Bus7 (.in(_74245_2_pin18));
  LED Bus4 (.in(_74245_2_pin15));
  LED Bus5 (.in(_74245_2_pin16));
  LED Bus2 (.in(_74245_2_pin13));
  LED Bus3 (.in(_74245_2_pin14));
  LED Bus0 (.in(_74245_2_pin11));
  LED Bus1 (.in(_74245_2_pin12));
  _74245 _74245_3 (
    .pin1(1'b0), .pin2(_74245_1_pin18), .pin3(_74245_1_pin17), .pin4(_74245_1_pin16), .pin5(_74245_1_pin15),
    .pin6(_74245_1_pin14), .pin7(_74245_1_pin13), .pin8(_74245_1_pin12), .pin9(_74245_1_pin11), .pin10(1'b0),
    .pin11(_74245_3_pin11), .pin12(_74245_3_pin12), .pin13(_74245_3_pin13), .pin14(_74245_3_pin14),
    .pin15(_74245_3_pin15), .pin16(_74245_3_pin16), .pin17(_74245_3_pin17), .pin18(_74245_3_pin18),
    .pin19(RegIn), .pin20(1'b1));
  _74245 _74245_4 (
    .pin1(1'b0), .pin2(_74245_2_pin18), .pin3(_74245_2_pin17), .pin4(_74245_2_pin16), .pin5(_74245_2_pin15),
    .pin6(_74245_2_pin14), .pin7(_74245_2_pin13), .pin8(_74245_2_pin12), .pin9(_74245_2_pin11), .pin10(1'b0),
    .pin11(_74245_4_pin11), .pin12(_74245_4_pin12), .pin13(_74245_4_pin13), .pin14(_74245_4_pin14),
    .pin15(_74245_4_pin15), .pin16(_74245_4_pin16), .pin17(_74245_4_pin17), .pin18(_74245_4_pin18),
    .pin19(RegIn), .pin20(1'b1));
  _74173 _74173_1 (
    .pin1(1'b0), .pin2(1'b0), .pin3(_74245_3_pin18), .pin4(_74245_3_pin17), .pin5(_74245_3_pin16),
    .pin6(_74245_3_pin15), .pin7(Clock), .pin8(1'b0), .pin9(RegOut), .pin10(RegOut), .pin11(_74245_1_pin15),
    .pin12(_74245_1_pin16), .pin13(_74245_1_pin17), .pin14(_74245_1_pin18), .pin15(Reset), .pin16(1'b1));
  LED Signal15 (.in(_74245_3_pin18));
  LED Signal14 (.in(_74245_3_pin17));
  LED Signal13 (.in(_74245_3_pin16));
  LED Signal12 (.in(_74245_3_pin15));
  LED Signal11 (.in(_74245_3_pin14));
  LED Signal10 (.in(_74245_3_pin13));
  LED Signal9 (.in(_74245_3_pin12));
  LED Signal8 (.in(_74245_3_pin11));
  LED Signal7 (.in(_74245_4_pin18));
  LED Signal6 (.in(_74245_4_pin17));
  LED Signal5 (.in(_74245_4_pin16));
  LED Signal4 (.in(_74245_4_pin15));
  LED Signal3 (.in(_74245_4_pin14));
  LED Signal2 (.in(_74245_4_pin13));
  LED Signal1 (.in(_74245_4_pin12));
  LED Signal0 (.in(_74245_4_pin11));

  // Notes on the sheet:
  //   busOut: default 1
  //   RegIn: default 1
  //   RegOut: default 1
endmodule
