// Digital circuit 16BitRegisterCounterInt.dig as structural Verilog
module _16BitRegisterCounterInt (
  input  RegOut,
  input  RegIn,
  input  Reset,
  input  Dec,
  input  Inc,
  output [15:0] SignalOut,
  output Bus0,
  output Bus1,
  output Bus2,
  output Bus3,
  output Bus4,
  output Bus5,
  output Bus6,
  output Bus7,
  output Bus8,
  output Bus9,
  output Bus10,
  output Bus11,
  output Bus12,
  output Bus13,
  output Bus14,
  output Bus15
);

  wire _74193_1_pin4, _74193_1_pin5, _74193_1_pin12, _74193_1_pin13, _74193_2_pin4, _74193_2_pin5,
       _74193_2_pin12, _74193_2_pin13;

  _74245 _74245_1 (
    .pin1(1'b0), .pin2(Bus15), .pin3(Bus14), .pin4(Bus13), .pin5(Bus12), .pin6(Bus11), .pin7(Bus10),
    .pin8(Bus9), .pin9(Bus8), .pin10(1'b0), .pin11(SignalOut[8]), .pin12(SignalOut[9]),
    .pin13(SignalOut[10]), .pin14(SignalOut[11]), .pin15(SignalOut[12]), .pin16(SignalOut[13]),
    .pin17(SignalOut[14]), .pin18(SignalOut[15]), .pin19(RegOut), .pin20(1'b1));
  _74245 _74245_2 (
    .pin1(1'b0), .pin2(Bus7), .pin3(Bus6), .pin4(Bus5), .pin5(Bus4), .pin6(Bus3), .pin7(Bus2), .pin8(Bus1),
    .pin9(Bus0), .pin10(1'b0), .pin11(SignalOut[0]), .pin12(SignalOut[1]), .pin13(SignalOut[2]),
    .pin14(SignalOut[3]), .pin15(SignalOut[4]), .pin16(SignalOut[5]), .pin17(SignalOut[6]),
    .pin18(SignalOut[7]), .pin19(RegOut), .pin20(1'b1));
  _74193 _74193_1 (
    .pin1(Bus13), .pin2(SignalOut[13]), .pin3(SignalOut[12]), .pin4(_74193_1_pin4), .pin5(_74193_1_pin5),
    .pin6(SignalOut[14]), .pin7(SignalOut[15]), .pin8(1'b0), .pin9(Bus15), .pin10(Bus14), .pin11(RegIn),
    .pin12(_74193_1_pin12), .pin13(_74193_1_pin13), .pin14(Reset), .pin15(Bus12), .pin16(1'b1));
  _74193 _74193_2 (
    .pin1(Bus5), .pin2(SignalOut[5]), .pin3(SignalOut[4]), .pin4(_74193_2_pin4), .pin5(_74193_2_pin5),
    .pin6(SignalOut[6]), .pin7(SignalOut[7]), .pin8(1'b0), .pin9(Bus7), .pin10(Bus6), .pin11(RegIn),
    .pin12(_74193_2_pin12), .pin13(_74193_2_pin13), .pin14(Reset), .pin15(Bus4), .pin16(1'b1));
  _74193 _74193_3 (
    .pin1(Bus9), .pin2(SignalOut[9]), .pin3(SignalOut[8]), .pin4(_74193_2_pin13), .pin5(_74193_2_pin12),
    .pin6(SignalOut[10]), .pin7(SignalOut[11]), .pin8(1'b0), .pin9(Bus11), .pin10(Bus10), .pin11(RegIn),
    .pin12(_74193_1_pin5), .pin13(_74193_1_pin4), .pin14(Reset), .pin15(Bus8), .pin16(1'b1));
  _74193 _74193_4 (
    .pin1(Bus1), .pin2(SignalOut[1]), .pin3(SignalOut[0]), .pin4(Dec), .pin5(Inc), .pin6(SignalOut[2]),
    .pin7(SignalOut[3]), .pin8(1'b0), .pin9(Bus3), .pin10(Bus2), .pin11(RegIn), .pin12(_74193_2_pin5),
    .pin13(_74193_2_pin4), .pin14(Reset), .pin15(Bus0), .pin16(1'b1));

  // Notes on the sheet:
  //   RegOut: default 1
  //   RegIn: default 1
endmodule
