// Digital circuit 16BitRegisterCounterInt2.dig as structural Verilog
module _16BitRegisterCounterInt2 (
  input  RegOut,
  input  RegIn,
  input  Reset,
  input  Dec,
  input  Inc,
  output [15:0] SignalOut,
  output [15:0] BusOut,
  output [15:0] BusIn
);

  wire _74193_1_pin4, _74193_1_pin5, _74193_1_pin12, _74193_1_pin13, _74193_2_pin4, _74193_2_pin5,
       _74193_2_pin12, _74193_2_pin13;

  _74245 _74245_1 (
    .pin1(1'b0), .pin2(BusIn[0]), .pin3(BusIn[1]), .pin4(BusIn[2]), .pin5(BusIn[3]), .pin6(BusIn[4]),
    .pin7(BusIn[5]), .pin8(BusIn[6]), .pin9(BusIn[7]), .pin10(1'b0), .pin11(SignalOut[8]),
    .pin12(SignalOut[9]), .pin13(SignalOut[10]), .pin14(SignalOut[11]), .pin15(SignalOut[12]),
    .pin16(SignalOut[13]), .pin17(SignalOut[14]), .pin18(SignalOut[15]), .pin19(RegOut), .pin20(1'b1));
  _74245 _74245_2 (
    .pin1(1'b0), .pin2(BusIn[8]), .pin3(BusIn[9]), .pin4(BusIn[10]), .pin5(BusIn[11]), .pin6(BusIn[12]),
    .pin7(BusIn[13]), .pin8(BusIn[14]), .pin9(BusIn[15]), .pin10(1'b0), .pin11(SignalOut[0]),
    .pin12(SignalOut[1]), .pin13(SignalOut[2]), .pin14(SignalOut[3]), .pin15(SignalOut[4]),
    .pin16(SignalOut[5]), .pin17(SignalOut[6]), .pin18(SignalOut[7]), .pin19(RegOut), .pin20(1'b1));
  _74193 _74193_1 (
    .pin1(BusIn[2]), .pin2(SignalOut[13]), .pin3(SignalOut[12]), .pin4(_74193_1_pin4), .pin5(_74193_1_pin5),
    .pin6(SignalOut[14]), .pin7(SignalOut[15]), .pin8(1'b0), .pin9(BusIn[0]), .pin10(BusIn[1]),
    .pin11(RegIn), .pin12(_74193_1_pin12), .pin13(_74193_1_pin13), .pin14(Reset), .pin15(BusIn[3]),
    .pin16(1'b1));
  _74193 _74193_2 (
    .pin1(BusIn[10]), .pin2(SignalOut[5]), .pin3(SignalOut[4]), .pin4(_74193_2_pin4), .pin5(_74193_2_pin5),
    .pin6(SignalOut[6]), .pin7(SignalOut[7]), .pin8(1'b0), .pin9(BusIn[8]), .pin10(BusIn[9]), .pin11(RegIn),
    .pin12(_74193_2_pin12), .pin13(_74193_2_pin13), .pin14(Reset), .pin15(BusIn[11]), .pin16(1'b1));
  _74193 _74193_3 (
    .pin1(BusIn[6]), .pin2(SignalOut[9]), .pin3(SignalOut[8]), .pin4(_74193_2_pin13), .pin5(_74193_2_pin12),
    .pin6(SignalOut[10]), .pin7(SignalOut[11]), .pin8(1'b0), .pin9(BusIn[4]), .pin10(BusIn[5]),
    .pin11(RegIn), .pin12(_74193_1_pin5), .pin13(_74193_1_pin4), .pin14(Reset), .pin15(BusIn[7]), .pin16(1'b1));
  _74193 _74193_4 (
    .pin1(BusIn[14]), .pin2(SignalOut[1]), .pin3(SignalOut[0]), .pin4(Dec), .pin5(Inc), .pin6(SignalOut[2]),
    .pin7(SignalOut[3]), .pin8(1'b0), .pin9(BusIn[12]), .pin10(BusIn[13]), .pin11(RegIn),
    .pin12(_74193_2_pin5), .pin13(_74193_2_pin4), .pin14(Reset), .pin15(BusIn[15]), .pin16(1'b1));

  assign BusOut = {BusIn[0], BusIn[1], BusIn[2], BusIn[3], BusIn[4], BusIn[5], BusIn[6], BusIn[7], BusIn[8], BusIn[9], BusIn[10], BusIn[11], BusIn[12], BusIn[13], BusIn[14], BusIn[15]};

  // Notes on the sheet:
  //   RegOut: default 1
  //   RegIn: default 1
endmodule
