// Digital circuit 16BitRegisterInt.dig as structural Verilog
module _16BitRegisterInt (
  input  RegOut,
  input  RegIn,
  input  Clock,
  input  Reset,
  input  BusIn0,
  input  BusIn1,
  input  BusIn2,
  input  BusIn3,
  input  BusIn4,
  input  BusIn5,
  input  BusIn6,
  input  BusIn7,
  input  BusIn8,
  input  BusIn9,
  input  BusIn10,
  input  BusIn11,
  input  BusIn12,
  input  BusIn13,
  input  BusIn14,
  input  BusIn15,
  output Sig0,
  output Sig1,
  output Sig2,
  output Sig3,
  output Sig4,
  output Sig5,
  output Sig6,
  output Sig7,
  output Sig8,
  output Sig9,
  output Sig10,
  output Sig11,
  output Sig12,
  output Sig13,
  output Sig14,
  output Sig15,
  output BusOut0,
  output BusOut1,
  output BusOut2,
  output BusOut3,
  output BusOut4,
  output BusOut5,
  output BusOut6,
  output BusOut7,
  output BusOut8,
  output BusOut9,
  output BusOut10,
  output BusOut11,
  output BusOut12,
  output BusOut13,
  output BusOut14,
  output BusOut15
);

  _74245 _74245_1 (
    .pin1(1'b0), .pin2(BusOut15), .pin3(BusOut14), .pin4(BusOut13), .pin5(BusOut12), .pin6(BusOut11),
    .pin7(BusOut10), .pin8(BusOut9), .pin9(BusOut8), .pin10(1'b0), .pin11(Sig8), .pin12(Sig9), .pin13(Sig10),
    .pin14(Sig11), .pin15(Sig12), .pin16(Sig13), .pin17(Sig14), .pin18(Sig15), .pin19(RegOut), .pin20(1'b1));
  _74245 _74245_2 (
    .pin1(1'b0), .pin2(BusOut7), .pin3(BusOut6), .pin4(BusOut5), .pin5(BusOut4), .pin6(BusOut3),
    .pin7(BusOut2), .pin8(BusOut1), .pin9(BusOut0), .pin10(1'b0), .pin11(Sig0), .pin12(Sig1), .pin13(Sig2),
    .pin14(Sig3), .pin15(Sig4), .pin16(Sig5), .pin17(Sig6), .pin18(Sig7), .pin19(RegOut), .pin20(1'b1));
  _74173 _74173_1 (
    .pin1(1'b0), .pin2(1'b0), .pin3(Sig15), .pin4(Sig14), .pin5(Sig13), .pin6(Sig12), .pin7(Clock),
    .pin8(1'b0), .pin9(RegIn), .pin10(RegIn), .pin11(BusIn12), .pin12(BusIn13), .pin13(BusIn14),
    .pin14(BusIn15), .pin15(Reset), .pin16(1'b1));
  _74173 _74173_2 (
    .pin1(1'b0), .pin2(1'b0), .pin3(Sig7), .pin4(Sig6), .pin5(Sig5), .pin6(Sig4), .pin7(Clock), .pin8(1'b0),
    .pin9(RegIn), .pin10(RegIn), .pin11(BusIn4), .pin12(BusIn5), .pin13(BusIn6), .pin14(BusIn7),
    .pin15(Reset), .pin16(1'b1));
  _74173 _74173_3 (
    .pin1(1'b0), .pin2(1'b0), .pin3(Sig11), .pin4(Sig10), .pin5(Sig9), .pin6(Sig8), .pin7(Clock),
    .pin8(1'b0), .pin9(RegIn), .pin10(RegIn), .pin11(BusIn8), .pin12(BusIn9), .pin13(BusIn10),
    .pin14(BusIn11), .pin15(Reset), .pin16(1'b1));
  _74173 _74173_4 (
    .pin1(1'b0), .pin2(1'b0), .pin3(Sig3), .pin4(Sig2), .pin5(Sig1), .pin6(Sig0), .pin7(Clock), .pin8(1'b0),
    .pin9(RegIn), .pin10(RegIn), .pin11(BusIn0), .pin12(BusIn1), .pin13(BusIn2), .pin14(BusIn3),
    .pin15(Reset), .pin16(1'b1));

  // Notes on the sheet:
  //   RegOut: default 1
  //   RegIn: default 1
endmodule
