// Digital circuit 16BitRegisterInt2.dig as structural Verilog
module _16BitRegisterInt2 (
  input  RegOut,
  input  RegIn,
  input  Clock,
  input  Reset,
  output BusOut0,
  output BusOut1,
  output BusOut2,
  output BusOut3,
  output BusOut4,
  output BusOut5,
  output BusOut6,
  output BusOut7,
  output BusOut8,
  output BusOut9,
  output BusOut10,
  output BusOut11,
  output BusOut12,
  output BusOut13,
  output BusOut14,
  output BusOut15,
  output [15:0] SignalOut
);

  _74245 _74245_1 (
    .pin1(1'b0), .pin2(BusOut15), .pin3(BusOut14), .pin4(BusOut13), .pin5(BusOut12), .pin6(BusOut11),
    .pin7(BusOut10), .pin8(BusOut9), .pin9(BusOut8), .pin10(1'b0), .pin11(SignalOut[8]),
    .pin12(SignalOut[9]), .pin13(SignalOut[10]), .pin14(SignalOut[11]), .pin15(SignalOut[12]),
    .pin16(SignalOut[13]), .pin17(SignalOut[14]), .pin18(SignalOut[15]), .pin19(RegOut), .pin20(1'b1));
  _74245 _74245_2 (
    .pin1(1'b0), .pin2(BusOut7), .pin3(BusOut6), .pin4(BusOut5), .pin5(BusOut4), .pin6(BusOut3),
    .pin7(BusOut2), .pin8(BusOut1), .pin9(BusOut0), .pin10(1'b0), .pin11(SignalOut[0]), .pin12(SignalOut[1]),
    .pin13(SignalOut[2]), .pin14(SignalOut[3]), .pin15(SignalOut[4]), .pin16(SignalOut[5]),
    .pin17(SignalOut[6]), .pin18(SignalOut[7]), .pin19(RegOut), .pin20(1'b1));
  _74173 _74173_1 (
    .pin1(1'b0), .pin2(1'b0), .pin3(SignalOut[15]), .pin4(SignalOut[14]), .pin5(SignalOut[13]),
    .pin6(SignalOut[12]), .pin7(Clock), .pin8(1'b0), .pin9(RegIn), .pin10(RegIn), .pin11(BusOut12),
    .pin12(BusOut13), .pin13(BusOut14), .pin14(BusOut15), .pin15(Reset), .pin16(1'b1));
  _74173 _74173_2 (
    .pin1(1'b0), .pin2(1'b0), .pin3(SignalOut[7]), .pin4(SignalOut[6]), .pin5(SignalOut[5]),
    .pin6(SignalOut[4]), .pin7(Clock), .pin8(1'b0), .pin9(RegIn), .pin10(RegIn), .pin11(BusOut4),
    .pin12(BusOut5), .pin13(BusOut6), .pin14(BusOut7), .pin15(Reset), .pin16(1'b1));
  _74173 _74173_3 (
    .pin1(1'b0), .pin2(1'b0), .pin3(SignalOut[11]), .pin4(SignalOut[10]), .pin5(SignalOut[9]),
    .pin6(SignalOut[8]), .pin7(Clock), .pin8(1'b0), .pin9(RegIn), .pin10(RegIn), .pin11(BusOut8),
    .pin12(BusOut9), .pin13(BusOut10), .pin14(BusOut11), .pin15(Reset), .pin16(1'b1));
  _74173 _74173_4 (
    .pin1(1'b0), .pin2(1'b0), .pin3(SignalOut[3]), .pin4(SignalOut[2]), .pin5(SignalOut[1]),
    .pin6(SignalOut[0]), .pin7(Clock), .pin8(1'b0), .pin9(RegIn), .pin10(RegIn), .pin11(BusOut0),
    .pin12(BusOut1), .pin13(BusOut2), .pin14(BusOut3), .pin15(Reset), .pin16(1'b1));

  // Notes on the sheet:
  //   RegOut: default 1
  //   RegIn: default 1
endmodule
