// Digital circuit 16BitRegisterSwitching.dig as structural Verilog
module _16BitRegisterSwitching (
  input  Clock,
  input  Reset,
  input  InLowHigh,
  input  InHighLow,
  input  InHighHigh,
  input  InLowLow,
  input  In,
  input  OutSwap,
  input  InLowHigh_2,
  input  InHighLow_2,
  input  Out,
  input  OutLow,
  input  In_2,
  input  InLowLow_2,
  input  OutHigh,
  input  InHighHigh_2,
  output Bus0,
  output Bus1,
  output Bus2,
  output Bus3,
  output Bus4,
  output Bus5,
  output Bus6,
  output Bus7,
  output Bus8,
  output Bus9,
  output Bus10,
  output Bus11,
  output Bus12,
  output Bus13,
  output Bus14,
  output Bus15,
  output Signal0,
  output Signal1,
  output Signal2,
  output Signal3,
  output Signal4,
  output Signal5,
  output Signal6,
  output Signal7,
  output Signal8,
  output Signal9,
  output Signal10,
  output Signal11,
  output Signal12,
  output Signal13,
  output Signal14,
  output Signal15
);

  wire _74173_1_pin9, _74173_2_pin9, and_1_out, and_2_out, HighHigh_pin1, HighHigh_pin11, HighHigh_pin12,
       HighHigh_pin13, HighHigh_pin14, HighHigh_pin15, HighHigh_pin16, HighHigh_pin17, HighHigh_pin18,
       HighHigh_pin19, HighLow_pin19, LowHigh_pin19, LowLow_pin11, LowLow_pin12, LowLow_pin13, LowLow_pin14,
       LowLow_pin15, LowLow_pin16, LowLow_pin17, LowLow_pin18, LowLow_pin19;

  _74245 HighHigh (
    .pin1(HighHigh_pin1), .pin2(Bus15), .pin3(Bus14), .pin4(Bus13), .pin5(Bus12), .pin6(Bus11), .pin7(Bus10),
    .pin8(Bus9), .pin9(Bus8), .pin10(1'b0), .pin11(HighHigh_pin11), .pin12(HighHigh_pin12),
    .pin13(HighHigh_pin13), .pin14(HighHigh_pin14), .pin15(HighHigh_pin15), .pin16(HighHigh_pin16),
    .pin17(HighHigh_pin17), .pin18(HighHigh_pin18), .pin19(HighHigh_pin19), .pin20(1'b1));
  _74245 LowLow (
    .pin1(HighHigh_pin1), .pin2(Bus7), .pin3(Bus6), .pin4(Bus5), .pin5(Bus4), .pin6(Bus3), .pin7(Bus2),
    .pin8(Bus1), .pin9(Bus0), .pin10(1'b0), .pin11(LowLow_pin11), .pin12(LowLow_pin12), .pin13(LowLow_pin13),
    .pin14(LowLow_pin14), .pin15(LowLow_pin15), .pin16(LowLow_pin16), .pin17(LowLow_pin17),
    .pin18(LowLow_pin18), .pin19(LowLow_pin19), .pin20(1'b1));
  _74245 HighLow (
    .pin1(HighHigh_pin1), .pin2(Bus15), .pin3(Bus14), .pin4(Bus13), .pin5(Bus12), .pin6(Bus11), .pin7(Bus10),
    .pin8(Bus9), .pin9(Bus8), .pin10(1'b0), .pin11(LowLow_pin11), .pin12(LowLow_pin12), .pin13(LowLow_pin13),
    .pin14(LowLow_pin14), .pin15(LowLow_pin15), .pin16(LowLow_pin16), .pin17(LowLow_pin17),
    .pin18(LowLow_pin18), .pin19(HighLow_pin19), .pin20(1'b1));
  _74245 LowHigh (
    .pin1(HighHigh_pin1), .pin2(Bus7), .pin3(Bus6), .pin4(Bus5), .pin5(Bus4), .pin6(Bus3), .pin7(Bus2),
    .pin8(Bus1), .pin9(Bus0), .pin10(1'b0), .pin11(HighHigh_pin11), .pin12(HighHigh_pin12),
    .pin13(HighHigh_pin13), .pin14(HighHigh_pin14), .pin15(HighHigh_pin15), .pin16(HighHigh_pin16),
    .pin17(HighHigh_pin17), .pin18(HighHigh_pin18), .pin19(LowHigh_pin19), .pin20(1'b1));
  LED Data15 (.in(HighHigh_pin18));
  LED Data14 (.in(HighHigh_pin17));
  LED led_1 (.in(HighHigh_pin16));
  LED led_2 (.in(HighHigh_pin15));
  LED led_3 (.in(HighHigh_pin14));
  LED led_4 (.in(HighHigh_pin13));
  LED led_5 (.in(HighHigh_pin12));
  LED Data8 (.in(HighHigh_pin11));
  LED Data7 (.in(LowLow_pin18));
  LED led_6 (.in(LowLow_pin17));
  LED led_7 (.in(LowLow_pin16));
  and and_1 (and_1_out, InLowLow, InHighHigh, InHighLow, InLowHigh);
  LED led_8 (.in(LowLow_pin15));
  LED led_9 (.in(LowLow_pin14));
  and and_2 (and_2_out, In, and_1_out);
  LED led_10 (.in(LowLow_pin13));
  LED led_11 (.in(LowLow_pin12));
  LED Data0 (.in(LowLow_pin11));
  _74245 _74245_1 (
    .pin1(1'b0), .pin2(HighHigh_pin18), .pin3(HighHigh_pin17), .pin4(HighHigh_pin16), .pin5(HighHigh_pin15),
    .pin6(HighHigh_pin14), .pin7(HighHigh_pin13), .pin8(HighHigh_pin12), .pin9(HighHigh_pin11), .pin10(1'b0),
    .pin11(Signal8), .pin12(Signal9), .pin13(Signal10), .pin14(Signal11), .pin15(Signal12), .pin16(Signal13),
    .pin17(Signal14), .pin18(Signal15), .pin19(HighHigh_pin1), .pin20(1'b1));
  _74245 _74245_2 (
    .pin1(1'b0), .pin2(LowLow_pin18), .pin3(LowLow_pin17), .pin4(LowLow_pin16), .pin5(LowLow_pin15),
    .pin6(LowLow_pin14), .pin7(LowLow_pin13), .pin8(LowLow_pin12), .pin9(LowLow_pin11), .pin10(1'b0),
    .pin11(Signal0), .pin12(Signal1), .pin13(Signal2), .pin14(Signal3), .pin15(Signal4), .pin16(Signal5),
    .pin17(Signal6), .pin18(Signal7), .pin19(HighHigh_pin1), .pin20(1'b1));
  _74173 _74173_1 (
    .pin1(1'b0), .pin2(1'b0), .pin3(Signal15), .pin4(Signal14), .pin5(Signal13), .pin6(Signal12),
    .pin7(Clock), .pin8(1'b0), .pin9(_74173_1_pin9), .pin10(_74173_1_pin9), .pin11(HighHigh_pin15),
    .pin12(HighHigh_pin16), .pin13(HighHigh_pin17), .pin14(HighHigh_pin18), .pin15(Reset), .pin16(1'b1));
  _74173 _74173_2 (
    .pin1(1'b0), .pin2(1'b0), .pin3(Signal7), .pin4(Signal6), .pin5(Signal5), .pin6(Signal4), .pin7(Clock),
    .pin8(1'b0), .pin9(_74173_2_pin9), .pin10(_74173_2_pin9), .pin11(LowLow_pin15), .pin12(LowLow_pin16),
    .pin13(LowLow_pin17), .pin14(LowLow_pin18), .pin15(Reset), .pin16(1'b1));
  and and_3 (_74173_1_pin9, HighHigh_pin19, LowHigh_pin19);
  and and_4 (_74173_2_pin9, LowLow_pin19, HighLow_pin19);
  _74173 _74173_3 (
    .pin1(1'b0), .pin2(1'b0), .pin3(Signal11), .pin4(Signal10), .pin5(Signal9), .pin6(Signal8), .pin7(Clock),
    .pin8(1'b0), .pin9(_74173_1_pin9), .pin10(_74173_1_pin9), .pin11(HighHigh_pin11), .pin12(HighHigh_pin12),
    .pin13(HighHigh_pin13), .pin14(HighHigh_pin14), .pin15(Reset), .pin16(1'b1));
  _74173 _74173_4 (
    .pin1(1'b0), .pin2(1'b0), .pin3(Signal3), .pin4(Signal2), .pin5(Signal1), .pin6(Signal0), .pin7(Clock),
    .pin8(1'b0), .pin9(_74173_2_pin9), .pin10(_74173_2_pin9), .pin11(LowLow_pin11), .pin12(LowLow_pin12),
    .pin13(LowLow_pin13), .pin14(LowLow_pin14), .pin15(Reset), .pin16(1'b1));
  and and_5 (LowHigh_pin19, InLowHigh_2, OutSwap);
  and and_6 (HighLow_pin19, InHighLow_2, OutSwap);
  and and_7 (LowLow_pin19, InLowLow_2, In_2, OutLow, Out);
  and and_8 (HighHigh_pin19, InHighHigh_2, OutHigh, In_2, Out);
  and and_9 (HighHigh_pin1, OutSwap, OutHigh, OutLow, Out);

  // Notes on the sheet:
  //   OutSwap: default 1
  //   InLowHigh_2: default 1
  //   InHighLow_2: default 1
  //   Out: default 1
  //   OutLow: default 1
  //   In_2: default 1
  //   InLowLow_2: default 1
  //   OutHigh: default 1
  //   InHighHigh_2: default 1
  //   RegOut
  //   HighLow
  //   LowLow
  //   LowHigh
  //   HighHigh
  //   RegInLow
  //   RegInHigh
  //   _HighHigh
endmodule
