// Digital circuit 16BitRegisterSwitching2.dig as structural Verilog
module _16BitRegisterSwitching2 (
  input  in_1,
  input  in_2,
  input  in_3,
  input  in_4,
  input  in_5,
  input  in_6,
  input  in_7,
  input  in_8,
  input  busOut,
  input  in_10,
  input  in_11,
  input  in_12,
  input  in_13,
  input  in_14,
  input  in_15,
  input  in_16,
  input  in_17,
  input  nRegOut,
  input  nin,
  input  Clock,
  input  Reset,
  input  noutLL,
  input  noutHH,
  input  noutSwap,
  input  ninLL,
  input  ninHH,
  input  ninLH,
  input  ninHL
);

  wire _74245_1_pin11, _74245_1_pin12, _74245_1_pin13, _74245_1_pin14, _74245_1_pin15, _74245_1_pin16,
       _74245_1_pin17, _74245_1_pin18, _74245_2_pin11, _74245_2_pin12, _74245_2_pin13, _74245_2_pin14,
       _74245_2_pin15, _74245_2_pin16, _74245_2_pin17, _74245_2_pin18, undriven, undriven_2, undriven_3,
       undriven_4, undriven_5, undriven_6, undriven_7, undriven_8, undriven_9, undriven_10, undriven_11,
       undriven_12, undriven_13, undriven_14, undriven_15, undriven_16;

  _74245 _74245_1 (
    .pin1(1'b1), .pin2(in_8), .pin3(in_7), .pin4(in_6), .pin5(in_5), .pin6(in_4), .pin7(in_3), .pin8(in_2),
    .pin9(in_1), .pin10(1'b0), .pin11(_74245_1_pin11), .pin12(_74245_1_pin12), .pin13(_74245_1_pin13),
    .pin14(_74245_1_pin14), .pin15(_74245_1_pin15), .pin16(_74245_1_pin16), .pin17(_74245_1_pin17),
    .pin18(_74245_1_pin18), .pin19(busOut), .pin20(1'b1));
  LED Bus14 (.in(_74245_1_pin17));
  LED Bus15 (.in(_74245_1_pin18));
  LED Bus12 (.in(_74245_1_pin15));
  LED Bus13 (.in(_74245_1_pin16));
  LED Bus10 (.in(_74245_1_pin13));
  LED Bus11 (.in(_74245_1_pin14));
  LED Bus8 (.in(_74245_1_pin11));
  LED Bus9 (.in(_74245_1_pin12));
  _74245 _74245_2 (
    .pin1(1'b1), .pin2(in_17), .pin3(in_16), .pin4(in_15), .pin5(in_14), .pin6(in_13), .pin7(in_12),
    .pin8(in_11), .pin9(in_10), .pin10(1'b0), .pin11(_74245_2_pin11), .pin12(_74245_2_pin12),
    .pin13(_74245_2_pin13), .pin14(_74245_2_pin14), .pin15(_74245_2_pin15), .pin16(_74245_2_pin16),
    .pin17(_74245_2_pin17), .pin18(_74245_2_pin18), .pin19(busOut), .pin20(1'b1));
  LED Bus6 (.in(_74245_2_pin17));
  LED Bus7 (.in(_74245_2_pin18));
  LED Bus4 (.in(_74245_2_pin15));
  LED Bus5 (.in(_74245_2_pin16));
  LED Bus2 (.in(_74245_2_pin13));
  LED Bus3 (.in(_74245_2_pin14));
  LED Bus0 (.in(_74245_2_pin11));
  LED Bus1 (.in(_74245_2_pin12));
  _16BitRegisterSwitchingInt _16bitregisterswitchingint_1 (
    .ninHL(ninHL), .ninLH(ninLH), .ninHH(ninHH), .ninLL(ninLL), .nIn(nin), .noutSwap(noutSwap),
    .noutHH(noutHH), .noutLL(noutLL), .nOut(nRegOut), .Clock(Clock), .Reset(Reset), .Bus15(_74245_1_pin18),
    .Bus14(_74245_1_pin17), .Bus13(_74245_1_pin16), .Bus12(_74245_1_pin15), .Bus11(_74245_1_pin14),
    .Bus10(_74245_1_pin13), .Bus9(_74245_1_pin12), .Bus8(_74245_1_pin11), .Bus7(_74245_2_pin18),
    .Bus6(_74245_2_pin17), .Bus5(_74245_2_pin16), .Bus4(_74245_2_pin15), .Bus3(_74245_2_pin14),
    .Bus2(_74245_2_pin13), .Bus1(_74245_2_pin12), .Bus0(_74245_2_pin11));  // open: SignalOut
  LED Signal15 (.in(undriven_9));
  LED Signal14 (.in(undriven_10));
  LED Signal13 (.in(undriven_11));
  LED Signal12 (.in(undriven_12));
  LED Signal11 (.in(undriven_13));
  LED Signal10 (.in(undriven_14));
  LED Signal9 (.in(undriven_15));
  LED Signal8 (.in(undriven_16));
  LED Signal7 (.in(undriven));
  LED Signal6 (.in(undriven_2));
  LED Signal5 (.in(undriven_3));
  LED Signal4 (.in(undriven_4));
  LED Signal3 (.in(undriven_5));
  LED Signal2 (.in(undriven_6));
  LED Signal1 (.in(undriven_7));
  LED Signal0 (.in(undriven_8));

  // Notes on the sheet:
  //   busOut: default 1
  //   nRegOut: default 1
  //   nin: default 1
  //   noutLL: default 1
  //   noutHH: default 1
  //   noutSwap: default 1
  //   ninLL: default 1
  //   ninHH: default 1
  //   ninLH: default 1
  //   ninHL: default 1
endmodule
