// Digital circuit 16BitRegisterSwitchingInt.dig as structural Verilog
module _16BitRegisterSwitchingInt (
  input  Clock,
  input  Reset,
  input  nOut,
  input  noutLL,
  input  noutHH,
  input  noutSwap,
  input  nIn,
  input  ninLL,
  input  ninHH,
  input  ninLH,
  input  ninHL,
  output Bus0,
  output Bus1,
  output Bus2,
  output Bus3,
  output Bus4,
  output Bus5,
  output Bus6,
  output Bus7,
  output Bus8,
  output Bus9,
  output Bus10,
  output Bus11,
  output Bus12,
  output Bus13,
  output Bus14,
  output Bus15,
  output [15:0] SignalOut
);

  wire and_1_out, and_2_out, HighHigh_pin1, HighHigh_pin11, HighHigh_pin12, HighHigh_pin13, HighHigh_pin14,
       HighHigh_pin15, HighHigh_pin16, HighHigh_pin17, HighHigh_pin18, HighHigh_pin19, HighLow_pin19,
       LowHigh_pin19, LowLow_pin11, LowLow_pin12, LowLow_pin13, LowLow_pin14, LowLow_pin15, LowLow_pin16,
       LowLow_pin17, LowLow_pin18, LowLow_pin19;

  _74245 HighHigh (
    .pin1(HighHigh_pin1), .pin2(Bus15), .pin3(Bus14), .pin4(Bus13), .pin5(Bus12), .pin6(Bus11), .pin7(Bus10),
    .pin8(Bus9), .pin9(Bus8), .pin10(1'b0), .pin11(HighHigh_pin11), .pin12(HighHigh_pin12),
    .pin13(HighHigh_pin13), .pin14(HighHigh_pin14), .pin15(HighHigh_pin15), .pin16(HighHigh_pin16),
    .pin17(HighHigh_pin17), .pin18(HighHigh_pin18), .pin19(HighHigh_pin19), .pin20(1'b1));
  _74245 LowLow (
    .pin1(HighHigh_pin1), .pin2(Bus7), .pin3(Bus6), .pin4(Bus5), .pin5(Bus4), .pin6(Bus3), .pin7(Bus2),
    .pin8(Bus1), .pin9(Bus0), .pin10(1'b0), .pin11(LowLow_pin11), .pin12(LowLow_pin12), .pin13(LowLow_pin13),
    .pin14(LowLow_pin14), .pin15(LowLow_pin15), .pin16(LowLow_pin16), .pin17(LowLow_pin17),
    .pin18(LowLow_pin18), .pin19(LowLow_pin19), .pin20(1'b1));
  _74245 HighLow (
    .pin1(HighHigh_pin1), .pin2(Bus15), .pin3(Bus14), .pin4(Bus13), .pin5(Bus12), .pin6(Bus11), .pin7(Bus10),
    .pin8(Bus9), .pin9(Bus8), .pin10(1'b0), .pin11(LowLow_pin11), .pin12(LowLow_pin12), .pin13(LowLow_pin13),
    .pin14(LowLow_pin14), .pin15(LowLow_pin15), .pin16(LowLow_pin16), .pin17(LowLow_pin17),
    .pin18(LowLow_pin18), .pin19(HighLow_pin19), .pin20(1'b1));
  _74245 LowHigh (
    .pin1(HighHigh_pin1), .pin2(Bus7), .pin3(Bus6), .pin4(Bus5), .pin5(Bus4), .pin6(Bus3), .pin7(Bus2),
    .pin8(Bus1), .pin9(Bus0), .pin10(1'b0), .pin11(HighHigh_pin11), .pin12(HighHigh_pin12),
    .pin13(HighHigh_pin13), .pin14(HighHigh_pin14), .pin15(HighHigh_pin15), .pin16(HighHigh_pin16),
    .pin17(HighHigh_pin17), .pin18(HighHigh_pin18), .pin19(LowHigh_pin19), .pin20(1'b1));
  and and_1 (and_1_out, LowLow_pin19, HighLow_pin19);
  and and_2 (and_2_out, HighHigh_pin19, LowHigh_pin19);
  and and_3 (HighLow_pin19, ninHL, noutSwap);
  and and_4 (LowHigh_pin19, ninLH, noutSwap);
  _74245 _74245_1 (
    .pin1(1'b0), .pin2(HighHigh_pin18), .pin3(HighHigh_pin17), .pin4(HighHigh_pin16), .pin5(HighHigh_pin15),
    .pin6(HighHigh_pin14), .pin7(HighHigh_pin13), .pin8(HighHigh_pin12), .pin9(HighHigh_pin11), .pin10(1'b0),
    .pin11(SignalOut[8]), .pin12(SignalOut[9]), .pin13(SignalOut[10]), .pin14(SignalOut[11]),
    .pin15(SignalOut[12]), .pin16(SignalOut[13]), .pin17(SignalOut[14]), .pin18(SignalOut[15]),
    .pin19(HighHigh_pin1), .pin20(1'b1));
  _74245 _74245_2 (
    .pin1(1'b0), .pin2(LowLow_pin18), .pin3(LowLow_pin17), .pin4(LowLow_pin16), .pin5(LowLow_pin15),
    .pin6(LowLow_pin14), .pin7(LowLow_pin13), .pin8(LowLow_pin12), .pin9(LowLow_pin11), .pin10(1'b0),
    .pin11(SignalOut[0]), .pin12(SignalOut[1]), .pin13(SignalOut[2]), .pin14(SignalOut[3]),
    .pin15(SignalOut[4]), .pin16(SignalOut[5]), .pin17(SignalOut[6]), .pin18(SignalOut[7]),
    .pin19(HighHigh_pin1), .pin20(1'b1));
  and and_5 (LowLow_pin19, ninLL, nIn, noutLL, nOut);
  and and_6 (HighHigh_pin19, nOut, ninHH, nIn, noutHH);
  and and_7 (HighHigh_pin1, noutSwap, noutHH, noutLL, nOut);
  _74173 _74173_1 (
    .pin1(1'b0), .pin2(1'b0), .pin3(SignalOut[15]), .pin4(SignalOut[14]), .pin5(SignalOut[13]),
    .pin6(SignalOut[12]), .pin7(Clock), .pin8(1'b0), .pin9(and_2_out), .pin10(and_2_out),
    .pin11(HighHigh_pin15), .pin12(HighHigh_pin16), .pin13(HighHigh_pin17), .pin14(HighHigh_pin18),
    .pin15(Reset), .pin16(1'b1));
  _74173 _74173_2 (
    .pin1(1'b0), .pin2(1'b0), .pin3(SignalOut[7]), .pin4(SignalOut[6]), .pin5(SignalOut[5]),
    .pin6(SignalOut[4]), .pin7(Clock), .pin8(1'b0), .pin9(and_1_out), .pin10(and_1_out),
    .pin11(LowLow_pin15), .pin12(LowLow_pin16), .pin13(LowLow_pin17), .pin14(LowLow_pin18), .pin15(Reset),
    .pin16(1'b1));
  _74173 _74173_3 (
    .pin1(1'b0), .pin2(1'b0), .pin3(SignalOut[11]), .pin4(SignalOut[10]), .pin5(SignalOut[9]),
    .pin6(SignalOut[8]), .pin7(Clock), .pin8(1'b0), .pin9(and_2_out), .pin10(and_2_out),
    .pin11(HighHigh_pin11), .pin12(HighHigh_pin12), .pin13(HighHigh_pin13), .pin14(HighHigh_pin14),
    .pin15(Reset), .pin16(1'b1));
  _74173 _74173_4 (
    .pin1(1'b0), .pin2(1'b0), .pin3(SignalOut[3]), .pin4(SignalOut[2]), .pin5(SignalOut[1]),
    .pin6(SignalOut[0]), .pin7(Clock), .pin8(1'b0), .pin9(and_1_out), .pin10(and_1_out),
    .pin11(LowLow_pin11), .pin12(LowLow_pin12), .pin13(LowLow_pin13), .pin14(LowLow_pin14), .pin15(Reset),
    .pin16(1'b1));

  // Notes on the sheet:
  //   nOut: default 1
  //   noutLL: default 1
  //   noutHH: default 1
  //   noutSwap: default 1
  //   nIn: default 1
  //   ninLL: default 1
  //   ninHH: default 1
  //   ninLH: default 1
  //   ninHL: default 1
  //   RegOut
  //   LowHigh
  //   HighLow
  //   LowLow
  //   HighHigh
  //   RegInHigh
  //   RegInLow
  //   _HighHigh
endmodule
