// Digital circuit 16Display.dig as structural Verilog
module _16Display (
  input  Input0,
  input  Input1,
  input  Input2,
  input  Input3,
  input  Input4,
  input  Input5,
  input  Input6,
  input  Input7,
  input  Input8,
  input  Input9,
  input  Input10,
  input  Input11,
  input  Input12,
  input  Input13,
  input  Input14,
  input  Input15
);

  Seven_Seg_Hex seven_seg_hex_1 (.d({Input12, Input13, Input14, Input15}), .dp(1'b0));
  Seven_Seg_Hex seven_seg_hex_2 (.d({Input8, Input9, Input10, Input11}), .dp(1'b0));
  Seven_Seg_Hex seven_seg_hex_3 (.d({Input4, Input5, Input6, Input7}), .dp(1'b0));
  Seven_Seg_Hex seven_seg_hex_4 (.d({Input0, Input1, Input2, Input3}), .dp(1'b0));
endmodule
