// Digital circuit 2BitCPU.dig as structural Verilog
module _2BitCPU (
  input  in_1,
  input  in_2,
  input  in_3,
  input  in_4,
  input  in_5,
  input  in_6,
  input  in_7,
  input  in_8,
  input  RegOut,
  input  RegIn,
  input  Clock,
  input  Reset,
  input  in_13
);

  wire _2bitregisterint_1_signal0, _2bitregisterint_1_signal1, _74245_1_pin11, _74245_1_pin12;

  _74245 _74245_1 (
    .pin1(1'b1), .pin2(in_8), .pin3(in_7), .pin4(in_6), .pin5(in_5), .pin6(in_4), .pin7(in_3), .pin8(in_2),
    .pin9(in_1), .pin10(1'b0), .pin11(_74245_1_pin11), .pin12(_74245_1_pin12), .pin19(in_13), .pin20(1'b1));  // open: pin13, pin14, pin15, pin16, pin17, pin18
  LED Bus0 (.in(_74245_1_pin11));
  LED Bus1 (.in(_74245_1_pin12));
  _2BitRegisterInt _2bitregisterint_1 (
    .RegOut(RegOut), .RegIn(RegIn), .Clock(Clock), .Reset(Reset), .BusOut1(_74245_1_pin12),
    .BusOut0(_74245_1_pin11), .BusIn1(_74245_1_pin12), .BusIn0(_74245_1_pin11),
    .Signal1(_2bitregisterint_1_signal1), .Signal0(_2bitregisterint_1_signal0));
  LED Signal1 (.in(_2bitregisterint_1_signal1));
  LED Signal0 (.in(_2bitregisterint_1_signal0));

  // Notes on the sheet:
  //   RegOut: default 1
  //   RegIn: default 1
endmodule
