// Digital circuit 2BitRegister.dig as structural Verilog
module _2BitRegister (
  input  in_1,
  input  in_2,
  input  in_3,
  input  in_4,
  input  in_5,
  input  in_6,
  input  in_7,
  input  in_8,
  input  RegOut,
  input  RegIn,
  input  Clock,
  input  Reset,
  input  in_13
);

  wire _74245_1_pin11, _74245_1_pin12, _74245_2_pin11, _74245_2_pin12;

  _74245 _74245_1 (
    .pin1(1'b1), .pin2(in_8), .pin3(in_7), .pin4(in_6), .pin5(in_5), .pin6(in_4), .pin7(in_3), .pin8(in_2),
    .pin9(in_1), .pin10(1'b0), .pin11(_74245_1_pin11), .pin12(_74245_1_pin12), .pin19(in_13), .pin20(1'b1));  // open: pin13, pin14, pin15, pin16, pin17, pin18
  LED Bus0 (.in(_74245_1_pin11));
  LED Bus1 (.in(_74245_1_pin12));
  _74245 _74245_2 (
    .pin1(1'b0), .pin8(_74245_1_pin12), .pin9(_74245_1_pin11), .pin10(1'b0), .pin11(_74245_2_pin11),
    .pin12(_74245_2_pin12), .pin19(RegOut), .pin20(1'b1));  // open: pin2, pin3, pin4, pin5, pin6, pin7, pin13, pin14, pin15, pin16, pin17, pin18
  _74173 _74173_1 (
    .pin1(1'b0), .pin2(1'b0), .pin3(_74245_2_pin11), .pin4(_74245_2_pin12), .pin7(Clock), .pin8(1'b0),
    .pin9(RegIn), .pin10(RegIn), .pin11(1'b1), .pin12(1'b1), .pin13(_74245_1_pin12), .pin14(_74245_1_pin11),
    .pin15(Reset), .pin16(1'b1));  // open: pin5, pin6
  LED Signal1 (.in(_74245_2_pin12));
  LED Signal0 (.in(_74245_2_pin11));

  // Notes on the sheet:
  //   RegOut: default 1
  //   RegIn: default 1
endmodule
