// Digital circuit 2BitRegisterInt.dig as structural Verilog
module _2BitRegisterInt (
  input  RegOut,
  input  RegIn,
  input  Clock,
  input  Reset,
  input  BusIn0,
  input  BusIn1,
  output BusOut0,
  output BusOut1,
  output Signal1,
  output Signal0
);

  _74245 _74245_1 (
    .pin1(1'b0), .pin8(BusOut1), .pin9(BusOut0), .pin10(1'b0), .pin11(Signal0), .pin12(Signal1),
    .pin19(RegOut), .pin20(1'b1));  // open: pin2, pin3, pin4, pin5, pin6, pin7, pin13, pin14, pin15, pin16, pin17, pin18
  _74173 _74173_1 (
    .pin1(1'b0), .pin2(1'b0), .pin3(Signal0), .pin4(Signal1), .pin7(Clock), .pin8(1'b0), .pin9(RegIn),
    .pin10(RegIn), .pin11(1'b1), .pin12(1'b1), .pin13(BusIn1), .pin14(BusIn0), .pin15(Reset), .pin16(1'b1));  // open: pin5, pin6

  // Notes on the sheet:
  //   RegOut: default 1
  //   RegIn: default 1
endmodule
