// Digital circuit 4BitRAM.dig as structural Verilog
module _4BitRAM (
  input  BusAIn3,
  input  BusAIn2,
  input  BusAIn1,
  input  BusAIn0,
  input  RAMInH,
  input  RAMInL,
  input  RAMOut,
  input  in_31,
  input  in_32,
  input  in_33,
  input  in_34,
  input  in_35,
  input  in_36,
  input  in_37,
  input  in_38,
  input  busOut,
  input  in_40,
  input  in_41,
  input  in_42,
  input  in_43,
  input  in_44,
  input  in_45,
  input  in_46,
  input  in_47,
  output Sig15,
  output Sig14,
  output Sig13,
  output Sig12,
  output Sig11,
  output Sig10,
  output Sig9,
  output Sig8,
  output Sig7,
  output Sig6,
  output Sig5,
  output Sig4,
  output Sig3,
  output Sig2,
  output Sig1,
  output Sig0,
  output HighADDR1,
  output HighADDR2,
  output HighADDR3,
  output HighHighEn,
  output LowLowEn,
  output HighLowEn,
  output LowHighEn,
  output H4,
  output h3,
  output h2,
  output h1,
  output l1,
  output l2,
  output l3,
  output l4,
  output out7,
  output out6,
  output out5,
  output out4,
  output out3,
  output out2,
  output out1,
  output out8
);

  wire _74283_1_pin9, and_3_out, and_4_out, and_6_out, and_8_out, not_1_out, or_1_out, or_2_out, or_3_out,
       or_4_out, or_5_out, or_6_out, xor_1_out;

  _74245 _74245_1 (
    .pin1(1'b1), .pin2(in_38), .pin3(in_37), .pin4(in_36), .pin5(in_35), .pin6(in_34), .pin7(in_33),
    .pin8(in_32), .pin9(in_31), .pin10(1'b0), .pin11(Sig8), .pin12(Sig9), .pin13(Sig10), .pin14(Sig11),
    .pin15(Sig12), .pin16(Sig13), .pin17(Sig14), .pin18(Sig15), .pin19(busOut), .pin20(1'b1));
  LED Bus15 (.in(Sig15));
  LED Bus13 (.in(Sig13));
  LED Bus14 (.in(Sig14));
  LED Bus11 (.in(Sig11));
  LED Bus12 (.in(Sig12));
  LED Bus9 (.in(Sig9));
  LED Bus10 (.in(Sig10));
  LED Bus8 (.in(Sig8));
  _74245 _74245_2 (
    .pin1(1'b1), .pin2(in_47), .pin3(in_46), .pin4(in_45), .pin5(in_44), .pin6(in_43), .pin7(in_42),
    .pin8(in_41), .pin9(in_40), .pin10(1'b0), .pin11(Sig0), .pin12(Sig1), .pin13(Sig2), .pin14(Sig3),
    .pin15(Sig4), .pin16(Sig5), .pin17(Sig6), .pin18(Sig7), .pin19(busOut), .pin20(1'b1));
  LED Bus7 (.in(Sig7));
  LED Bus5 (.in(Sig5));
  LED Bus6 (.in(Sig6));
  LED Bus3 (.in(Sig3));
  LED Bus4 (.in(Sig4));
  LED Bus1 (.in(Sig1));
  LED Bus2 (.in(Sig2));
  LED Bus0 (.in(Sig0));
  _74245 _74245_3 (
    .pin1(1'b1), .pin2(l1), .pin3(l2), .pin4(l3), .pin5(l4), .pin6(h1), .pin7(h2), .pin8(h3), .pin9(H4),
    .pin10(1'b0), .pin11(out8), .pin12(out7), .pin13(out6), .pin14(out5), .pin15(out4), .pin16(out3),
    .pin17(out2), .pin18(out1), .pin19(LowLowEn), .pin20(1'b1));
  _74245 _74245_4 (
    .pin1(1'b1), .pin2(h1), .pin3(h2), .pin4(h3), .pin5(H4), .pin6(l1), .pin7(l2), .pin8(l3), .pin9(l4),
    .pin10(1'b0), .pin11(out8), .pin12(out7), .pin13(out6), .pin14(out5), .pin15(out4), .pin16(out3),
    .pin17(out2), .pin18(out1), .pin19(HighLowEn), .pin20(1'b1));
  // _28c16A High: pin names not known; wires that end beside it: 1'b0, 1'b0, 1'b0, 1'b0, 1'b0, HighADDR3, HighADDR2, HighADDR1, h1, h2, h3, 1'b1, 1'b0, 1'b0, 1'b1, 1'b0, 1'b0, 1'b0
  // _28c16B _28c16b_1: pin names not known; wires that end beside it: 1'b0, 1'b0, 1'b0, 1'b0, 1'b0, 1'b0, BusAIn3, BusAIn2, BusAIn1, l1, l2, l3, 1'b0, 1'b1, 1'b0, 1'b0, 1'b1, 1'b0, 1'b0, 1'b0
  _74283 _74283_1 (
    .pin1(HighADDR2), .pin2(1'b0), .pin3(BusAIn2), .pin4(HighADDR1), .pin5(BusAIn1), .pin6(1'b0),
    .pin7(BusAIn0), .pin8(1'b0), .pin9(_74283_1_pin9), .pin11(1'b0), .pin12(1'b0), .pin13(HighADDR3),
    .pin14(BusAIn3), .pin15(1'b0), .pin16(1'b1));  // open: pin10
  not not_1 (not_1_out, BusAIn0);
  and and_1 (HighHighEn, or_1_out, or_3_out);
  or or_1 (or_1_out, BusAIn0, and_8_out);
  and and_2 (LowLowEn, or_1_out, or_5_out);
  or or_2 (or_2_out, not_1_out, and_8_out);
  LED led_1 (.in(xor_1_out));
  and and_3 (and_3_out, RAMInH, xor_1_out);
  xor xor_1 (xor_1_out, and_4_out, RAMOut);
  and and_4 (and_4_out, RAMInH, RAMInL);
  and and_5 (HighLowEn, or_2_out, or_4_out);
  or or_3 (or_3_out, BusAIn0, and_6_out);
  and and_6 (and_6_out, RAMInL, xor_1_out);
  and and_7 (LowHighEn, or_2_out, or_6_out);
  or or_4 (or_4_out, not_1_out, and_6_out);
  and and_8 (and_8_out, RAMOut, xor_1_out);
  or or_5 (or_5_out, BusAIn0, and_3_out);
  or or_6 (or_6_out, not_1_out, and_3_out);

  // Notes on the sheet:
  //   RAMInH: default 1
  //   RAMInL: default 1
  //   RAMOut: default 1
  //   busOut: default 1
  //   ODD ADDR
endmodule
