// Digital circuit Counter.dig as structural Verilog
module Counter (
  input  in_1,
  input  in_2,
  input  in_3,
  input  in_4,
  input  in_5,
  input  in_6,
  input  in_7,
  input  in_8,
  input  in_9,
  input  in_10,
  input  in_11,
  input  in_12,
  input  in_13
);

  wire _74193_1_pin2, _74193_1_pin3, _74193_1_pin4, _74193_1_pin5, _74193_1_pin6, _74193_1_pin7,
       _74193_1_pin12, _74193_1_pin13, _74193_2_pin2, _74193_2_pin3, _74193_2_pin6, _74193_2_pin7,
       _74245_1_pin2, _74245_1_pin3, _74245_1_pin4, _74245_1_pin5, _74245_1_pin6, _74245_1_pin7,
       _74245_1_pin8, _74245_1_pin9;

  LED led_1 (.in(in_8));
  LED led_2 (.in(in_6));
  LED led_3 (.in(in_7));
  LED led_4 (.in(in_4));
  LED led_5 (.in(in_5));
  LED led_6 (.in(in_2));
  LED led_7 (.in(in_3));
  LED led_8 (.in(in_1));
  LED led_9 ();  // open: in
  _74193 _74193_1 (
    .pin1(in_6), .pin2(_74193_1_pin2), .pin3(_74193_1_pin3), .pin4(_74193_1_pin4), .pin5(_74193_1_pin5),
    .pin6(_74193_1_pin6), .pin7(_74193_1_pin7), .pin8(1'b0), .pin9(in_7), .pin10(in_8), .pin11(in_11),
    .pin12(_74193_1_pin12), .pin13(_74193_1_pin13), .pin14(in_12), .pin15(in_5), .pin16(1'b1));
  _74193 _74193_2 (
    .pin1(in_2), .pin2(_74193_2_pin2), .pin3(_74193_2_pin3), .pin4(in_9), .pin5(in_10), .pin6(_74193_2_pin6),
    .pin7(_74193_2_pin7), .pin8(1'b0), .pin9(in_3), .pin10(in_4), .pin11(in_11), .pin12(_74193_1_pin5),
    .pin13(_74193_1_pin4), .pin14(in_12), .pin15(in_1), .pin16(1'b1));
  LED led_10 (.in(_74193_1_pin13));
  LED led_11 (.in(_74193_1_pin12));
  LED led_12 (.in(_74193_1_pin7));
  LED led_13 (.in(_74193_1_pin6));
  LED led_14 (.in(_74193_1_pin2));
  LED led_15 (.in(_74193_1_pin3));
  LED led_16 (.in(_74193_2_pin7));
  LED led_17 (.in(_74193_2_pin6));
  LED led_18 (.in(_74193_2_pin2));
  LED led_19 (.in(_74193_2_pin3));
  LED led_20 (.in(_74245_1_pin8));
  LED led_21 (.in(_74245_1_pin9));
  LED led_22 (.in(_74245_1_pin6));
  LED led_23 (.in(_74245_1_pin7));
  LED led_24 (.in(_74245_1_pin4));
  LED led_25 (.in(_74245_1_pin5));
  _74245 _74245_1 (
    .pin1(1'b0), .pin2(_74245_1_pin2), .pin3(_74245_1_pin3), .pin4(_74245_1_pin4), .pin5(_74245_1_pin5),
    .pin6(_74245_1_pin6), .pin7(_74245_1_pin7), .pin8(_74245_1_pin8), .pin9(_74245_1_pin9), .pin10(1'b0),
    .pin11(_74193_1_pin7), .pin12(_74193_1_pin6), .pin13(_74193_1_pin2), .pin14(_74193_1_pin3),
    .pin15(_74193_2_pin7), .pin16(_74193_2_pin6), .pin17(_74193_2_pin2), .pin18(_74193_2_pin3),
    .pin19(in_13), .pin20(1'b1));
  LED led_26 (.in(_74245_1_pin3));
  LED led_27 (.in(_74245_1_pin2));
endmodule
