// Digital circuit EEPROMTest.dig as structural Verilog
module EEPROMTest (
  input  in_1,
  input  in_2,
  input  in_3,
  input  in_4,
  input  in_5,
  input  in_6,
  input  in_7,
  input  in_8,
  input  in_9
);

  wire Control1_p2, Control1_p3, Control1_p4, Control1_p5, Control1_p6, Control1_p8, Control2_p2,
       Control2_p3, Control2_p4, Control2_p5, Control2_p6, Control2_p8, not_1_out, not_2_out, not_3_out,
       not_4_out, not_5_out, not_6_out, not_7_out, not_8_out, not_9_out, not_10_out, not_11_out, undriven,
       undriven_2, undriven_3, undriven_4;

  not not_1 (not_1_out, Control2_p5);
  LED Flag (.in(Control2_p5));
  not not_2 (not_2_out, Control2_p3);
  LED Jump (.in(Control2_p3));
  not not_3 (not_3_out, Control2_p2);
  LED PCOut (.in(Control2_p2));
  LED PCInc (.in(undriven));
  LED OutIn (.in(undriven_2));
  not not_4 (not_4_out, Control2_p4);
  LED BIn (.in(Control2_p4));
  LED SU (.in(Control2_p6));
  not not_5 (not_5_out, Control2_p8);
  LED ALUOut (.in(Control2_p8));
  not not_6 (not_6_out, Control1_p5);
  LED AOut (.in(Control1_p5));
  not not_7 (not_7_out, Control1_p3);
  LED AIn (.in(Control1_p3));
  not not_8 (not_8_out, Control1_p2);
  LED IRIn (.in(Control1_p2));
  not not_9 (not_9_out, undriven_3);
  LED IROut (.in(undriven_3));
  not not_10 (not_10_out, undriven_4);
  LED RAMOut (.in(undriven_4));
  LED RAMIn (.in(Control1_p4));
  // _28c16 Control2: pin names not known; wires that end beside it: 1'b0, Control2_p2, Control2_p3, Control2_p4, Control2_p5, Control2_p6, in_1, Control2_p8, in_2, 1'b0, in_3, 1'b0, in_7, 1'b0, in_6, 1'b1, in_5, in_9, in_4, in_8, 1'b1, 1'b1
  not not_11 (not_11_out, Control1_p6);
  LED MARIn (.in(Control1_p6));
  // _28c16 Control1: pin names not known; wires that end beside it: 1'b0, Control1_p2, Control1_p3, Control1_p4, Control1_p5, Control1_p6, in_1, Control1_p8, in_2, 1'b0, in_3, 1'b0, in_7, 1'b0, in_6, 1'b1, in_5, in_9, in_7, in_6, in_5, in_4, in_4, in_8, 1'b0, 1'b1
  LED Halt (.in(Control1_p8));

  // Notes on the sheet:
  //   Controller
endmodule
