// Digital circuit Interupts.dig as structural Verilog
module Interupts (
  input  Data0,
  input  Data1,
  input  Data2,
  input  Data3,
  input  Data4,
  input  Data5,
  input  Data6,
  input  DataB1,
  input  DataB2,
  input  DataB3,
  input  DataB4,
  input  DataB5,
  input  DataB6,
  input  DataB7,
  input  DataB8,
  input  DataB9,
  input  DataB10,
  input  DataB11,
  input  DataB12,
  input  DataB13,
  input  DataB14,
  input  DataB15,
  input  in_23,
  input  in_24,
  input  in_25,
  input  in_26
);

  wire _74173_1_pin3, _74173_1_pin4, _74173_1_pin5, _74173_1_pin6, _74173_1_pin9, or_1_out, or_2_out,
       or_3_out, or_4_out, or_5_out, or_6_out, or_7_out, or_8_out, or_9_out, or_10_out, or_11_out, or_12_out,
       or_13_out, or_14_out, or_15_out, or_16_out, or_17_out;

  or or_1 (or_1_out, Data6, Data5, Data4, Data3);
  or or_2 (or_2_out, Data6, Data5, Data2, Data1);
  or or_3 (or_3_out, Data6, Data4, Data2, Data0);
  LED led_1 (.in(or_1_out));
  LED led_2 (.in(or_2_out));
  LED led_3 (.in(or_3_out));
  or or_4 (or_4_out, DataB15, DataB14, DataB13, DataB12);
  or or_5 (or_5_out, DataB11, DataB10, DataB9, DataB8);
  or or_6 (or_6_out, DataB15, DataB14, DataB13, DataB12);
  or or_7 (or_7_out, DataB7, DataB6, DataB5, DataB4);
  or or_8 (or_8_out, DataB15, DataB14, DataB10, DataB7);
  or or_9 (or_9_out, DataB11, DataB6, DataB3, DataB2);
  or or_10 (or_10_out, DataB15, DataB13, DataB11, DataB9);
  or or_11 (or_11_out, DataB7, DataB5, DataB3, DataB1);
  or or_12 (or_12_out, or_4_out, or_5_out);
  or or_13 (or_13_out, or_6_out, or_7_out);
  or or_14 (or_14_out, or_8_out, or_9_out);
  LED led_4 (.in(or_12_out));
  or or_15 (or_15_out, or_10_out, or_11_out);
  LED led_5 (.in(or_13_out));
  LED led_6 (.in(or_14_out));
  LED led_7 (.in(or_15_out));
  LED led_8 (.in(1'b0));
  _74173 _74173_1 (
    .pin1(1'b0), .pin2(1'b0), .pin3(_74173_1_pin3), .pin4(_74173_1_pin4), .pin5(_74173_1_pin5),
    .pin6(_74173_1_pin6), .pin7(in_25), .pin8(1'b0), .pin9(_74173_1_pin9), .pin10(_74173_1_pin9),
    .pin11(in_24), .pin12(in_24), .pin13(in_24), .pin14(in_26), .pin15(in_23), .pin16(1'b1));
  LED led_9 (.in(_74173_1_pin6));
  LED led_10 (.in(_74173_1_pin5));
  LED led_11 (.in(_74173_1_pin4));
  LED led_12 (.in(_74173_1_pin3));
  or or_16 (or_16_out, _74173_1_pin6, _74173_1_pin5);
  or or_17 (or_17_out, _74173_1_pin4, _74173_1_pin3);
  or or_18 (_74173_1_pin9, or_16_out, or_17_out);
  LED led_13 (.in(_74173_1_pin9));
endmodule
