// Digital circuit Mult.dig as structural Verilog
module Mult (
  input  in_1,
  input  in_2,
  input  in_3,
  input  in_4,
  input  in_5,
  input  in_6
);

  wire _74283_1_p3, _74283_1_p5, _74283_1_p7, and_1_out;

  LED led_1 (.in(_74283_1_p5));
  LED led_2 (.in(_74283_1_p3));
  // _74283 _74283_1: pin names not known; wires that end beside it: in_6, in_4, _74283_1_p3, in_3, _74283_1_p5, in_2, _74283_1_p7
  LED led_3 (.in(and_1_out));
  LED led_4 (.in(_74283_1_p7));
  and and_1 (and_1_out, in_5, in_1);
endmodule
