// Digital circuit MultxTester.dig as structural Verilog
module MultxTester (
  input  ADDR3,
  input  ADDR2,
  input  ADDR1,
  input  ADDR0
);

  wire _74138_1_pin7, _74138_1_pin9, _74138_1_pin10, _74138_1_pin11, _74138_1_pin12, _74138_1_pin13,
       _74138_1_pin14, _74138_1_pin15, _74138_2_pin7, _74138_2_pin9, _74138_2_pin10, _74138_2_pin11,
       _74138_2_pin12, _74138_2_pin13, _74138_2_pin14, _74138_2_pin15, not_1_out;

  LED led_1 (.in(_74138_1_pin7));
  LED led_2 (.in(_74138_1_pin9));
  LED led_3 (.in(_74138_1_pin10));
  LED led_4 (.in(_74138_1_pin11));
  LED led_5 (.in(_74138_1_pin12));
  LED led_6 (.in(_74138_1_pin13));
  not not_1 (not_1_out, ADDR3);
  _74138 _74138_1 (
    .pin1(ADDR0), .pin2(ADDR1), .pin3(ADDR2), .pin4(not_1_out), .pin5(1'b0), .pin6(1'b1),
    .pin7(_74138_1_pin7), .pin8(1'b0), .pin9(_74138_1_pin9), .pin10(_74138_1_pin10), .pin11(_74138_1_pin11),
    .pin12(_74138_1_pin12), .pin13(_74138_1_pin13), .pin14(_74138_1_pin14), .pin15(_74138_1_pin15),
    .pin16(1'b1));
  LED led_7 (.in(_74138_1_pin14));
  LED led_8 (.in(_74138_1_pin15));
  LED led_9 (.in(_74138_2_pin7));
  LED led_10 (.in(_74138_2_pin9));
  LED led_11 (.in(_74138_2_pin10));
  LED led_12 (.in(_74138_2_pin11));
  LED led_13 (.in(_74138_2_pin12));
  LED led_14 (.in(_74138_2_pin13));
  _74138 _74138_2 (
    .pin1(ADDR0), .pin2(ADDR1), .pin3(ADDR2), .pin4(ADDR3), .pin5(1'b0), .pin6(1'b1), .pin7(_74138_2_pin7),
    .pin8(1'b0), .pin9(_74138_2_pin9), .pin10(_74138_2_pin10), .pin11(_74138_2_pin11),
    .pin12(_74138_2_pin12), .pin13(_74138_2_pin13), .pin14(_74138_2_pin14), .pin15(_74138_2_pin15),
    .pin16(1'b1));
  LED led_15 (.in(_74138_2_pin14));
  LED led_16 (.in(_74138_2_pin15));
endmodule
