// Digital circuit RAMTest.dig as structural Verilog
module RAMTest (
  input  ADDR3,
  input  ADDR2,
  input  ADDR1,
  input  ADDR0
);

  wire _74189_a_1_pin5, _74189_a_1_pin7, _74189_a_1_pin9, _74189_a_1_pin11, B_pin5, B_pin7, B_pin9, B_pin11,
       not_1_out, not_2_out, not_3_out, not_4_out, not_5_out, not_6_out, not_7_out, not_8_out;

  _74189_A _74189_a_1 (
    .pin1(ADDR0), .pin2(1'b0), .pin3(1'b1), .pin4(1'b0), .pin5(_74189_a_1_pin5), .pin6(1'b0),
    .pin7(_74189_a_1_pin7), .pin8(1'b0), .pin9(_74189_a_1_pin9), .pin10(1'b0), .pin11(_74189_a_1_pin11),
    .pin12(1'b0), .pin13(ADDR3), .pin14(ADDR2), .pin15(ADDR1), .pin16(1'b1));
  not not_1 (not_1_out, B_pin9);
  not not_2 (not_2_out, B_pin11);
  LED led_1 (.in(not_2_out));
  LED led_2 (.in(not_1_out));
  not not_3 (not_3_out, B_pin5);
  not not_4 (not_4_out, B_pin7);
  LED led_3 (.in(not_4_out));
  LED led_4 (.in(not_3_out));
  not not_5 (not_5_out, _74189_a_1_pin9);
  not not_6 (not_6_out, _74189_a_1_pin11);
  LED led_5 (.in(not_6_out));
  LED led_6 (.in(not_5_out));
  _74189 B (
    .pin1(ADDR0), .pin2(1'b0), .pin3(1'b1), .pin4(1'b0), .pin5(B_pin5), .pin6(1'b0), .pin7(B_pin7),
    .pin8(1'b0), .pin9(B_pin9), .pin10(1'b0), .pin11(B_pin11), .pin12(1'b0), .pin13(ADDR3), .pin14(ADDR2),
    .pin15(ADDR1), .pin16(1'b1));
  not not_7 (not_7_out, _74189_a_1_pin5);
  not not_8 (not_8_out, _74189_a_1_pin7);
  LED led_7 (.in(not_8_out));
  LED led_8 (.in(not_7_out));
endmodule
