// Digital circuit RAMTest2.dig as structural Verilog
module RAMTest2 (
  input  ADDR3,
  input  ADDR2,
  input  ADDR1,
  input  ADDR0
);

  wire not_1_out, not_2_out, not_3_out, not_4_out, not_5_out, not_6_out, not_7_out, not_8_out, RAMA_pin5,
       RAMA_pin7, RAMA_pin9, RAMA_pin11, RAMB_pin5, RAMB_pin7, RAMB_pin9, RAMB_pin11;

  _74189 RAMA (
    .pin1(ADDR0), .pin2(1'b0), .pin3(1'b1), .pin4(1'b0), .pin5(RAMA_pin5), .pin6(1'b0), .pin7(RAMA_pin7),
    .pin8(1'b0), .pin9(RAMA_pin9), .pin10(1'b0), .pin11(RAMA_pin11), .pin12(1'b0), .pin13(ADDR3),
    .pin14(ADDR2), .pin15(ADDR1), .pin16(1'b1));
  not not_1 (not_1_out, RAMB_pin11);
  LED led_1 (.in(not_1_out));
  not not_2 (not_2_out, RAMB_pin7);
  not not_3 (not_3_out, RAMB_pin9);
  LED led_2 (.in(not_3_out));
  LED led_3 (.in(not_2_out));
  not not_4 (not_4_out, RAMA_pin11);
  not not_5 (not_5_out, RAMB_pin5);
  LED led_4 (.in(not_5_out));
  LED led_5 (.in(not_4_out));
  not not_6 (not_6_out, RAMA_pin7);
  not not_7 (not_7_out, RAMA_pin9);
  LED led_6 (.in(not_7_out));
  LED led_7 (.in(not_6_out));
  _74189 RAMB (
    .pin1(ADDR0), .pin2(1'b0), .pin3(1'b1), .pin4(1'b0), .pin5(RAMB_pin5), .pin6(1'b0), .pin7(RAMB_pin7),
    .pin8(1'b0), .pin9(RAMB_pin9), .pin10(1'b0), .pin11(RAMB_pin11), .pin12(1'b0), .pin13(ADDR3),
    .pin14(ADDR2), .pin15(ADDR1), .pin16(1'b1));
  not not_8 (not_8_out, RAMA_pin5);
  LED led_8 (.in(not_8_out));
endmodule
