// Digital circuit Register.dig as structural Verilog
module Register (
  input  in_1,
  input  in_2,
  input  in_3,
  input  in_4,
  input  in_5,
  input  in_6,
  input  in_7,
  input  in_8,
  input  in_9,
  input  in_10,
  input  in_11,
  input  in_12,
  input  in_13
);

  wire _74173_1_pin3, _74173_1_pin4, _74173_1_pin5, _74173_1_pin6, _74173_2_pin3, _74173_2_pin4,
       _74173_2_pin6, _74245_1_pin11, _74245_1_pin12, _74245_1_pin13, _74245_1_pin14, _74245_1_pin15,
       _74245_1_pin16, _74245_1_pin17, _74245_1_pin18;

  _74245 _74245_1 (
    .pin1(1'b1), .pin2(in_8), .pin3(in_7), .pin4(in_6), .pin5(in_5), .pin6(in_4), .pin7(in_3), .pin8(in_2),
    .pin9(in_1), .pin10(1'b0), .pin11(_74245_1_pin11), .pin12(_74245_1_pin12), .pin13(_74245_1_pin13),
    .pin14(_74245_1_pin14), .pin15(_74245_1_pin15), .pin16(_74245_1_pin16), .pin17(_74245_1_pin17),
    .pin18(_74245_1_pin18), .pin19(in_9), .pin20(1'b1));
  LED led_1 (.in(_74245_1_pin17));
  LED led_2 (.in(_74245_1_pin18));
  LED led_3 (.in(_74245_1_pin15));
  LED led_4 (.in(_74245_1_pin16));
  LED led_5 (.in(_74245_1_pin13));
  LED led_6 (.in(_74245_1_pin14));
  LED led_7 (.in(_74245_1_pin11));
  LED led_8 (.in(_74245_1_pin12));
  _74173 _74173_1 (
    .pin1(1'b0), .pin2(1'b0), .pin3(_74173_1_pin3), .pin4(_74173_1_pin4), .pin5(_74173_1_pin5),
    .pin6(_74173_1_pin6), .pin7(in_10), .pin8(1'b0), .pin9(in_12), .pin10(in_12), .pin11(_74245_1_pin14),
    .pin12(_74245_1_pin13), .pin13(_74245_1_pin12), .pin14(_74245_1_pin11), .pin15(in_11), .pin16(1'b1));
  _74173 _74173_2 (
    .pin1(1'b0), .pin2(1'b0), .pin3(_74173_2_pin3), .pin4(_74173_2_pin4), .pin5(_74173_1_pin3),
    .pin6(_74173_2_pin6), .pin7(in_10), .pin8(1'b0), .pin9(in_12), .pin10(in_12), .pin11(_74245_1_pin18),
    .pin12(_74245_1_pin17), .pin13(_74245_1_pin16), .pin14(_74245_1_pin15), .pin15(in_11), .pin16(1'b1));
  LED led_9 (.in(_74173_1_pin3));
  LED led_10 (.in(_74173_2_pin6));
  LED led_11 (.in(_74173_2_pin3));
  LED led_12 (.in(_74173_2_pin4));
  LED led_13 (.in(_74173_1_pin5));
  LED led_14 (.in(_74173_1_pin6));
  LED led_15 (.in(_74173_1_pin3));
  LED led_16 (.in(_74173_1_pin4));
  _74245 _74245_2 (
    .pin1(1'b1), .pin2(_74173_1_pin3), .pin3(_74173_1_pin4), .pin4(_74173_1_pin5), .pin5(_74173_1_pin6),
    .pin6(_74173_2_pin3), .pin7(_74173_2_pin4), .pin8(_74173_1_pin3), .pin9(_74173_2_pin6), .pin10(1'b0),
    .pin11(_74245_1_pin18), .pin12(_74245_1_pin17), .pin13(_74245_1_pin16), .pin14(_74245_1_pin15),
    .pin15(_74245_1_pin14), .pin16(_74245_1_pin13), .pin17(_74245_1_pin12), .pin18(_74245_1_pin11),
    .pin19(in_13), .pin20(1'b1));
endmodule
