// Digital circuit direction.dig as structural Verilog
module direction (
  input  nRAMinL,
  input  nRAMinH,
  input  nRAMout
);

  wire and_1_out, not_1_out, or_1_out;

  LED led_1 (.in(or_1_out));
  or or_1 (or_1_out, and_1_out, not_1_out);
  and and_1 (and_1_out, nRAMinL, nRAMinH);
  not not_1 (not_1_out, nRAMout);
  LED led_2 (.in(nRAMout));
endmodule
