// Digital circuit newRAM.dig as structural Verilog
module newRAM (
  input  in_1,
  input  in_2,
  input  in_3,
  input  in_4
);

  wire _74189_1_pin5, _74189_1_pin7, _74189_1_pin9, _74189_1_pin11;

  _74189 _74189_1 (
    .pin1(in_4), .pin2(1'b0), .pin3(1'b1), .pin4(1'b0), .pin5(_74189_1_pin5), .pin6(1'b0),
    .pin7(_74189_1_pin7), .pin8(1'b0), .pin9(_74189_1_pin9), .pin10(1'b0), .pin11(_74189_1_pin11),
    .pin12(1'b0), .pin13(in_1), .pin14(in_2), .pin15(in_3), .pin16(1'b1));
  LED led_1 (.in(_74189_1_pin11));
  LED led_2 (.in(_74189_1_pin9));
  LED led_3 (.in(_74189_1_pin7));
  LED led_4 (.in(_74189_1_pin5));
endmodule
